// Logisim project 5.20.circ as structural Verilog: 1 circuit, main circuit main
module main (
  input  x,
  input  T3,
  input  z,
  input  T2,
  input  w,
  input  T5,
  input  G,
  input  y,
  input  T1,
  output Output
);

  wire and_1_out, and_2_out, and_3_out, and_4_out, and_5_out, CLK_out, not_1_out, or_1_out, or_2_out;

  not not_1 (not_1_out, G);
  and and_1 (and_1_out, x, T3);
  and and_2 (and_2_out, z, T2);
  and and_3 (and_3_out, w, T5, G);
  and and_4 (and_4_out, w, T5, not_1_out);
  and and_5 (and_5_out, y, T1);
  J_K_Flip_Flop j_k_ff_1 (.J(or_1_out), .clk(CLK_out), .K(or_2_out), .Q(Output));  // open: Qn, preset, en, reset
  Clock CLK (.out(CLK_out));
  or or_1 (or_1_out, and_1_out, and_2_out, and_3_out);
  or or_2 (or_2_out, and_2_out, and_4_out, and_5_out);

  // Notes on the sheet:
  //   JF = xT3 + Zt2 + wT5G KF = yT1 + zT2 + wT5G'
  //   5.20
endmodule
