// Logisim project 5.23.circ as structural Verilog: 1 circuit, main circuit main
module main (
  input  T0,
  input  T1,
  input  T2,
  input  IEN,
  input  FGI,
  input  FGO,
  output Output
);

  wire and_1_out, CLK_out, nor_1_out, or_1_out;

  nor nor_1 (nor_1_out, T0, T1, T2);
  or or_1 (or_1_out, FGI, FGO);
  and and_1 (and_1_out, nor_1_out, IEN, or_1_out);
  Clock CLK (.out(CLK_out));
  J_K_Flip_Flop j_k_ff_1 (.J(and_1_out), .clk(CLK_out), .K(T2), .Q(Output));  // open: Qn, preset, en, reset

  // Notes on the sheet:
  //   (T0 + T1 + T2)' (IEN) (FGI + FGO) : R <-- 1
  //   RT2 : R <-- 0
  //   5.23
endmodule
