// Logisim project 5.24.circ as structural Verilog: 1 circuit, main circuit main
module main (
  input  T0,
  input  D5,
  input  T4,
  output Output
);

  wire and_1_out;

  and and_1 (and_1_out, D5, T4);
  or or_1 (Output, T0, and_1_out);

  // Notes on the sheet:
  //   X2 places PC onto the bus. From Table 5.6:
  //   R’T0: AR <--  PC
  //   RT0: TR <--  PC
  //   D5T4: M[AR] <--  PC
  //   X2 = R’T0 + RT0 + D5 T4 = (R’ + R) T0 + D5T4 = T0 + D5T4
  //   5.24
endmodule
