// Logisim project 5.25.circ as structural Verilog: 1 circuit, main circuit main
module main (
  input  R,
  input  T2,
  input  D7,
  input  T3,
  input  D0,
  input  D11,
  input  D2,
  input  T5,
  input  D5,
  input  D3,
  input  D4,
  input  T4,
  input  D6,
  input  T6,
  output out_15
);

  wire and_1_out, and_2_out, and_3_out, and_4_out, and_5_out, CLK_out, not_1_out, or_1_out, or_2_out,
       or_3_out;

  and and_1 (and_1_out, R, T2);
  and and_2 (and_2_out, D7, T3);
  or or_1 (or_1_out, D0, D11, D2, D5);
  or or_2 (or_2_out, D3, D4);
  and and_3 (and_3_out, D6, T6);
  and and_4 (and_4_out, or_1_out, T5);
  and and_5 (and_5_out, or_2_out, T4);
  or or_3 (or_3_out, and_1_out, and_2_out, and_4_out, and_5_out, and_3_out);
  not not_1 (not_1_out, or_3_out);
  Counter #(.width(1), .max('h1)) counter_1 (
    .D(not_1_out), .Q(out_15), .clk(CLK_out), .clr(or_3_out));  // open: load, count, carry
  Clock CLK (.out(CLK_out));

  // Notes on the sheet:
  //   From Table 5.6:
  //   CLR (SC) = RT2 + D7T3 (I’+I) + (D0 + D1 + D2 + D5 ) T5 + (D3 + D4) T4 + D6T6
  //   5.25
endmodule
