// Logisim project Week 1 8-Bit Register.circ as structural Verilog: 4 circuits, main circuit main
module main (
  input  DATA_IN,
  input  CARYY_IN,
  input  in_3,
  input  [2:0] LIC__LOAD__INCLEMENT__CLEAR,
  output DATA_OUT,
  output ARRY_OUT
);

  wire and_2_out, and_3_out, CLOCK_out, multiplexer_1_out, not_1_out, not_2_out, not_3_out, xor_1_out;
  wire [1:0] or_1_out;

  Clock CLOCK (.out(CLOCK_out));
  xor xor_1 (xor_1_out, CARYY_IN, DATA_OUT);
  not not_1 (not_1_out, LIC__LOAD__INCLEMENT__CLEAR[0]);
  not not_2 (not_2_out, LIC__LOAD__INCLEMENT__CLEAR[1]);
  not not_3 (not_3_out, LIC__LOAD__INCLEMENT__CLEAR[2]);
  Multiplexer #(.select(2)) multiplexer_1 (
    .in0(DATA_IN), .in1(xor_1_out), .in2(1'b0), .out(multiplexer_1_out), .sel(or_1_out), .en(in_3));  // open: in3
  and and_1 (or_1_out[1], not_3_out, not_2_out);
  and and_2 (and_2_out, not_3_out, not_1_out);
  and and_3 (and_3_out, LIC__LOAD__INCLEMENT__CLEAR[1], not_3_out);
  D_Flip_Flop d_ff_1 (.clk(CLOCK_out), .D(multiplexer_1_out), .Q(DATA_OUT), .en(in_3));  // open: Qn, preset, reset
  and and_4 (ARRY_OUT, DATA_OUT, CARYY_IN);
  buf or_1 (or_1_out[0], and_3_out);  // OR_Gate
endmodule

module _4_BIT_REGISTER (
  input  [3:0] in_1,
  input  in_2,
  input  in_3,
  input  [2:0] in_4,
  output [3:0] out_5,
  output out_6
);

  wire clock_1_out, main_1_arry_out, main_2_arry_out, main_3_arry_out;

  Clock clock_1 (.out(clock_1_out));
  main main_1 (
    .DATA_IN(in_1[0]), .CARYY_IN(in_2), .LIC__LOAD__INCLEMENT__CLEAR(in_4), .DATA_OUT(out_5[0]),
    .ARRY_OUT(main_1_arry_out), .in_3(in_3));
  main main_2 (
    .DATA_IN(in_1[1]), .CARYY_IN(main_1_arry_out), .LIC__LOAD__INCLEMENT__CLEAR(in_4), .DATA_OUT(out_5[1]),
    .ARRY_OUT(main_2_arry_out), .in_3(in_3));
  main main_3 (
    .DATA_IN(in_1[2]), .CARYY_IN(main_2_arry_out), .LIC__LOAD__INCLEMENT__CLEAR(in_4), .DATA_OUT(out_5[2]),
    .ARRY_OUT(main_3_arry_out), .in_3(in_3));
  main main_4 (
    .DATA_IN(in_1[3]), .CARYY_IN(main_3_arry_out), .LIC__LOAD__INCLEMENT__CLEAR(in_4), .DATA_OUT(out_5[3]),
    .ARRY_OUT(out_6), .in_3(in_3));
  Hex_Digit_Display hex_digit_display_1 (.value(out_5));  // open: dp
endmodule

module _8_BIT_REGISTER (
  input  in_1,
  input  in_2,
  input  [7:0] in_3,
  input  [2:0] in_4,
  output [7:0] out_5,
  output out_6
);

  wire clock_1_out, n4_bit_register_1_out_6;

  Clock clock_1 (.out(clock_1_out));
  _4_BIT_REGISTER u_4_bit_register_1 (
    .in_1(in_3[3:0]), .in_2(in_1), .in_3(in_2), .in_4(in_4), .out_5(out_5[3:0]),
    .out_6(n4_bit_register_1_out_6));
  _4_BIT_REGISTER u_4_bit_register_2 (
    .in_1(in_3[7:4]), .in_2(n4_bit_register_1_out_6), .in_3(in_2), .in_4(in_4), .out_5(out_5[7:4]),
    .out_6(out_6));
  Hex_Digit_Display hex_digit_display_1 (.value(out_5[7:4]));  // open: dp
  Hex_Digit_Display hex_digit_display_2 (.value(out_5[3:0]));  // open: dp
endmodule

module _8_BIT_REGISTER_USE (
  input  [7:0] in_1,
  input  in_2,
  input  in_3,
  input  [2:0] in_4,
  output [7:0] out_5,
  output out_6
);

  wire clock_1_out;

  Clock clock_1 (.out(clock_1_out));
  _8_BIT_REGISTER u_8_bit_register_1 (.in_1(in_2), .in_2(in_3), .in_3(in_1), .in_4(in_4), .out_5(out_5), .out_6(out_6));
  Hex_Digit_Display hex_digit_display_1 (.value(out_5[7:4]));  // open: dp
  Hex_Digit_Display hex_digit_display_2 (.value(out_5[3:0]));  // open: dp
endmodule
