// Logisim project Week 2 16-Bit Arithmetic Logic Unit.circ as structural Verilog: 3 circuits, main circuit main
module main (
  input  B,
  input  A,
  input  CARRY_IN,
  input  [1:0] OPERATION,
  input  BINARY_CONV,
  output out_6,
  output CARRY_OUT
);

  wire adder_1_out, and_1_out, multiplexer_1_out, not_1_out, or_1_out;

  not not_1 (not_1_out, B);
  Multiplexer multiplexer_1 (.in0(not_1_out), .in1(B), .out(multiplexer_1_out), .sel(BINARY_CONV));  // open: en
  and and_1 (and_1_out, B, multiplexer_1_out);
  or or_1 (or_1_out, B, multiplexer_1_out);
  Adder #(.width(1)) adder_1 (.a(A), .b(multiplexer_1_out), .out(adder_1_out), .cin(CARRY_IN), .cout(CARRY_OUT));
  Multiplexer #(.select(2)) multiplexer_2 (
    .in0(and_1_out), .in1(or_1_out), .in2(adder_1_out), .out(out_6), .sel(OPERATION));  // open: in3, en
endmodule

module _16_BIT_ALU (
  input  CARRY_IN,
  input  BIN_CONV,
  input  [1:0] OPRTN,
  input  [15:0] A,
  input  [15:0] B,
  output [15:0] RESULT,
  output ZERO,
  output OVERFLOW,
  output CARRY_OUT
);

  wire main_1_carry_out, main_2_carry_out, main_3_carry_out, main_4_carry_out, main_5_carry_out,
       main_6_carry_out, main_7_carry_out, main_8_carry_out, main_9_carry_out, main_10_carry_out,
       main_11_carry_out, main_12_carry_out, main_13_carry_out, main_14_carry_out, main_15_carry_out;

  main main_1 (
    .OPERATION(OPRTN), .out_6(RESULT[0]), .CARRY_OUT(main_1_carry_out), .B(B[0]), .A(A[0]),
    .CARRY_IN(CARRY_IN), .BINARY_CONV(BIN_CONV));
  main main_2 (
    .OPERATION(OPRTN), .out_6(RESULT[1]), .CARRY_OUT(main_2_carry_out), .B(B[1]), .A(A[1]),
    .CARRY_IN(main_1_carry_out), .BINARY_CONV(BIN_CONV));
  main main_3 (
    .OPERATION(OPRTN), .out_6(RESULT[2]), .CARRY_OUT(main_3_carry_out), .B(B[2]), .A(A[2]),
    .CARRY_IN(main_2_carry_out), .BINARY_CONV(BIN_CONV));
  main main_4 (
    .OPERATION(OPRTN), .out_6(RESULT[3]), .CARRY_OUT(main_4_carry_out), .B(B[3]), .A(A[3]),
    .CARRY_IN(main_3_carry_out), .BINARY_CONV(BIN_CONV));
  main main_5 (
    .OPERATION(OPRTN), .out_6(RESULT[4]), .CARRY_OUT(main_5_carry_out), .B(B[4]), .A(A[4]),
    .CARRY_IN(main_4_carry_out), .BINARY_CONV(BIN_CONV));
  main main_6 (
    .OPERATION(OPRTN), .out_6(RESULT[5]), .CARRY_OUT(main_6_carry_out), .B(B[5]), .A(A[5]),
    .CARRY_IN(main_5_carry_out), .BINARY_CONV(BIN_CONV));
  main main_7 (
    .OPERATION(OPRTN), .out_6(RESULT[6]), .CARRY_OUT(main_7_carry_out), .B(B[6]), .A(A[6]),
    .CARRY_IN(main_6_carry_out), .BINARY_CONV(BIN_CONV));
  main main_8 (
    .OPERATION(OPRTN), .out_6(RESULT[7]), .CARRY_OUT(main_8_carry_out), .B(B[7]), .A(A[7]),
    .CARRY_IN(main_7_carry_out), .BINARY_CONV(BIN_CONV));
  main main_9 (
    .OPERATION(OPRTN), .out_6(RESULT[8]), .CARRY_OUT(main_9_carry_out), .B(B[8]), .A(A[8]),
    .CARRY_IN(main_8_carry_out), .BINARY_CONV(BIN_CONV));
  main main_10 (
    .OPERATION(OPRTN), .out_6(RESULT[9]), .CARRY_OUT(main_10_carry_out), .B(B[9]), .A(A[9]),
    .CARRY_IN(main_9_carry_out), .BINARY_CONV(BIN_CONV));
  main main_11 (
    .OPERATION(OPRTN), .out_6(RESULT[10]), .CARRY_OUT(main_11_carry_out), .B(B[10]), .A(A[10]),
    .CARRY_IN(main_10_carry_out), .BINARY_CONV(BIN_CONV));
  main main_12 (
    .OPERATION(OPRTN), .out_6(RESULT[11]), .CARRY_OUT(main_12_carry_out), .B(B[11]), .A(A[11]),
    .CARRY_IN(main_11_carry_out), .BINARY_CONV(BIN_CONV));
  main main_13 (
    .OPERATION(OPRTN), .out_6(RESULT[12]), .CARRY_OUT(main_13_carry_out), .B(B[12]), .A(A[12]),
    .CARRY_IN(main_12_carry_out), .BINARY_CONV(BIN_CONV));
  main main_14 (
    .OPERATION(OPRTN), .out_6(RESULT[13]), .CARRY_OUT(main_14_carry_out), .B(B[13]), .A(A[13]),
    .CARRY_IN(main_13_carry_out), .BINARY_CONV(BIN_CONV));
  main main_15 (
    .OPERATION(OPRTN), .out_6(RESULT[14]), .CARRY_OUT(main_15_carry_out), .B(B[14]), .A(A[14]),
    .CARRY_IN(main_14_carry_out), .BINARY_CONV(BIN_CONV));
  main main_16 (
    .OPERATION(OPRTN), .out_6(RESULT[15]), .CARRY_OUT(CARRY_OUT), .B(B[15]), .A(A[15]),
    .CARRY_IN(main_15_carry_out), .BINARY_CONV(BIN_CONV));
  xor xor_1 (OVERFLOW, main_15_carry_out, CARRY_OUT);
  nor nor_1 (ZERO, RESULT[0], RESULT[1], RESULT[2], RESULT[3], RESULT[4], RESULT[5], RESULT[6], RESULT[7], RESULT[8], RESULT[9], RESULT[10], RESULT[11], RESULT[12], RESULT[13], RESULT[14], RESULT[15]);
endmodule

module _16_BIT_ALU_USE (
  input  [15:0] in_1,
  input  [15:0] in_2,
  input  in_3,
  input  in_4,
  input  [1:0] in_5,
  output out_6,
  output out_7,
  output [15:0] out_8,
  output out_9
);

  _16_BIT_ALU u_16_bit_alu_1 (
    .CARRY_IN(in_3), .BIN_CONV(in_4), .OPRTN(in_5), .A(in_2), .B(in_1), .OVERFLOW(out_6), .CARRY_OUT(out_9),
    .RESULT(out_8), .ZERO(out_7));
  Hex_Digit_Display hex_digit_display_1 (.value(out_8[3:0]));  // open: dp
  Hex_Digit_Display hex_digit_display_2 (.value(out_8[7:4]));  // open: dp
  Hex_Digit_Display hex_digit_display_3 (.value(out_8[15:12]));  // open: dp
  Hex_Digit_Display hex_digit_display_4 (.value(out_8[11:8]));  // open: dp
endmodule
