// Logisim project Week 3 & 4.circ as structural Verilog: 12 circuits, main circuit main
module main (
  input  in_1,
  input  in_2,
  input  in_3,
  input  in_4,
  input  in_5,
  input  in_6,
  input  in_7,
  input  in_8,
  input  in_9,
  input  in_10,
  input  in_11,
  input  in_12,
  input  in_13,
  input  in_14,
  input  in_15,
  input  in_16,
  input  [7:0] in_17,
  input  in_18,
  input  in_19,
  input  in_20,
  input  in_21,
  input  in_22,
  input  in_23,
  input  in_24,
  input  [4:0] in_25,
  input  in_26,
  input  in_27,
  input  in_28,
  input  in_29,
  input  in_30,
  input  in_31,
  input  in_32,
  input  in_33,
  input  in_34,
  input  in_35,
  input  in_36,
  input  in_37,
  input  in_38,
  input  in_39,
  input  in_40,
  input  in_41,
  input  [3:0] in_42,
  input  in_43,
  input  in_44,
  input  in_45,
  output [7:0] out_46
);

  wire clock_1_out;
  wire [3:0] abus_1_output, abus_1_output_2, alubus_1_output_2, alubus_1_output_3;
  wire [7:0] alu16bit_1_output_to_register, alubus_1_output, CCR_p3, dbus_1__8_bit_out, INPR_p3;
  wire [9:0] adder_1_out, AR_output, dbus_1__10_bit_out, IR_output, multiplexer_1_out, PC_output, SP_output,
       X_output;
  wire [9:8] abus_1_output_3;
  wire [15:0] AC_output, alu16bit_1_output, dbus_1__16_bit_out, dbus_1__16_bit_out_2, GPRA_output,
       GPRB_output, ram_1_data;
  wire [15:10] IR_output_2;

  _5_Bit_Register X (
    .INPUT(in_25), .L(in_21), .I(in_18), .C(in_15), .OUTPUT({X_output[9], X_output[3:0]}));  // open: CARRY_OUT
  Adder #(.width(10)) adder_1 (
    .a({{6{X_output[9]}}, X_output[3:0]}), .b(dbus_1__10_bit_out), .out(adder_1_out));  // open: cin, cout
  DBus dbus_1 (
    .D1(in_30), .D2(in_29), .D0(in_31), ._10_BIT_OUT(dbus_1__10_bit_out),
    ._16_BIT_OUT_2(dbus_1__16_bit_out_2), ._8_BIT_OUT(dbus_1__8_bit_out), .MEMORY(ram_1_data),
    .GPRB(GPRB_output), .GPRA(GPRA_output), .AC(AC_output),
    .ABUS({abus_1_output_3, abus_1_output_2, abus_1_output}), .INPR(INPR_p3), .IR({IR_output_2, IR_output}),
    ._16_BIT_OUT(dbus_1__16_bit_out), .X({X_output[9], X_output[3:0]}));
  Multiplexer #(.width(10), .enable("false")) multiplexer_1 (
    .in0(IR_output), .in1(adder_1_out), .out(multiplexer_1_out), .sel(in_14));
  Hex_Digit_Display hex_digit_display_1 (.value(alubus_1_output_3));  // open: dp
  Hex_Digit_Display hex_digit_display_2 (.value(alubus_1_output_2));  // open: dp
  Hex_Digit_Display hex_digit_display_3 (.value(AC_output[15:12]));  // open: dp
  Hex_Digit_Display hex_digit_display_4 (.value(AC_output[11:8]));  // open: dp
  _10_Bit_Register AR (
    .L(in_11), .INPUT(multiplexer_1_out), .I(in_8), .C(in_5), .OUTPUT(AR_output));  // open: CARRY_OUT
  _16_Bit_Register IR (
    .INPUT(dbus_1__16_bit_out), .OUTPUT({IR_output_2, IR_output}), .L(in_22), .I(in_19), .C(in_16));  // open: CARRY_OUT
  _16_Bit_Register GPRA (
    .INPUT(dbus_1__16_bit_out_2), .OUTPUT(GPRA_output), .L(in_36), .I(in_34), .C(in_32));  // open: CARRY_OUT
  Hex_Digit_Display hex_digit_display_5 (.value(alubus_1_output[3:0]));  // open: dp
  Hex_Digit_Display hex_digit_display_6 (.value(alubus_1_output[7:4]));  // open: dp
  Hex_Digit_Display hex_digit_display_7 (.value(AC_output[7:4]));  // open: dp
  Hex_Digit_Display hex_digit_display_8 (.value(AC_output[3:0]));  // open: dp
  RAM #(.addrWidth(10), .dataWidth(16), .bus("separate")) ram_1 (
    .addr({abus_1_output_3, abus_1_output_2, abus_1_output}), .din(dbus_1__16_bit_out_2), .data(ram_1_data),
    .str(in_1), .clk(clock_1_out), .ld(in_2));  // open: sel, clr
  _10_Bit_Register PC (
    .L(in_12), .INPUT(dbus_1__10_bit_out), .I(in_9), .C(in_6), .OUTPUT(PC_output));  // open: CARRY_OUT
  ALUBus alubus_1 (
    .S(in_38), .A(GPRA_output), .B(GPRB_output),
    .OUTPUT({alubus_1_output_3, alubus_1_output_2, alubus_1_output}));
  _16_Bit_Register GPRB (
    .INPUT(dbus_1__16_bit_out_2), .OUTPUT(GPRB_output), .L(in_37), .I(in_35), .C(in_33));  // open: CARRY_OUT
  ALU16Bit alu16bit_1 (
    .Input_from_Register(CCR_p3), .Output_to_Register(alu16bit_1_output_to_register),
    .A({alubus_1_output_3, alubus_1_output_2, alubus_1_output}), .Output(alu16bit_1_output), .B(AC_output),
    .S0(in_42));
  _10_Bit_Register SP (
    .L(in_13), .INPUT(dbus_1__10_bit_out), .I(in_10), .C(in_7), .OUTPUT(SP_output));  // open: CARRY_OUT
  Clock clock_1 (.out(clock_1_out));
  ABus abus_1 (
    .A0(in_3), .A1(in_4), .Adress_Register(AR_output), .Stack_Pointer(SP_output),
    .Program_Counter(PC_output), .Output({abus_1_output_3, abus_1_output_2, abus_1_output}));
  // _8_Bit_Register INPR: pin names not known; wires that end beside it: in_17, clock_1_out, INPR_p3, in_20, in_23, in_24
  // _8_Bit_Register OUTR: pin names not known; wires that end beside it: dbus_1__8_bit_out, clock_1_out, out_46, in_26, in_27, in_28
  Hex_Digit_Display hex_digit_display_9 (.value(dbus_1__16_bit_out_2[11:8]));  // open: dp
  Hex_Digit_Display hex_digit_display_10 (.value(dbus_1__16_bit_out_2[15:12]));  // open: dp
  _16_Bit_Register AC (
    .INPUT(alu16bit_1_output), .OUTPUT(AC_output), .L(in_45), .I(in_44), .C(in_43));  // open: CARRY_OUT
  Hex_Digit_Display hex_digit_display_11 (.value(dbus_1__16_bit_out_2[7:4]));  // open: dp
  Hex_Digit_Display hex_digit_display_12 (.value(dbus_1__16_bit_out_2[3:0]));  // open: dp
  // _8_Bit_Register CCR: pin names not known; wires that end beside it: alu16bit_1_output_to_register, clock_1_out, CCR_p3, in_39, in_40, in_41
  Hex_Digit_Display hex_digit_display_13 (.value(abus_1_output_2));  // open: dp
  Hex_Digit_Display hex_digit_display_14 (.value({2'b00, abus_1_output_3}));  // open: dp
  Hex_Digit_Display hex_digit_display_15 (.value(abus_1_output));  // open: dp

  // Notes on the sheet:
  //   Extension to 10bit
  //   ALU-BUS DISPLAY
  //   AC DISPLAY
  //   D-BUS DISPLAY
  //   A-BUS DISPLAY
endmodule

module _8_Bit_Register (
  input  [7:0] INPUT,
  input  L,
  input  I,
  input  C,
  output CARRY_OUT,
  output [7:0] OUTPUT
);

  wire and_2_out, and_3_out, and_4_out, and_5_out, and_6_out, and_7_out, and_8_out, and_9_out, and_10_out,
       and_11_out, and_12_out, and_13_out, and_14_out, and_15_out, and_16_out, and_17_out, and_18_out,
       and_19_out, and_20_out, and_21_out, and_22_out, and_23_out, and_24_out, and_25_out, and_26_out,
       CLOCK_out, not_1_out, not_2_out, not_3_out, not_4_out, not_5_out, not_6_out, not_7_out, not_8_out,
       not_9_out, not_10_out, or_1_out, or_2_out, or_3_out, or_4_out, or_5_out, or_6_out, or_7_out, or_8_out,
       or_9_out, or_10_out, or_11_out, or_12_out, or_13_out, or_14_out, or_15_out, or_16_out;

  not not_1 (not_1_out, L);
  not not_2 (not_2_out, INPUT[7]);
  not not_3 (not_3_out, INPUT[6]);
  not not_4 (not_4_out, INPUT[5]);
  not not_5 (not_5_out, INPUT[4]);
  not not_6 (not_6_out, INPUT[3]);
  not not_7 (not_7_out, INPUT[2]);
  not not_8 (not_8_out, INPUT[1]);
  not not_9 (not_9_out, INPUT[0]);
  not not_10 (not_10_out, I);
  and and_1 (CARRY_OUT, and_4_out, OUTPUT[7]);
  and and_2 (and_2_out, L, not_2_out);
  and and_3 (and_3_out, INPUT[7], L);
  and and_4 (and_4_out, and_7_out, OUTPUT[6]);
  and and_5 (and_5_out, L, not_3_out);
  and and_6 (and_6_out, INPUT[6], L);
  and and_7 (and_7_out, and_10_out, OUTPUT[5]);
  and and_8 (and_8_out, L, not_4_out);
  and and_9 (and_9_out, INPUT[5], L);
  and and_10 (and_10_out, and_13_out, OUTPUT[4]);
  and and_11 (and_11_out, L, not_5_out);
  and and_12 (and_12_out, INPUT[4], L);
  and and_13 (and_13_out, and_16_out, OUTPUT[3]);
  and and_14 (and_14_out, L, not_6_out);
  and and_15 (and_15_out, INPUT[3], L);
  and and_16 (and_16_out, and_19_out, OUTPUT[2]);
  and and_17 (and_17_out, L, not_7_out);
  and and_18 (and_18_out, INPUT[2], L);
  and and_19 (and_19_out, and_22_out, OUTPUT[1]);
  and and_20 (and_20_out, L, not_8_out);
  and and_21 (and_21_out, INPUT[1], L);
  and and_22 (and_22_out, and_26_out, OUTPUT[0]);
  and and_23 (and_23_out, L, not_9_out);
  and and_24 (and_24_out, INPUT[0], L);
  and and_25 (and_25_out, not_1_out, not_10_out, C);
  and and_26 (and_26_out, not_1_out, I);
  or or_1 (or_1_out, and_4_out, and_25_out, and_2_out);
  or or_2 (or_2_out, and_4_out, and_3_out);
  or or_3 (or_3_out, and_7_out, and_25_out, and_5_out);
  or or_4 (or_4_out, and_7_out, and_6_out);
  or or_5 (or_5_out, and_10_out, and_25_out, and_8_out);
  or or_6 (or_6_out, and_10_out, and_9_out);
  or or_7 (or_7_out, and_13_out, and_25_out, and_11_out);
  or or_8 (or_8_out, and_13_out, and_12_out);
  or or_9 (or_9_out, and_16_out, and_25_out, and_14_out);
  or or_10 (or_10_out, and_16_out, and_15_out);
  or or_11 (or_11_out, and_19_out, and_25_out, and_17_out);
  or or_12 (or_12_out, and_19_out, and_18_out);
  or or_13 (or_13_out, and_22_out, and_25_out, and_20_out);
  or or_14 (or_14_out, and_22_out, and_21_out);
  or or_15 (or_15_out, and_26_out, and_25_out, and_23_out);
  or or_16 (or_16_out, and_26_out, and_24_out);
  Clock CLOCK (.out(CLOCK_out));
  J_K_Flip_Flop j_k_ff_1 (.J(or_2_out), .clk(CLOCK_out), .K(or_1_out), .Q(OUTPUT[7]));  // open: Qn, preset, en, reset
  J_K_Flip_Flop j_k_ff_2 (.J(or_4_out), .clk(CLOCK_out), .K(or_3_out), .Q(OUTPUT[6]));  // open: Qn, preset, en, reset
  J_K_Flip_Flop j_k_ff_3 (.J(or_6_out), .clk(CLOCK_out), .K(or_5_out), .Q(OUTPUT[5]));  // open: Qn, preset, en, reset
  J_K_Flip_Flop j_k_ff_4 (.J(or_8_out), .clk(CLOCK_out), .K(or_7_out), .Q(OUTPUT[4]));  // open: Qn, preset, en, reset
  J_K_Flip_Flop j_k_ff_5 (.J(or_10_out), .clk(CLOCK_out), .K(or_9_out), .Q(OUTPUT[3]));  // open: Qn, preset, en, reset
  J_K_Flip_Flop j_k_ff_6 (.J(or_12_out), .clk(CLOCK_out), .K(or_11_out), .Q(OUTPUT[2]));  // open: Qn, preset, en, reset
  J_K_Flip_Flop j_k_ff_7 (.J(or_14_out), .clk(CLOCK_out), .K(or_13_out), .Q(OUTPUT[1]));  // open: Qn, preset, en, reset
  J_K_Flip_Flop j_k_ff_8 (.J(or_16_out), .clk(CLOCK_out), .K(or_15_out), .Q(OUTPUT[0]));  // open: Qn, preset, en, reset
endmodule

module ABus (
  input  A0,
  input  A1,
  input  [9:0] Adress_Register,
  input  [9:0] Stack_Pointer,
  input  [9:0] Program_Counter,
  output [9:0] Output
);

  wire decoder_1_out0, decoder_1_out1, decoder_1_out2, decoder_1_out3, decoder_2_out0, decoder_2_out1,
       decoder_2_out2, decoder_2_out3, decoder_3_out0, decoder_3_out1, decoder_3_out2, decoder_3_out3,
       decoder_4_out0, decoder_4_out1, decoder_4_out2, decoder_4_out3, decoder_5_out0, decoder_5_out1,
       decoder_5_out2, decoder_5_out3, decoder_6_out0, decoder_6_out1, decoder_6_out2, decoder_6_out3,
       decoder_7_out0, decoder_7_out1, decoder_7_out2, decoder_7_out3, decoder_8_out0, decoder_8_out1,
       decoder_8_out2, decoder_8_out3, decoder_9_out0, decoder_9_out1, decoder_9_out2, decoder_9_out3,
       decoder_10_out0, decoder_10_out1, decoder_10_out2, decoder_10_out3;

  assign Output[0] = decoder_1_out0 ? Program_Counter[0] : 1'bz;  // Controlled_Buffer controlled_buffer_1
  Decoder #(.select(2), .enable("false")) decoder_1 (
    .out0(decoder_1_out0), .out1(decoder_1_out1), .out2(decoder_1_out2), .out3(decoder_1_out3), .sel({A1, A0}));
  assign Output[0] = decoder_1_out1 ? Adress_Register[0] : 1'bz;  // Controlled_Buffer controlled_buffer_2
  assign Output[0] = decoder_1_out2 ? Stack_Pointer[0] : 1'bz;  // Controlled_Buffer controlled_buffer_3
  assign Output[0] = decoder_1_out3 ? Stack_Pointer[0] : 1'bz;  // Controlled_Buffer controlled_buffer_4
  assign Output[1] = decoder_2_out0 ? Program_Counter[1] : 1'bz;  // Controlled_Buffer controlled_buffer_5
  Decoder #(.select(2), .enable("false")) decoder_2 (
    .out0(decoder_2_out0), .out1(decoder_2_out1), .out2(decoder_2_out2), .out3(decoder_2_out3), .sel({A1, A0}));
  assign Output[1] = decoder_2_out1 ? Adress_Register[1] : 1'bz;  // Controlled_Buffer controlled_buffer_6
  assign Output[1] = decoder_2_out2 ? Stack_Pointer[1] : 1'bz;  // Controlled_Buffer controlled_buffer_7
  assign Output[1] = decoder_2_out3 ? Stack_Pointer[1] : 1'bz;  // Controlled_Buffer controlled_buffer_8
  assign Output[2] = decoder_3_out0 ? Program_Counter[2] : 1'bz;  // Controlled_Buffer controlled_buffer_9
  Decoder #(.select(2), .enable("false")) decoder_3 (
    .out0(decoder_3_out0), .out1(decoder_3_out1), .out2(decoder_3_out2), .out3(decoder_3_out3), .sel({A1, A0}));
  assign Output[2] = decoder_3_out1 ? Adress_Register[2] : 1'bz;  // Controlled_Buffer controlled_buffer_10
  assign Output[2] = decoder_3_out2 ? Stack_Pointer[2] : 1'bz;  // Controlled_Buffer controlled_buffer_11
  assign Output[2] = decoder_3_out3 ? Stack_Pointer[2] : 1'bz;  // Controlled_Buffer controlled_buffer_12
  assign Output[3] = decoder_4_out0 ? Program_Counter[3] : 1'bz;  // Controlled_Buffer controlled_buffer_13
  Decoder #(.select(2), .enable("false")) decoder_4 (
    .out0(decoder_4_out0), .out1(decoder_4_out1), .out2(decoder_4_out2), .out3(decoder_4_out3), .sel({A1, A0}));
  assign Output[3] = decoder_4_out1 ? Adress_Register[3] : 1'bz;  // Controlled_Buffer controlled_buffer_14
  assign Output[3] = decoder_4_out2 ? Stack_Pointer[3] : 1'bz;  // Controlled_Buffer controlled_buffer_15
  assign Output[3] = decoder_4_out3 ? Stack_Pointer[3] : 1'bz;  // Controlled_Buffer controlled_buffer_16
  assign Output[4] = decoder_5_out0 ? Program_Counter[4] : 1'bz;  // Controlled_Buffer controlled_buffer_17
  Decoder #(.select(2), .enable("false")) decoder_5 (
    .out0(decoder_5_out0), .out1(decoder_5_out1), .out2(decoder_5_out2), .out3(decoder_5_out3), .sel({A1, A0}));
  assign Output[4] = decoder_5_out1 ? Adress_Register[4] : 1'bz;  // Controlled_Buffer controlled_buffer_18
  assign Output[4] = decoder_5_out2 ? Stack_Pointer[4] : 1'bz;  // Controlled_Buffer controlled_buffer_19
  assign Output[4] = decoder_5_out3 ? Stack_Pointer[4] : 1'bz;  // Controlled_Buffer controlled_buffer_20
  assign Output[5] = decoder_6_out0 ? Program_Counter[5] : 1'bz;  // Controlled_Buffer controlled_buffer_21
  Decoder #(.select(2), .enable("false")) decoder_6 (
    .out0(decoder_6_out0), .out1(decoder_6_out1), .out2(decoder_6_out2), .out3(decoder_6_out3), .sel({A1, A0}));
  assign Output[5] = decoder_6_out1 ? Adress_Register[5] : 1'bz;  // Controlled_Buffer controlled_buffer_22
  assign Output[5] = decoder_6_out2 ? Stack_Pointer[5] : 1'bz;  // Controlled_Buffer controlled_buffer_23
  assign Output[5] = decoder_6_out3 ? Stack_Pointer[5] : 1'bz;  // Controlled_Buffer controlled_buffer_24
  assign Output[6] = decoder_7_out0 ? Program_Counter[6] : 1'bz;  // Controlled_Buffer controlled_buffer_25
  Decoder #(.select(2), .enable("false")) decoder_7 (
    .out0(decoder_7_out0), .out1(decoder_7_out1), .out2(decoder_7_out2), .out3(decoder_7_out3), .sel({A1, A0}));
  assign Output[6] = decoder_7_out1 ? Adress_Register[6] : 1'bz;  // Controlled_Buffer controlled_buffer_26
  assign Output[6] = decoder_7_out2 ? Stack_Pointer[6] : 1'bz;  // Controlled_Buffer controlled_buffer_27
  assign Output[6] = decoder_7_out3 ? Stack_Pointer[6] : 1'bz;  // Controlled_Buffer controlled_buffer_28
  assign Output[7] = decoder_8_out0 ? Program_Counter[7] : 1'bz;  // Controlled_Buffer controlled_buffer_29
  Decoder #(.select(2), .enable("false")) decoder_8 (
    .out0(decoder_8_out0), .out1(decoder_8_out1), .out2(decoder_8_out2), .out3(decoder_8_out3), .sel({A1, A0}));
  assign Output[7] = decoder_8_out1 ? Adress_Register[7] : 1'bz;  // Controlled_Buffer controlled_buffer_30
  assign Output[7] = decoder_8_out2 ? Stack_Pointer[7] : 1'bz;  // Controlled_Buffer controlled_buffer_31
  assign Output[7] = decoder_8_out3 ? Stack_Pointer[7] : 1'bz;  // Controlled_Buffer controlled_buffer_32
  assign Output[8] = decoder_9_out0 ? Program_Counter[8] : 1'bz;  // Controlled_Buffer controlled_buffer_33
  Decoder #(.select(2), .enable("false")) decoder_9 (
    .out0(decoder_9_out0), .out1(decoder_9_out1), .out2(decoder_9_out2), .out3(decoder_9_out3), .sel({A1, A0}));
  assign Output[8] = decoder_9_out1 ? Adress_Register[8] : 1'bz;  // Controlled_Buffer controlled_buffer_34
  assign Output[8] = decoder_9_out2 ? Stack_Pointer[8] : 1'bz;  // Controlled_Buffer controlled_buffer_35
  assign Output[8] = decoder_9_out3 ? Stack_Pointer[8] : 1'bz;  // Controlled_Buffer controlled_buffer_36
  assign Output[9] = decoder_10_out0 ? Program_Counter[9] : 1'bz;  // Controlled_Buffer controlled_buffer_37
  Decoder #(.select(2), .enable("false")) decoder_10 (
    .out0(decoder_10_out0), .out1(decoder_10_out1), .out2(decoder_10_out2), .out3(decoder_10_out3),
    .sel({A1, A0}));
  assign Output[9] = decoder_10_out1 ? Adress_Register[9] : 1'bz;  // Controlled_Buffer controlled_buffer_38
  assign Output[9] = decoder_10_out2 ? Stack_Pointer[9] : 1'bz;  // Controlled_Buffer controlled_buffer_39
  assign Output[9] = decoder_10_out3 ? Stack_Pointer[9] : 1'bz;  // Controlled_Buffer controlled_buffer_40

  // Other names for the same wires on the sheet: AR0 = Adress_Register[0]; AR1 = Adress_Register[1];
  //   AR2 = Adress_Register[2]; AR3 = Adress_Register[3]; AR4 = Adress_Register[4]; AR5 = Adress_Register[5];
  //   AR6 = Adress_Register[6]; AR7 = Adress_Register[7]; AR8 = Adress_Register[8]; AR9 = Adress_Register[9];
  //   A0_t = Output[0]; A1_t = Output[1]; A2 = Output[2]; A3 = Output[3]; A4 = Output[4]; A5 = Output[5];
  //   A6 = Output[6]; A7 = Output[7]; A8 = Output[8]; A9 = Output[9]; PC0 = Program_Counter[0];
  //   PC1 = Program_Counter[1]; PC2 = Program_Counter[2]; PC3 = Program_Counter[3]; PC4 = Program_Counter[4];
  //   PC5 = Program_Counter[5]; PC6 = Program_Counter[6]; PC7 = Program_Counter[7]; PC8 = Program_Counter[8];
  //   PC9 = Program_Counter[9]; SP0 = Stack_Pointer[0]; SP1 = Stack_Pointer[1]; SP2 = Stack_Pointer[2];
  //   SP3 = Stack_Pointer[3]; SP4 = Stack_Pointer[4]; SP5 = Stack_Pointer[5]; SP6 = Stack_Pointer[6];
  //   SP7 = Stack_Pointer[7]; SP8 = Stack_Pointer[8]; SP9 = Stack_Pointer[9]
endmodule

module DBus (
  input  D1,
  input  D2,
  input  D0,
  input  [15:0] MEMORY,
  input  [15:0] GPRB,
  input  [15:0] GPRA,
  input  [15:0] AC,
  input  [9:0] ABUS,
  input  [7:0] INPR,
  input  [15:0] IR,
  input  [4:0] X,
  output [9:0] _10_BIT_OUT,
  output [15:0] _16_BIT_OUT,
  output [15:0] _16_BIT_OUT_2,
  output [7:0] _8_BIT_OUT
);

  wire decoder_1_out0, decoder_1_out1, decoder_1_out2, decoder_1_out3, decoder_1_out4, decoder_1_out5,
       decoder_1_out6, decoder_1_out7, decoder_2_out0, decoder_2_out1, decoder_2_out2, decoder_2_out3,
       decoder_2_out4, decoder_2_out5, decoder_2_out6, decoder_2_out7, decoder_3_out0, decoder_3_out1,
       decoder_3_out2, decoder_3_out3, decoder_3_out4, decoder_3_out5, decoder_3_out6, decoder_3_out7,
       decoder_4_out0, decoder_4_out1, decoder_4_out2, decoder_4_out3, decoder_4_out4, decoder_4_out5,
       decoder_4_out6, decoder_4_out7, decoder_5_out0, decoder_5_out1, decoder_5_out2, decoder_5_out3,
       decoder_5_out4, decoder_5_out5, decoder_5_out6, decoder_5_out7, decoder_6_out0, decoder_6_out1,
       decoder_6_out2, decoder_6_out3, decoder_6_out4, decoder_6_out5, decoder_6_out6, decoder_6_out7,
       decoder_7_out0, decoder_7_out1, decoder_7_out2, decoder_7_out3, decoder_7_out4, decoder_7_out5,
       decoder_7_out6, decoder_7_out7, decoder_8_out0, decoder_8_out1, decoder_8_out2, decoder_8_out3,
       decoder_8_out4, decoder_8_out5, decoder_8_out6, decoder_8_out7, decoder_9_out0, decoder_9_out1,
       decoder_9_out2, decoder_9_out3, decoder_9_out4, decoder_9_out5, decoder_9_out6, decoder_9_out7,
       decoder_10_out0, decoder_10_out1, decoder_10_out2, decoder_10_out3, decoder_10_out4, decoder_10_out5,
       decoder_10_out6, decoder_10_out7, decoder_11_out0, decoder_11_out1, decoder_11_out2, decoder_11_out3,
       decoder_11_out4, decoder_11_out5, decoder_11_out6, decoder_11_out7, decoder_12_out0, decoder_12_out1,
       decoder_12_out2, decoder_12_out3, decoder_12_out4, decoder_12_out5, decoder_12_out6, decoder_12_out7,
       decoder_13_out0, decoder_13_out1, decoder_13_out2, decoder_13_out3, decoder_13_out4, decoder_13_out5,
       decoder_13_out6, decoder_13_out7, decoder_14_out0, decoder_14_out1, decoder_14_out2, decoder_14_out3,
       decoder_14_out4, decoder_14_out5, decoder_14_out6, decoder_14_out7, decoder_15_out0, decoder_15_out1,
       decoder_15_out2, decoder_15_out3, decoder_15_out4, decoder_15_out5, decoder_15_out6, decoder_15_out7,
       decoder_16_out0, decoder_16_out1, decoder_16_out2, decoder_16_out3, decoder_16_out4, decoder_16_out5,
       decoder_16_out6, decoder_16_out7;

  Decoder #(.select(3), .enable("false")) decoder_1 (
    .out0(decoder_1_out0), .out1(decoder_1_out1), .out2(decoder_1_out2), .out3(decoder_1_out3),
    .out4(decoder_1_out4), .out5(decoder_1_out5), .out6(decoder_1_out6), .out7(decoder_1_out7),
    .sel({D2, D1, D0}));
  Decoder #(.select(3), .enable("false")) decoder_2 (
    .out0(decoder_2_out0), .out1(decoder_2_out1), .out2(decoder_2_out2), .out3(decoder_2_out3),
    .out4(decoder_2_out4), .out5(decoder_2_out5), .out6(decoder_2_out6), .out7(decoder_2_out7),
    .sel({D2, D1, D0}));
  Decoder #(.select(3), .enable("false")) decoder_3 (
    .out0(decoder_3_out0), .out1(decoder_3_out1), .out2(decoder_3_out2), .out3(decoder_3_out3),
    .out4(decoder_3_out4), .out5(decoder_3_out5), .out6(decoder_3_out6), .out7(decoder_3_out7),
    .sel({D2, D1, D0}));
  Decoder #(.select(3), .enable("false")) decoder_4 (
    .out0(decoder_4_out0), .out1(decoder_4_out1), .out2(decoder_4_out2), .out3(decoder_4_out3),
    .out4(decoder_4_out4), .out5(decoder_4_out5), .out6(decoder_4_out6), .out7(decoder_4_out7),
    .sel({D2, D1, D0}));
  Decoder #(.select(3), .enable("false")) decoder_5 (
    .out0(decoder_5_out0), .out1(decoder_5_out1), .out2(decoder_5_out2), .out3(decoder_5_out3),
    .out4(decoder_5_out4), .out5(decoder_5_out5), .out6(decoder_5_out6), .out7(decoder_5_out7),
    .sel({D2, D1, D0}));
  Decoder #(.select(3), .enable("false")) decoder_6 (
    .out0(decoder_6_out0), .out1(decoder_6_out1), .out2(decoder_6_out2), .out3(decoder_6_out3),
    .out4(decoder_6_out4), .out5(decoder_6_out5), .out6(decoder_6_out6), .out7(decoder_6_out7),
    .sel({D2, D1, D0}));
  Decoder #(.select(3), .enable("false")) decoder_7 (
    .out0(decoder_7_out0), .out1(decoder_7_out1), .out2(decoder_7_out2), .out3(decoder_7_out3),
    .out4(decoder_7_out4), .out5(decoder_7_out5), .out6(decoder_7_out6), .out7(decoder_7_out7),
    .sel({D2, D1, D0}));
  Decoder #(.select(3), .enable("false")) decoder_8 (
    .out0(decoder_8_out0), .out1(decoder_8_out1), .out2(decoder_8_out2), .out3(decoder_8_out3),
    .out4(decoder_8_out4), .out5(decoder_8_out5), .out6(decoder_8_out6), .out7(decoder_8_out7),
    .sel({D2, D1, D0}));
  Decoder #(.select(3), .enable("false")) decoder_9 (
    .out0(decoder_9_out0), .out1(decoder_9_out1), .out2(decoder_9_out2), .out3(decoder_9_out3),
    .out4(decoder_9_out4), .out5(decoder_9_out5), .out6(decoder_9_out6), .out7(decoder_9_out7),
    .sel({D2, D1, D0}));
  Decoder #(.select(3), .enable("false")) decoder_10 (
    .out0(decoder_10_out0), .out1(decoder_10_out1), .out2(decoder_10_out2), .out3(decoder_10_out3),
    .out4(decoder_10_out4), .out5(decoder_10_out5), .out6(decoder_10_out6), .out7(decoder_10_out7),
    .sel({D2, D1, D0}));
  Decoder #(.select(3), .enable("false")) decoder_11 (
    .out0(decoder_11_out0), .out1(decoder_11_out1), .out2(decoder_11_out2), .out3(decoder_11_out3),
    .out4(decoder_11_out4), .out5(decoder_11_out5), .out6(decoder_11_out6), .out7(decoder_11_out7),
    .sel({D2, D1, D0}));
  Decoder #(.select(3), .enable("false")) decoder_12 (
    .out0(decoder_12_out0), .out1(decoder_12_out1), .out2(decoder_12_out2), .out3(decoder_12_out3),
    .out4(decoder_12_out4), .out5(decoder_12_out5), .out6(decoder_12_out6), .out7(decoder_12_out7),
    .sel({D2, D1, D0}));
  Decoder #(.select(3), .enable("false")) decoder_13 (
    .out0(decoder_13_out0), .out1(decoder_13_out1), .out2(decoder_13_out2), .out3(decoder_13_out3),
    .out4(decoder_13_out4), .out5(decoder_13_out5), .out6(decoder_13_out6), .out7(decoder_13_out7),
    .sel({D2, D1, D0}));
  Decoder #(.select(3), .enable("false")) decoder_14 (
    .out0(decoder_14_out0), .out1(decoder_14_out1), .out2(decoder_14_out2), .out3(decoder_14_out3),
    .out4(decoder_14_out4), .out5(decoder_14_out5), .out6(decoder_14_out6), .out7(decoder_14_out7),
    .sel({D2, D1, D0}));
  Decoder #(.select(3), .enable("false")) decoder_15 (
    .out0(decoder_15_out0), .out1(decoder_15_out1), .out2(decoder_15_out2), .out3(decoder_15_out3),
    .out4(decoder_15_out4), .out5(decoder_15_out5), .out6(decoder_15_out6), .out7(decoder_15_out7),
    .sel({D2, D1, D0}));
  Decoder #(.select(3), .enable("false")) decoder_16 (
    .out0(decoder_16_out0), .out1(decoder_16_out1), .out2(decoder_16_out2), .out3(decoder_16_out3),
    .out4(decoder_16_out4), .out5(decoder_16_out5), .out6(decoder_16_out6), .out7(decoder_16_out7),
    .sel({D2, D1, D0}));
  assign _8_BIT_OUT[0] = decoder_8_out0 ? MEMORY[0] : 1'bz;  // Controlled_Buffer controlled_buffer_1
  assign _8_BIT_OUT[1] = decoder_9_out0 ? MEMORY[1] : 1'bz;  // Controlled_Buffer controlled_buffer_2
  assign _8_BIT_OUT[1] = decoder_9_out1 ? ABUS[1] : 1'bz;  // Controlled_Buffer controlled_buffer_3
  assign _8_BIT_OUT[2] = decoder_10_out0 ? MEMORY[2] : 1'bz;  // Controlled_Buffer controlled_buffer_4
  assign _8_BIT_OUT[2] = decoder_10_out1 ? ABUS[2] : 1'bz;  // Controlled_Buffer controlled_buffer_5
  assign _8_BIT_OUT[3] = decoder_11_out0 ? MEMORY[3] : 1'bz;  // Controlled_Buffer controlled_buffer_6
  assign _8_BIT_OUT[3] = decoder_11_out1 ? ABUS[3] : 1'bz;  // Controlled_Buffer controlled_buffer_7
  assign _8_BIT_OUT[4] = decoder_12_out0 ? MEMORY[4] : 1'bz;  // Controlled_Buffer controlled_buffer_8
  assign _8_BIT_OUT[4] = decoder_12_out1 ? ABUS[4] : 1'bz;  // Controlled_Buffer controlled_buffer_9
  assign _8_BIT_OUT[5] = decoder_1_out0 ? MEMORY[5] : 1'bz;  // Controlled_Buffer controlled_buffer_10
  assign _8_BIT_OUT[5] = decoder_1_out1 ? ABUS[5] : 1'bz;  // Controlled_Buffer controlled_buffer_11
  assign _8_BIT_OUT[6] = decoder_2_out0 ? MEMORY[6] : 1'bz;  // Controlled_Buffer controlled_buffer_12
  assign _8_BIT_OUT[6] = decoder_2_out1 ? ABUS[6] : 1'bz;  // Controlled_Buffer controlled_buffer_13
  assign _8_BIT_OUT[7] = decoder_3_out0 ? MEMORY[7] : 1'bz;  // Controlled_Buffer controlled_buffer_14
  assign _8_BIT_OUT[7] = decoder_3_out1 ? ABUS[7] : 1'bz;  // Controlled_Buffer controlled_buffer_15
  assign _10_BIT_OUT[8] = decoder_4_out0 ? MEMORY[8] : 1'bz;  // Controlled_Buffer controlled_buffer_16
  assign _10_BIT_OUT[8] = decoder_4_out1 ? ABUS[8] : 1'bz;  // Controlled_Buffer controlled_buffer_17
  assign _10_BIT_OUT[9] = decoder_5_out0 ? MEMORY[9] : 1'bz;  // Controlled_Buffer controlled_buffer_18
  assign _10_BIT_OUT[9] = decoder_5_out1 ? ABUS[9] : 1'bz;  // Controlled_Buffer controlled_buffer_19
  assign _16_BIT_OUT[10] = decoder_6_out0 ? MEMORY[10] : 1'bz;  // Controlled_Buffer controlled_buffer_20
  assign _16_BIT_OUT[10] = decoder_6_out1 ? 1'b0 : 1'bz;  // Controlled_Buffer controlled_buffer_21
  assign _16_BIT_OUT[11] = decoder_7_out0 ? MEMORY[11] : 1'bz;  // Controlled_Buffer controlled_buffer_22
  assign _16_BIT_OUT[11] = decoder_7_out1 ? 1'b0 : 1'bz;  // Controlled_Buffer controlled_buffer_23
  assign _16_BIT_OUT[12] = decoder_13_out0 ? MEMORY[12] : 1'bz;  // Controlled_Buffer controlled_buffer_24
  assign _16_BIT_OUT[12] = decoder_13_out1 ? 1'b0 : 1'bz;  // Controlled_Buffer controlled_buffer_25
  assign _16_BIT_OUT[13] = decoder_14_out0 ? MEMORY[13] : 1'bz;  // Controlled_Buffer controlled_buffer_26
  assign _16_BIT_OUT[14] = decoder_15_out0 ? MEMORY[14] : 1'bz;  // Controlled_Buffer controlled_buffer_27
  assign _16_BIT_OUT[14] = decoder_15_out1 ? 1'b0 : 1'bz;  // Controlled_Buffer controlled_buffer_28
  assign _16_BIT_OUT[15] = decoder_16_out0 ? MEMORY[15] : 1'bz;  // Controlled_Buffer controlled_buffer_29
  assign _16_BIT_OUT[15] = decoder_16_out1 ? 1'b0 : 1'bz;  // Controlled_Buffer controlled_buffer_30
  assign _8_BIT_OUT[0] = decoder_8_out1 ? ABUS[0] : 1'bz;  // Controlled_Buffer controlled_buffer_31
  assign _8_BIT_OUT[0] = decoder_8_out2 ? GPRB[0] : 1'bz;  // Controlled_Buffer controlled_buffer_32
  assign _8_BIT_OUT[1] = decoder_9_out2 ? GPRB[1] : 1'bz;  // Controlled_Buffer controlled_buffer_33
  assign _8_BIT_OUT[1] = decoder_9_out3 ? AC[1] : 1'bz;  // Controlled_Buffer controlled_buffer_34
  assign _8_BIT_OUT[2] = decoder_10_out2 ? GPRB[2] : 1'bz;  // Controlled_Buffer controlled_buffer_35
  assign _8_BIT_OUT[2] = decoder_10_out3 ? AC[2] : 1'bz;  // Controlled_Buffer controlled_buffer_36
  assign _8_BIT_OUT[3] = decoder_11_out2 ? GPRB[3] : 1'bz;  // Controlled_Buffer controlled_buffer_37
  assign _8_BIT_OUT[3] = decoder_11_out3 ? AC[3] : 1'bz;  // Controlled_Buffer controlled_buffer_38
  assign _8_BIT_OUT[4] = decoder_12_out2 ? GPRB[4] : 1'bz;  // Controlled_Buffer controlled_buffer_39
  assign _8_BIT_OUT[4] = decoder_12_out3 ? AC[4] : 1'bz;  // Controlled_Buffer controlled_buffer_40
  assign _8_BIT_OUT[5] = decoder_1_out2 ? GPRB[5] : 1'bz;  // Controlled_Buffer controlled_buffer_41
  assign _8_BIT_OUT[5] = decoder_1_out3 ? AC[5] : 1'bz;  // Controlled_Buffer controlled_buffer_42
  assign _8_BIT_OUT[6] = decoder_2_out2 ? GPRB[6] : 1'bz;  // Controlled_Buffer controlled_buffer_43
  assign _8_BIT_OUT[6] = decoder_2_out3 ? AC[6] : 1'bz;  // Controlled_Buffer controlled_buffer_44
  assign _8_BIT_OUT[7] = decoder_3_out2 ? GPRB[7] : 1'bz;  // Controlled_Buffer controlled_buffer_45
  assign _8_BIT_OUT[7] = decoder_3_out3 ? AC[7] : 1'bz;  // Controlled_Buffer controlled_buffer_46
  assign _10_BIT_OUT[8] = decoder_4_out2 ? GPRB[8] : 1'bz;  // Controlled_Buffer controlled_buffer_47
  assign _10_BIT_OUT[8] = decoder_4_out3 ? AC[8] : 1'bz;  // Controlled_Buffer controlled_buffer_48
  assign _10_BIT_OUT[9] = decoder_5_out2 ? GPRB[9] : 1'bz;  // Controlled_Buffer controlled_buffer_49
  assign _10_BIT_OUT[9] = decoder_5_out3 ? AC[9] : 1'bz;  // Controlled_Buffer controlled_buffer_50
  assign _16_BIT_OUT[10] = decoder_6_out2 ? GPRB[10] : 1'bz;  // Controlled_Buffer controlled_buffer_51
  assign _16_BIT_OUT[10] = decoder_6_out3 ? AC[10] : 1'bz;  // Controlled_Buffer controlled_buffer_52
  assign _16_BIT_OUT[11] = decoder_7_out2 ? GPRB[11] : 1'bz;  // Controlled_Buffer controlled_buffer_53
  assign _16_BIT_OUT[11] = decoder_7_out3 ? AC[11] : 1'bz;  // Controlled_Buffer controlled_buffer_54
  assign _16_BIT_OUT[12] = decoder_13_out2 ? GPRB[12] : 1'bz;  // Controlled_Buffer controlled_buffer_55
  assign _16_BIT_OUT[12] = decoder_13_out3 ? AC[12] : 1'bz;  // Controlled_Buffer controlled_buffer_56
  assign _16_BIT_OUT[13] = decoder_14_out1 ? 1'b0 : 1'bz;  // Controlled_Buffer controlled_buffer_57
  assign _16_BIT_OUT[13] = decoder_14_out2 ? GPRB[13] : 1'bz;  // Controlled_Buffer controlled_buffer_58
  assign _16_BIT_OUT[14] = decoder_15_out2 ? GPRB[14] : 1'bz;  // Controlled_Buffer controlled_buffer_59
  assign _16_BIT_OUT[14] = decoder_15_out3 ? AC[14] : 1'bz;  // Controlled_Buffer controlled_buffer_60
  assign _16_BIT_OUT[15] = decoder_16_out2 ? GPRB[15] : 1'bz;  // Controlled_Buffer controlled_buffer_61
  assign _16_BIT_OUT[15] = decoder_16_out3 ? AC[15] : 1'bz;  // Controlled_Buffer controlled_buffer_62
  assign _8_BIT_OUT[0] = decoder_8_out3 ? AC[0] : 1'bz;  // Controlled_Buffer controlled_buffer_63
  assign _8_BIT_OUT[0] = decoder_8_out4 ? GPRA[0] : 1'bz;  // Controlled_Buffer controlled_buffer_64
  assign _8_BIT_OUT[0] = decoder_8_out5 ? X[0] : 1'bz;  // Controlled_Buffer controlled_buffer_65
  assign _8_BIT_OUT[1] = decoder_9_out4 ? GPRA[1] : 1'bz;  // Controlled_Buffer controlled_buffer_66
  assign _8_BIT_OUT[1] = decoder_9_out5 ? X[1] : 1'bz;  // Controlled_Buffer controlled_buffer_67
  assign _8_BIT_OUT[2] = decoder_10_out4 ? GPRA[2] : 1'bz;  // Controlled_Buffer controlled_buffer_68
  assign _8_BIT_OUT[2] = decoder_10_out5 ? X[2] : 1'bz;  // Controlled_Buffer controlled_buffer_69
  assign _8_BIT_OUT[3] = decoder_11_out4 ? GPRA[3] : 1'bz;  // Controlled_Buffer controlled_buffer_70
  assign _8_BIT_OUT[3] = decoder_11_out5 ? X[3] : 1'bz;  // Controlled_Buffer controlled_buffer_71
  assign _8_BIT_OUT[4] = decoder_12_out4 ? GPRA[4] : 1'bz;  // Controlled_Buffer controlled_buffer_72
  assign _8_BIT_OUT[4] = decoder_12_out5 ? X[4] : 1'bz;  // Controlled_Buffer controlled_buffer_73
  assign _8_BIT_OUT[5] = decoder_1_out4 ? GPRA[5] : 1'bz;  // Controlled_Buffer controlled_buffer_74
  assign _8_BIT_OUT[5] = decoder_1_out5 ? X[4] : 1'bz;  // Controlled_Buffer controlled_buffer_75
  assign _8_BIT_OUT[5] = decoder_1_out6 ? INPR[5] : 1'bz;  // Controlled_Buffer controlled_buffer_76
  assign _8_BIT_OUT[6] = decoder_2_out4 ? GPRA[6] : 1'bz;  // Controlled_Buffer controlled_buffer_77
  assign _8_BIT_OUT[6] = decoder_2_out5 ? X[4] : 1'bz;  // Controlled_Buffer controlled_buffer_78
  assign _8_BIT_OUT[6] = decoder_2_out6 ? INPR[6] : 1'bz;  // Controlled_Buffer controlled_buffer_79
  assign _8_BIT_OUT[7] = decoder_3_out4 ? GPRA[7] : 1'bz;  // Controlled_Buffer controlled_buffer_80
  assign _8_BIT_OUT[7] = decoder_3_out5 ? X[4] : 1'bz;  // Controlled_Buffer controlled_buffer_81
  assign _8_BIT_OUT[7] = decoder_3_out6 ? INPR[7] : 1'bz;  // Controlled_Buffer controlled_buffer_82
  assign _10_BIT_OUT[8] = decoder_4_out4 ? GPRA[8] : 1'bz;  // Controlled_Buffer controlled_buffer_83
  assign _10_BIT_OUT[8] = decoder_4_out5 ? X[4] : 1'bz;  // Controlled_Buffer controlled_buffer_84
  assign _10_BIT_OUT[8] = decoder_4_out6 ? 1'b0 : 1'bz;  // Controlled_Buffer controlled_buffer_85
  assign _10_BIT_OUT[9] = decoder_5_out4 ? GPRA[9] : 1'bz;  // Controlled_Buffer controlled_buffer_86
  assign _10_BIT_OUT[9] = decoder_5_out5 ? X[4] : 1'bz;  // Controlled_Buffer controlled_buffer_87
  assign _10_BIT_OUT[9] = decoder_5_out6 ? 1'b0 : 1'bz;  // Controlled_Buffer controlled_buffer_88
  assign _16_BIT_OUT[10] = decoder_6_out4 ? GPRA[10] : 1'bz;  // Controlled_Buffer controlled_buffer_89
  assign _16_BIT_OUT[10] = decoder_6_out5 ? X[4] : 1'bz;  // Controlled_Buffer controlled_buffer_90
  assign _16_BIT_OUT[10] = decoder_6_out6 ? 1'b0 : 1'bz;  // Controlled_Buffer controlled_buffer_91
  assign _16_BIT_OUT[11] = decoder_7_out4 ? GPRA[11] : 1'bz;  // Controlled_Buffer controlled_buffer_92
  assign _16_BIT_OUT[11] = decoder_7_out5 ? X[4] : 1'bz;  // Controlled_Buffer controlled_buffer_93
  assign _16_BIT_OUT[11] = decoder_7_out6 ? 1'b0 : 1'bz;  // Controlled_Buffer controlled_buffer_94
  assign _16_BIT_OUT[12] = decoder_13_out4 ? GPRA[12] : 1'bz;  // Controlled_Buffer controlled_buffer_95
  assign _16_BIT_OUT[12] = decoder_13_out5 ? X[4] : 1'bz;  // Controlled_Buffer controlled_buffer_96
  assign _16_BIT_OUT[13] = decoder_14_out3 ? AC[13] : 1'bz;  // Controlled_Buffer controlled_buffer_97
  assign _16_BIT_OUT[13] = decoder_14_out4 ? GPRA[13] : 1'bz;  // Controlled_Buffer controlled_buffer_98
  assign _16_BIT_OUT[13] = decoder_14_out5 ? X[4] : 1'bz;  // Controlled_Buffer controlled_buffer_99
  assign _16_BIT_OUT[14] = decoder_15_out4 ? GPRA[14] : 1'bz;  // Controlled_Buffer controlled_buffer_100
  assign _16_BIT_OUT[14] = decoder_15_out5 ? X[4] : 1'bz;  // Controlled_Buffer controlled_buffer_101
  assign _16_BIT_OUT[15] = decoder_16_out4 ? GPRA[15] : 1'bz;  // Controlled_Buffer controlled_buffer_102
  assign _16_BIT_OUT[15] = decoder_16_out5 ? X[4] : 1'bz;  // Controlled_Buffer controlled_buffer_103
  assign _8_BIT_OUT[0] = decoder_8_out6 ? INPR[0] : 1'bz;  // Controlled_Buffer controlled_buffer_104
  assign _8_BIT_OUT[0] = decoder_8_out7 ? IR[0] : 1'bz;  // Controlled_Buffer controlled_buffer_105
  assign _8_BIT_OUT[1] = decoder_9_out6 ? INPR[1] : 1'bz;  // Controlled_Buffer controlled_buffer_106
  assign _8_BIT_OUT[1] = decoder_9_out7 ? IR[1] : 1'bz;  // Controlled_Buffer controlled_buffer_107
  assign _8_BIT_OUT[2] = decoder_10_out6 ? INPR[2] : 1'bz;  // Controlled_Buffer controlled_buffer_108
  assign _8_BIT_OUT[2] = decoder_10_out7 ? IR[2] : 1'bz;  // Controlled_Buffer controlled_buffer_109
  assign _8_BIT_OUT[3] = decoder_11_out6 ? INPR[3] : 1'bz;  // Controlled_Buffer controlled_buffer_110
  assign _8_BIT_OUT[3] = decoder_11_out7 ? IR[3] : 1'bz;  // Controlled_Buffer controlled_buffer_111
  assign _8_BIT_OUT[4] = decoder_12_out6 ? INPR[4] : 1'bz;  // Controlled_Buffer controlled_buffer_112
  assign _8_BIT_OUT[4] = decoder_12_out7 ? IR[4] : 1'bz;  // Controlled_Buffer controlled_buffer_113
  assign _8_BIT_OUT[5] = decoder_1_out7 ? IR[5] : 1'bz;  // Controlled_Buffer controlled_buffer_114
  assign _8_BIT_OUT[6] = decoder_2_out7 ? IR[6] : 1'bz;  // Controlled_Buffer controlled_buffer_115
  assign _8_BIT_OUT[7] = decoder_3_out7 ? IR[7] : 1'bz;  // Controlled_Buffer controlled_buffer_116
  assign _10_BIT_OUT[8] = decoder_4_out7 ? IR[8] : 1'bz;  // Controlled_Buffer controlled_buffer_117
  assign _10_BIT_OUT[9] = decoder_5_out7 ? IR[9] : 1'bz;  // Controlled_Buffer controlled_buffer_118
  assign _16_BIT_OUT[10] = decoder_6_out7 ? IR[10] : 1'bz;  // Controlled_Buffer controlled_buffer_119
  assign _16_BIT_OUT[11] = decoder_7_out7 ? IR[11] : 1'bz;  // Controlled_Buffer controlled_buffer_120
  assign _16_BIT_OUT[12] = decoder_13_out6 ? 1'b0 : 1'bz;  // Controlled_Buffer controlled_buffer_121
  assign _16_BIT_OUT[12] = decoder_13_out7 ? IR[12] : 1'bz;  // Controlled_Buffer controlled_buffer_122
  assign _16_BIT_OUT[13] = decoder_14_out6 ? 1'b0 : 1'bz;  // Controlled_Buffer controlled_buffer_123
  assign _16_BIT_OUT[13] = decoder_14_out7 ? IR[13] : 1'bz;  // Controlled_Buffer controlled_buffer_124
  assign _16_BIT_OUT[14] = decoder_15_out6 ? 1'b0 : 1'bz;  // Controlled_Buffer controlled_buffer_125
  assign _16_BIT_OUT[14] = decoder_15_out7 ? IR[14] : 1'bz;  // Controlled_Buffer controlled_buffer_126
  assign _16_BIT_OUT[15] = decoder_16_out6 ? 1'b0 : 1'bz;  // Controlled_Buffer controlled_buffer_127
  assign _16_BIT_OUT[15] = decoder_16_out7 ? IR[15] : 1'bz;  // Controlled_Buffer controlled_buffer_128

  assign _10_BIT_OUT[7:0] = _8_BIT_OUT;
  assign _16_BIT_OUT[9:0] = {_10_BIT_OUT[9:8], _8_BIT_OUT};
  assign _16_BIT_OUT_2 = {_16_BIT_OUT[15:10], _10_BIT_OUT[9:8], _8_BIT_OUT};

  // Other names for the same wires on the sheet: D0_t = _8_BIT_OUT[0]; D1_t = _8_BIT_OUT[1]; D2_t = _8_BIT_OUT[2];
  //   D3 = _8_BIT_OUT[3]; D4 = _8_BIT_OUT[4]; D5 = _8_BIT_OUT[5]; D6 = _8_BIT_OUT[6]; D7 = _8_BIT_OUT[7];
  //   D8 = _10_BIT_OUT[8]; D9 = _10_BIT_OUT[9]; D10 = _16_BIT_OUT[10]; D11 = _16_BIT_OUT[11]; D12 = _16_BIT_OUT[12];
  //   D13 = _16_BIT_OUT[13]; D14 = _16_BIT_OUT[14]; D15 = _16_BIT_OUT[15]; A0 = ABUS[0]; A1 = ABUS[1]; A2 = ABUS[2];
  //   A3 = ABUS[3]; A4 = ABUS[4]; A5 = ABUS[5]; A6 = ABUS[6]; A7 = ABUS[7]; A8 = ABUS[8]; A9 = ABUS[9]; IN0 = INPR[0];
  //   IN1 = INPR[1]; IN2 = INPR[2]; IN3 = INPR[3]; IN4 = INPR[4]; IN5 = INPR[5]; IN6 = INPR[6]; IN7 = INPR[7];
  //   M0 = MEMORY[0]; M1 = MEMORY[1]; M2 = MEMORY[2]; M3 = MEMORY[3]; M4 = MEMORY[4]; M5 = MEMORY[5]; M6 = MEMORY[6];
  //   M7 = MEMORY[7]; M8 = MEMORY[8]; M9 = MEMORY[9]; M10 = MEMORY[10]; M11 = MEMORY[11]; M12 = MEMORY[12];
  //   M13 = MEMORY[13]; M14 = MEMORY[14]; M15 = MEMORY[15]
endmodule

module _5_Bit_Register (
  input  [4:0] INPUT,
  input  L,
  input  I,
  input  C,
  output CARRY_OUT,
  output [4:0] OUTPUT
);

  wire and_2_out, and_3_out, and_4_out, and_5_out, and_6_out, and_7_out, and_8_out, and_9_out, and_10_out,
       and_11_out, and_12_out, and_13_out, and_14_out, and_15_out, and_16_out, and_17_out, CLOCK_out,
       not_1_out, not_2_out, not_3_out, not_4_out, not_5_out, not_6_out, not_7_out, or_1_out, or_2_out,
       or_3_out, or_4_out, or_5_out, or_6_out, or_7_out, or_8_out, or_9_out, or_10_out;

  not not_1 (not_1_out, INPUT[4]);
  not not_2 (not_2_out, INPUT[3]);
  not not_3 (not_3_out, INPUT[2]);
  not not_4 (not_4_out, INPUT[1]);
  not not_5 (not_5_out, INPUT[0]);
  not not_6 (not_6_out, L);
  not not_7 (not_7_out, I);
  and and_1 (CARRY_OUT, and_4_out, OUTPUT[4]);
  and and_2 (and_2_out, L, not_1_out);
  and and_3 (and_3_out, INPUT[4], L);
  and and_4 (and_4_out, and_7_out, OUTPUT[3]);
  and and_5 (and_5_out, L, not_2_out);
  and and_6 (and_6_out, INPUT[3], L);
  and and_7 (and_7_out, and_10_out, OUTPUT[2]);
  and and_8 (and_8_out, L, not_3_out);
  and and_9 (and_9_out, INPUT[2], L);
  and and_10 (and_10_out, and_13_out, OUTPUT[1]);
  and and_11 (and_11_out, L, not_4_out);
  and and_12 (and_12_out, INPUT[1], L);
  and and_13 (and_13_out, and_17_out, OUTPUT[0]);
  and and_14 (and_14_out, L, not_5_out);
  and and_15 (and_15_out, INPUT[0], L);
  and and_16 (and_16_out, not_6_out, not_7_out, C);
  and and_17 (and_17_out, not_6_out, I);
  or or_1 (or_1_out, and_4_out, and_16_out, and_2_out);
  or or_2 (or_2_out, and_4_out, and_3_out);
  or or_3 (or_3_out, and_7_out, and_16_out, and_5_out);
  or or_4 (or_4_out, and_7_out, and_6_out);
  or or_5 (or_5_out, and_10_out, and_16_out, and_8_out);
  or or_6 (or_6_out, and_10_out, and_9_out);
  or or_7 (or_7_out, and_13_out, and_16_out, and_11_out);
  or or_8 (or_8_out, and_13_out, and_12_out);
  or or_9 (or_9_out, and_17_out, and_16_out, and_14_out);
  or or_10 (or_10_out, and_17_out, and_15_out);
  Clock CLOCK (.out(CLOCK_out));
  J_K_Flip_Flop j_k_ff_1 (.J(or_2_out), .clk(CLOCK_out), .K(or_1_out), .Q(OUTPUT[4]));  // open: Qn, preset, en, reset
  J_K_Flip_Flop j_k_ff_2 (.J(or_4_out), .clk(CLOCK_out), .K(or_3_out), .Q(OUTPUT[3]));  // open: Qn, preset, en, reset
  J_K_Flip_Flop j_k_ff_3 (.J(or_6_out), .clk(CLOCK_out), .K(or_5_out), .Q(OUTPUT[2]));  // open: Qn, preset, en, reset
  J_K_Flip_Flop j_k_ff_4 (.J(or_8_out), .clk(CLOCK_out), .K(or_7_out), .Q(OUTPUT[1]));  // open: Qn, preset, en, reset
  J_K_Flip_Flop j_k_ff_5 (.J(or_10_out), .clk(CLOCK_out), .K(or_9_out), .Q(OUTPUT[0]));  // open: Qn, preset, en, reset
endmodule

module _10_Bit_Register (
  input  [9:0] INPUT,
  input  L,
  input  I,
  input  C,
  output CARRY_OUT,
  output [9:0] OUTPUT
);

  wire and_2_out, and_3_out, and_4_out, and_5_out, and_6_out, and_7_out, and_8_out, and_9_out, and_10_out,
       and_11_out, and_12_out, and_13_out, and_14_out, and_15_out, and_16_out, and_17_out, and_18_out,
       and_19_out, and_20_out, and_21_out, and_22_out, and_23_out, and_24_out, and_25_out, and_26_out,
       and_27_out, and_28_out, and_29_out, and_30_out, and_31_out, and_32_out, CLOCK_out, not_1_out,
       not_2_out, not_3_out, not_4_out, not_5_out, not_6_out, not_7_out, not_8_out, not_9_out, not_10_out,
       not_11_out, not_12_out, or_1_out, or_2_out, or_3_out, or_4_out, or_5_out, or_6_out, or_7_out,
       or_8_out, or_9_out, or_10_out, or_11_out, or_12_out, or_13_out, or_14_out, or_15_out, or_16_out,
       or_17_out, or_18_out, or_19_out, or_20_out;

  not not_1 (not_1_out, INPUT[9]);
  not not_2 (not_2_out, INPUT[8]);
  not not_3 (not_3_out, INPUT[7]);
  not not_4 (not_4_out, INPUT[6]);
  not not_5 (not_5_out, INPUT[5]);
  not not_6 (not_6_out, INPUT[4]);
  not not_7 (not_7_out, INPUT[3]);
  not not_8 (not_8_out, INPUT[2]);
  not not_9 (not_9_out, INPUT[1]);
  not not_10 (not_10_out, INPUT[0]);
  not not_11 (not_11_out, I);
  not not_12 (not_12_out, L);
  and and_1 (CARRY_OUT, and_4_out, OUTPUT[9]);
  and and_2 (and_2_out, L, not_1_out);
  and and_3 (and_3_out, INPUT[9], L);
  and and_4 (and_4_out, and_7_out, OUTPUT[8]);
  and and_5 (and_5_out, L, not_2_out);
  and and_6 (and_6_out, INPUT[8], L);
  and and_7 (and_7_out, and_10_out, OUTPUT[7]);
  and and_8 (and_8_out, L, not_3_out);
  and and_9 (and_9_out, INPUT[7], L);
  and and_10 (and_10_out, and_13_out, OUTPUT[6]);
  and and_11 (and_11_out, L, not_4_out);
  and and_12 (and_12_out, INPUT[6], L);
  and and_13 (and_13_out, and_16_out, OUTPUT[5]);
  and and_14 (and_14_out, L, not_5_out);
  and and_15 (and_15_out, INPUT[5], L);
  and and_16 (and_16_out, and_19_out, OUTPUT[4]);
  and and_17 (and_17_out, L, not_6_out);
  and and_18 (and_18_out, INPUT[4], L);
  and and_19 (and_19_out, and_22_out, OUTPUT[3]);
  and and_20 (and_20_out, L, not_7_out);
  and and_21 (and_21_out, INPUT[3], L);
  and and_22 (and_22_out, and_25_out, OUTPUT[2]);
  and and_23 (and_23_out, L, not_8_out);
  and and_24 (and_24_out, INPUT[2], L);
  and and_25 (and_25_out, and_28_out, OUTPUT[1]);
  and and_26 (and_26_out, L, not_9_out);
  and and_27 (and_27_out, INPUT[1], L);
  and and_28 (and_28_out, and_31_out, OUTPUT[0]);
  and and_29 (and_29_out, L, not_10_out);
  and and_30 (and_30_out, INPUT[0], L);
  and and_31 (and_31_out, not_12_out, I);
  or or_1 (or_1_out, and_4_out, and_32_out, and_2_out);
  or or_2 (or_2_out, and_4_out, and_3_out);
  or or_3 (or_3_out, and_7_out, and_32_out, and_5_out);
  or or_4 (or_4_out, and_7_out, and_6_out);
  or or_5 (or_5_out, and_10_out, and_32_out, and_8_out);
  or or_6 (or_6_out, and_10_out, and_9_out);
  or or_7 (or_7_out, and_13_out, and_32_out, and_11_out);
  or or_8 (or_8_out, and_13_out, and_12_out);
  or or_9 (or_9_out, and_16_out, and_32_out, and_14_out);
  or or_10 (or_10_out, and_16_out, and_15_out);
  or or_11 (or_11_out, and_19_out, and_32_out, and_17_out);
  or or_12 (or_12_out, and_19_out, and_18_out);
  or or_13 (or_13_out, and_22_out, and_32_out, and_20_out);
  or or_14 (or_14_out, and_22_out, and_21_out);
  or or_15 (or_15_out, and_25_out, and_32_out, and_23_out);
  or or_16 (or_16_out, and_25_out, and_24_out);
  or or_17 (or_17_out, and_28_out, and_32_out, and_26_out);
  or or_18 (or_18_out, and_28_out, and_27_out);
  or or_19 (or_19_out, and_31_out, and_32_out, and_29_out);
  or or_20 (or_20_out, and_31_out, and_30_out);
  and and_32 (and_32_out, not_12_out, not_11_out, C);
  J_K_Flip_Flop j_k_ff_1 (.J(or_2_out), .clk(CLOCK_out), .K(or_1_out), .Q(OUTPUT[9]));  // open: Qn, preset, en, reset
  J_K_Flip_Flop j_k_ff_2 (.J(or_4_out), .clk(CLOCK_out), .K(or_3_out), .Q(OUTPUT[8]));  // open: Qn, preset, en, reset
  J_K_Flip_Flop j_k_ff_3 (.J(or_6_out), .clk(CLOCK_out), .K(or_5_out), .Q(OUTPUT[7]));  // open: Qn, preset, en, reset
  J_K_Flip_Flop j_k_ff_4 (.J(or_8_out), .clk(CLOCK_out), .K(or_7_out), .Q(OUTPUT[6]));  // open: Qn, preset, en, reset
  J_K_Flip_Flop j_k_ff_5 (.J(or_10_out), .clk(CLOCK_out), .K(or_9_out), .Q(OUTPUT[5]));  // open: Qn, preset, en, reset
  J_K_Flip_Flop j_k_ff_6 (.J(or_12_out), .clk(CLOCK_out), .K(or_11_out), .Q(OUTPUT[4]));  // open: Qn, preset, en, reset
  J_K_Flip_Flop j_k_ff_7 (.J(or_14_out), .clk(CLOCK_out), .K(or_13_out), .Q(OUTPUT[3]));  // open: Qn, preset, en, reset
  J_K_Flip_Flop j_k_ff_8 (.J(or_16_out), .clk(CLOCK_out), .K(or_15_out), .Q(OUTPUT[2]));  // open: Qn, preset, en, reset
  J_K_Flip_Flop j_k_ff_9 (.J(or_18_out), .clk(CLOCK_out), .K(or_17_out), .Q(OUTPUT[1]));  // open: Qn, preset, en, reset
  J_K_Flip_Flop j_k_ff_10 (
    .J(or_20_out), .clk(CLOCK_out), .K(or_19_out), .Q(OUTPUT[0]));  // open: Qn, preset, en, reset
  Clock CLOCK (.out(CLOCK_out));
endmodule

module _16_Bit_Register (
  input  [15:0] INPUT,
  input  L,
  input  I,
  input  C,
  output CARRY_OUT,
  output [15:0] OUTPUT
);

  wire and_2_out, and_3_out, and_4_out, and_5_out, and_6_out, and_7_out, and_8_out, and_9_out, and_10_out,
       and_11_out, and_12_out, and_13_out, and_14_out, and_15_out, and_16_out, and_17_out, and_18_out,
       and_19_out, and_20_out, and_21_out, and_22_out, and_23_out, and_24_out, and_25_out, and_26_out,
       and_27_out, and_28_out, and_29_out, and_30_out, and_31_out, and_32_out, and_33_out, and_34_out,
       and_35_out, and_36_out, and_37_out, and_38_out, and_39_out, and_40_out, and_41_out, and_42_out,
       and_43_out, and_44_out, and_45_out, and_46_out, and_47_out, and_48_out, and_49_out, and_50_out,
       CLOCK_out, not_1_out, not_2_out, not_3_out, not_4_out, not_5_out, not_6_out, not_7_out, not_8_out,
       not_9_out, not_10_out, not_11_out, not_12_out, not_13_out, not_14_out, not_15_out, not_16_out,
       not_17_out, not_18_out, or_1_out, or_2_out, or_3_out, or_4_out, or_5_out, or_6_out, or_7_out,
       or_8_out, or_9_out, or_10_out, or_11_out, or_12_out, or_13_out, or_14_out, or_15_out, or_16_out,
       or_17_out, or_18_out, or_19_out, or_20_out, or_21_out, or_22_out, or_23_out, or_24_out, or_25_out,
       or_26_out, or_27_out, or_28_out, or_29_out, or_30_out, or_31_out, or_32_out;

  not not_1 (not_1_out, INPUT[15]);
  not not_2 (not_2_out, INPUT[14]);
  not not_3 (not_3_out, INPUT[13]);
  not not_4 (not_4_out, INPUT[12]);
  not not_5 (not_5_out, INPUT[11]);
  not not_6 (not_6_out, INPUT[10]);
  not not_7 (not_7_out, INPUT[9]);
  not not_8 (not_8_out, INPUT[8]);
  not not_9 (not_9_out, INPUT[7]);
  not not_10 (not_10_out, INPUT[6]);
  not not_11 (not_11_out, INPUT[5]);
  not not_12 (not_12_out, INPUT[4]);
  not not_13 (not_13_out, INPUT[3]);
  not not_14 (not_14_out, INPUT[2]);
  not not_15 (not_15_out, INPUT[1]);
  not not_16 (not_16_out, INPUT[0]);
  not not_17 (not_17_out, L);
  and and_1 (CARRY_OUT, and_4_out, OUTPUT[15]);
  and and_2 (and_2_out, L, not_1_out);
  and and_3 (and_3_out, INPUT[15], L);
  and and_4 (and_4_out, and_7_out, OUTPUT[14]);
  and and_5 (and_5_out, L, not_2_out);
  and and_6 (and_6_out, INPUT[14], L);
  and and_7 (and_7_out, and_10_out, OUTPUT[13]);
  and and_8 (and_8_out, L, not_3_out);
  and and_9 (and_9_out, INPUT[13], L);
  and and_10 (and_10_out, and_13_out, OUTPUT[12]);
  and and_11 (and_11_out, L, not_4_out);
  and and_12 (and_12_out, INPUT[12], L);
  and and_13 (and_13_out, and_16_out, OUTPUT[11]);
  and and_14 (and_14_out, L, not_5_out);
  and and_15 (and_15_out, INPUT[11], L);
  and and_16 (and_16_out, and_19_out, OUTPUT[10]);
  and and_17 (and_17_out, L, not_6_out);
  and and_18 (and_18_out, INPUT[10], L);
  and and_19 (and_19_out, and_22_out, OUTPUT[9]);
  and and_20 (and_20_out, L, not_7_out);
  and and_21 (and_21_out, INPUT[9], L);
  and and_22 (and_22_out, and_25_out, OUTPUT[8]);
  and and_23 (and_23_out, L, not_8_out);
  and and_24 (and_24_out, INPUT[8], L);
  and and_25 (and_25_out, and_28_out, OUTPUT[7]);
  and and_26 (and_26_out, L, not_9_out);
  and and_27 (and_27_out, INPUT[7], L);
  and and_28 (and_28_out, and_31_out, OUTPUT[6]);
  and and_29 (and_29_out, L, not_10_out);
  and and_30 (and_30_out, INPUT[6], L);
  and and_31 (and_31_out, and_34_out, OUTPUT[5]);
  and and_32 (and_32_out, L, not_11_out);
  and and_33 (and_33_out, INPUT[5], L);
  and and_34 (and_34_out, and_37_out, OUTPUT[4]);
  and and_35 (and_35_out, L, not_12_out);
  and and_36 (and_36_out, INPUT[4], L);
  and and_37 (and_37_out, and_40_out, OUTPUT[3]);
  and and_38 (and_38_out, L, not_13_out);
  and and_39 (and_39_out, INPUT[3], L);
  and and_40 (and_40_out, and_43_out, OUTPUT[2]);
  and and_41 (and_41_out, L, not_14_out);
  and and_42 (and_42_out, INPUT[2], L);
  and and_43 (and_43_out, and_46_out, OUTPUT[1]);
  and and_44 (and_44_out, L, not_15_out);
  and and_45 (and_45_out, INPUT[1], L);
  and and_46 (and_46_out, and_50_out, OUTPUT[0]);
  and and_47 (and_47_out, L, not_16_out);
  and and_48 (and_48_out, INPUT[0], L);
  not not_18 (not_18_out, I);
  or or_1 (or_1_out, and_4_out, and_49_out, and_2_out);
  or or_2 (or_2_out, and_4_out, and_3_out);
  or or_3 (or_3_out, and_7_out, and_49_out, and_5_out);
  or or_4 (or_4_out, and_7_out, and_6_out);
  or or_5 (or_5_out, and_10_out, and_49_out, and_8_out);
  or or_6 (or_6_out, and_10_out, and_9_out);
  or or_7 (or_7_out, and_13_out, and_49_out, and_11_out);
  or or_8 (or_8_out, and_13_out, and_12_out);
  or or_9 (or_9_out, and_16_out, and_49_out, and_14_out);
  or or_10 (or_10_out, and_16_out, and_15_out);
  or or_11 (or_11_out, and_19_out, and_49_out, and_17_out);
  or or_12 (or_12_out, and_19_out, and_18_out);
  or or_13 (or_13_out, and_22_out, and_49_out, and_20_out);
  or or_14 (or_14_out, and_22_out, and_21_out);
  or or_15 (or_15_out, and_25_out, and_49_out, and_23_out);
  or or_16 (or_16_out, and_25_out, and_24_out);
  or or_17 (or_17_out, and_28_out, and_49_out, and_26_out);
  or or_18 (or_18_out, and_28_out, and_27_out);
  or or_19 (or_19_out, and_31_out, and_49_out, and_29_out);
  or or_20 (or_20_out, and_31_out, and_30_out);
  or or_21 (or_21_out, and_34_out, and_49_out, and_32_out);
  or or_22 (or_22_out, and_34_out, and_33_out);
  or or_23 (or_23_out, and_37_out, and_49_out, and_35_out);
  or or_24 (or_24_out, and_37_out, and_36_out);
  or or_25 (or_25_out, and_40_out, and_49_out, and_38_out);
  or or_26 (or_26_out, and_40_out, and_39_out);
  or or_27 (or_27_out, and_43_out, and_49_out, and_41_out);
  or or_28 (or_28_out, and_43_out, and_42_out);
  or or_29 (or_29_out, and_46_out, and_49_out, and_44_out);
  or or_30 (or_30_out, and_46_out, and_45_out);
  or or_31 (or_31_out, and_50_out, and_49_out, and_47_out);
  or or_32 (or_32_out, and_50_out, and_48_out);
  and and_49 (and_49_out, not_17_out, not_18_out, C);
  and and_50 (and_50_out, not_17_out, I);
  J_K_Flip_Flop j_k_ff_1 (.J(or_2_out), .clk(CLOCK_out), .K(or_1_out), .Q(OUTPUT[15]));  // open: Qn, preset, en, reset
  J_K_Flip_Flop j_k_ff_2 (.J(or_4_out), .clk(CLOCK_out), .K(or_3_out), .Q(OUTPUT[14]));  // open: Qn, preset, en, reset
  J_K_Flip_Flop j_k_ff_3 (.J(or_6_out), .clk(CLOCK_out), .K(or_5_out), .Q(OUTPUT[13]));  // open: Qn, preset, en, reset
  J_K_Flip_Flop j_k_ff_4 (.J(or_8_out), .clk(CLOCK_out), .K(or_7_out), .Q(OUTPUT[12]));  // open: Qn, preset, en, reset
  J_K_Flip_Flop j_k_ff_5 (.J(or_10_out), .clk(CLOCK_out), .K(or_9_out), .Q(OUTPUT[11]));  // open: Qn, preset, en, reset
  J_K_Flip_Flop j_k_ff_6 (
    .J(or_12_out), .clk(CLOCK_out), .K(or_11_out), .Q(OUTPUT[10]));  // open: Qn, preset, en, reset
  J_K_Flip_Flop j_k_ff_7 (.J(or_14_out), .clk(CLOCK_out), .K(or_13_out), .Q(OUTPUT[9]));  // open: Qn, preset, en, reset
  J_K_Flip_Flop j_k_ff_8 (.J(or_16_out), .clk(CLOCK_out), .K(or_15_out), .Q(OUTPUT[8]));  // open: Qn, preset, en, reset
  J_K_Flip_Flop j_k_ff_9 (.J(or_18_out), .clk(CLOCK_out), .K(or_17_out), .Q(OUTPUT[7]));  // open: Qn, preset, en, reset
  J_K_Flip_Flop j_k_ff_10 (
    .J(or_20_out), .clk(CLOCK_out), .K(or_19_out), .Q(OUTPUT[6]));  // open: Qn, preset, en, reset
  J_K_Flip_Flop j_k_ff_11 (
    .J(or_22_out), .clk(CLOCK_out), .K(or_21_out), .Q(OUTPUT[5]));  // open: Qn, preset, en, reset
  J_K_Flip_Flop j_k_ff_12 (
    .J(or_24_out), .clk(CLOCK_out), .K(or_23_out), .Q(OUTPUT[4]));  // open: Qn, preset, en, reset
  J_K_Flip_Flop j_k_ff_13 (
    .J(or_26_out), .clk(CLOCK_out), .K(or_25_out), .Q(OUTPUT[3]));  // open: Qn, preset, en, reset
  J_K_Flip_Flop j_k_ff_14 (
    .J(or_28_out), .clk(CLOCK_out), .K(or_27_out), .Q(OUTPUT[2]));  // open: Qn, preset, en, reset
  J_K_Flip_Flop j_k_ff_15 (
    .J(or_30_out), .clk(CLOCK_out), .K(or_29_out), .Q(OUTPUT[1]));  // open: Qn, preset, en, reset
  J_K_Flip_Flop j_k_ff_16 (
    .J(or_32_out), .clk(CLOCK_out), .K(or_31_out), .Q(OUTPUT[0]));  // open: Qn, preset, en, reset
  Clock CLOCK (.out(CLOCK_out));
endmodule

module ALUBus (
  input  S,
  input  [15:0] A,
  input  [15:0] B,
  output [15:0] OUTPUT
);

  wire decoder_1_out0, decoder_1_out1, decoder_2_out0, decoder_2_out1, decoder_3_out0, decoder_3_out1,
       decoder_4_out0, decoder_4_out1, decoder_5_out0, decoder_5_out1, decoder_6_out0, decoder_6_out1,
       decoder_7_out0, decoder_7_out1, decoder_8_out0, decoder_8_out1, decoder_9_out0, decoder_9_out1,
       decoder_10_out0, decoder_10_out1, decoder_11_out0, decoder_11_out1, decoder_12_out0, decoder_12_out1,
       decoder_13_out0, decoder_13_out1, decoder_14_out0, decoder_14_out1, decoder_15_out0, decoder_15_out1,
       decoder_16_out0, decoder_16_out1;

  assign OUTPUT[15] = decoder_1_out1 ? B[15] : 1'bz;  // Controlled_Buffer controlled_buffer_1
  assign OUTPUT[15] = decoder_1_out0 ? A[15] : 1'bz;  // Controlled_Buffer controlled_buffer_2
  Decoder #(.enable("false")) decoder_1 (.out0(decoder_1_out0), .out1(decoder_1_out1), .sel(S));
  assign OUTPUT[14] = decoder_2_out0 ? A[14] : 1'bz;  // Controlled_Buffer controlled_buffer_3
  Decoder #(.enable("false")) decoder_2 (.out0(decoder_2_out0), .out1(decoder_2_out1), .sel(S));
  assign OUTPUT[14] = decoder_2_out1 ? B[14] : 1'bz;  // Controlled_Buffer controlled_buffer_4
  assign OUTPUT[13] = decoder_3_out1 ? B[13] : 1'bz;  // Controlled_Buffer controlled_buffer_5
  assign OUTPUT[13] = decoder_3_out0 ? A[13] : 1'bz;  // Controlled_Buffer controlled_buffer_6
  Decoder #(.enable("false")) decoder_3 (.out0(decoder_3_out0), .out1(decoder_3_out1), .sel(S));
  Decoder #(.enable("false")) decoder_4 (.out0(decoder_4_out0), .out1(decoder_4_out1), .sel(S));
  assign OUTPUT[12] = decoder_4_out1 ? B[12] : 1'bz;  // Controlled_Buffer controlled_buffer_7
  assign OUTPUT[12] = decoder_4_out0 ? A[12] : 1'bz;  // Controlled_Buffer controlled_buffer_8
  assign OUTPUT[11] = decoder_5_out0 ? A[11] : 1'bz;  // Controlled_Buffer controlled_buffer_9
  Decoder #(.enable("false")) decoder_5 (.out0(decoder_5_out0), .out1(decoder_5_out1), .sel(S));
  assign OUTPUT[11] = decoder_5_out1 ? B[11] : 1'bz;  // Controlled_Buffer controlled_buffer_10
  assign OUTPUT[10] = decoder_6_out1 ? B[10] : 1'bz;  // Controlled_Buffer controlled_buffer_11
  assign OUTPUT[10] = decoder_6_out0 ? A[10] : 1'bz;  // Controlled_Buffer controlled_buffer_12
  Decoder #(.enable("false")) decoder_6 (.out0(decoder_6_out0), .out1(decoder_6_out1), .sel(S));
  Decoder #(.enable("false")) decoder_7 (.out0(decoder_7_out0), .out1(decoder_7_out1), .sel(S));
  assign OUTPUT[9] = decoder_7_out1 ? B[9] : 1'bz;  // Controlled_Buffer controlled_buffer_13
  assign OUTPUT[9] = decoder_7_out0 ? A[9] : 1'bz;  // Controlled_Buffer controlled_buffer_14
  assign OUTPUT[8] = decoder_8_out0 ? A[8] : 1'bz;  // Controlled_Buffer controlled_buffer_15
  Decoder #(.enable("false")) decoder_8 (.out0(decoder_8_out0), .out1(decoder_8_out1), .sel(S));
  assign OUTPUT[8] = decoder_8_out1 ? B[8] : 1'bz;  // Controlled_Buffer controlled_buffer_16
  assign OUTPUT[7] = decoder_9_out1 ? B[7] : 1'bz;  // Controlled_Buffer controlled_buffer_17
  assign OUTPUT[7] = decoder_9_out0 ? A[7] : 1'bz;  // Controlled_Buffer controlled_buffer_18
  Decoder #(.enable("false")) decoder_9 (.out0(decoder_9_out0), .out1(decoder_9_out1), .sel(S));
  assign OUTPUT[6] = decoder_10_out0 ? A[6] : 1'bz;  // Controlled_Buffer controlled_buffer_19
  Decoder #(.enable("false")) decoder_10 (.out0(decoder_10_out0), .out1(decoder_10_out1), .sel(S));
  assign OUTPUT[6] = decoder_10_out1 ? B[6] : 1'bz;  // Controlled_Buffer controlled_buffer_20
  assign OUTPUT[5] = decoder_11_out0 ? A[5] : 1'bz;  // Controlled_Buffer controlled_buffer_21
  Decoder #(.enable("false")) decoder_11 (.out0(decoder_11_out0), .out1(decoder_11_out1), .sel(S));
  assign OUTPUT[5] = decoder_11_out1 ? B[5] : 1'bz;  // Controlled_Buffer controlled_buffer_22
  assign OUTPUT[4] = decoder_12_out1 ? B[4] : 1'bz;  // Controlled_Buffer controlled_buffer_23
  assign OUTPUT[4] = decoder_12_out0 ? A[4] : 1'bz;  // Controlled_Buffer controlled_buffer_24
  Decoder #(.enable("false")) decoder_12 (.out0(decoder_12_out0), .out1(decoder_12_out1), .sel(S));
  assign OUTPUT[3] = decoder_13_out0 ? A[3] : 1'bz;  // Controlled_Buffer controlled_buffer_25
  Decoder #(.enable("false")) decoder_13 (.out0(decoder_13_out0), .out1(decoder_13_out1), .sel(S));
  assign OUTPUT[3] = decoder_13_out1 ? B[3] : 1'bz;  // Controlled_Buffer controlled_buffer_26
  assign OUTPUT[2] = decoder_14_out0 ? A[2] : 1'bz;  // Controlled_Buffer controlled_buffer_27
  Decoder #(.enable("false")) decoder_14 (.out0(decoder_14_out0), .out1(decoder_14_out1), .sel(S));
  assign OUTPUT[2] = decoder_14_out1 ? B[2] : 1'bz;  // Controlled_Buffer controlled_buffer_28
  assign OUTPUT[1] = decoder_15_out1 ? B[1] : 1'bz;  // Controlled_Buffer controlled_buffer_29
  assign OUTPUT[1] = decoder_15_out0 ? A[1] : 1'bz;  // Controlled_Buffer controlled_buffer_30
  Decoder #(.enable("false")) decoder_15 (.out0(decoder_15_out0), .out1(decoder_15_out1), .sel(S));
  assign OUTPUT[0] = decoder_16_out0 ? A[0] : 1'bz;  // Controlled_Buffer controlled_buffer_31
  Decoder #(.enable("false")) decoder_16 (.out0(decoder_16_out0), .out1(decoder_16_out1), .sel(S));
  assign OUTPUT[0] = decoder_16_out1 ? B[0] : 1'bz;  // Controlled_Buffer controlled_buffer_32

  // Other names for the same wires on the sheet: O0 = OUTPUT[0]; O1 = OUTPUT[1]; O2 = OUTPUT[2]; O3 = OUTPUT[3];
  //   O4 = OUTPUT[4]; O5 = OUTPUT[5]; O6 = OUTPUT[6]; O7 = OUTPUT[7]; O8 = OUTPUT[8]; O9 = OUTPUT[9];
  //   O10 = OUTPUT[10]; O11 = OUTPUT[11]; O12 = OUTPUT[12]; O13 = OUTPUT[13]; O14 = OUTPUT[14]; O15 = OUTPUT[15]
endmodule

module LogicUnit1Bit (
  input  A,
  input  B,
  input  S1,
  input  S0,
  input  CARRY_IN,
  output OUTPUT,
  output CARRY_OUT
);

  wire and_1_out, not_1_out, not_2_out, not_3_out, not_4_out, or_1_out, xor_1_out;

  not not_1 (not_1_out, A);
  and and_1 (and_1_out, B, A);
  not not_2 (not_2_out, and_1_out);
  not not_3 (not_3_out, or_1_out);
  or or_1 (or_1_out, A, B);
  not not_4 (not_4_out, xor_1_out);
  xor xor_1 (xor_1_out, A, B);
  Multiplexer #(.select(3), .enable("false")) multiplexer_1 (
    .in0(and_1_out), .in1(not_2_out), .in2(not_3_out), .in3(not_4_out), .in4(or_1_out), .in5(xor_1_out),
    .in6(not_1_out), .in7(not_1_out), .out(OUTPUT), .sel({S1, S0, CARRY_IN}));

  assign CARRY_OUT = CARRY_IN;
endmodule

module ArithmeticUnit1Bit (
  input  CARRY_IN,
  input  A,
  input  B,
  input  S1,
  input  S0,
  output DATA_OUT,
  output CARRY_OUT
);

  wire multiplexer_1_out, not_1_out;

  not not_1 (not_1_out, B);
  Multiplexer #(.select(2), .enable("false")) multiplexer_1 (
    .in0(1'b0), .in1(B), .in2(not_1_out), .in3(1'b1), .out(multiplexer_1_out), .sel({S1, S0}));
  Adder #(.width(1)) adder_1 (.a(A), .b(multiplexer_1_out), .out(DATA_OUT), .cin(CARRY_IN), .cout(CARRY_OUT));
endmodule

module ALU16Bit (
  input  [3:0] S0,
  input  [7:0] Input_from_Register,
  input  [15:0] A,
  input  [15:0] B,
  output [7:0] Output_to_Register,
  output [15:0] Output
);

  wire alu1bit_1_carry_out, alu1bit_2_carry_out, alu1bit_3_carry_out, alu1bit_4_carry_out,
       alu1bit_5_carry_out, alu1bit_6_carry_out, alu1bit_7_carry_out, alu1bit_8_carry_out,
       alu1bit_9_carry_out, alu1bit_10_carry_out, alu1bit_11_carry_out, alu1bit_12_carry_out,
       alu1bit_13_carry_out, alu1bit_14_carry_out, alu1bit_15_carry_out, and_1_out, and_2_out, and_3_out,
       and_4_out, and_5_out, and_6_out, multiplexer_4_out, multiplexer_6_out, nand_1_out, not_1_out,
       not_2_out, not_3_out, Oo1, Oo2, or_1_out, or_2_out, R___L, xnor_1_out, xor_1_out, xor_2_out,
       xor_3_out, xor_4_out;

  Multiplexer #(.select(3), .enable("false")) multiplexer_1 (
    .in0(1'b0), .in1(A[15]), .in2(A[0]), .in3(1'b0), .in4(1'b0), .in5(A[15]), .in6(1'b0), .out(R___L),
    .sel({S0[1:0], Input_from_Register[0]}));  // open: in7
  and and_1 (and_1_out, and_2_out, nand_1_out);
  xor xor_1 (xor_1_out, A[14], A[15]);
  Multiplexer #(.enable("false")) multiplexer_2 (
    .in0(Input_from_Register[1]), .in1(xor_1_out), .out(Oo2), .sel(and_1_out));
  Multiplexer #(.enable("false")) multiplexer_3 (.in0(Oo2), .in1(Oo1), .out(Output_to_Register[1]), .sel(S0[3]));
  and and_2 (and_2_out, not_1_out, S0[1]);
  nand nand_1 (nand_1_out, S0[3], S0[2]);
  not not_1 (not_1_out, Input_from_Register[0]);
  Multiplexer #(.select(3), .enable("false")) multiplexer_4 (
    .in0(1'b1), .in1(1'b1), .in2(1'b1), .in3(1'b0), .in4(1'b0), .in5(1'b0), .in6(1'b0),
    .out(multiplexer_4_out), .sel({S0[1:0], Input_from_Register[0]}));  // open: in7
  ALU1Bit alu1bit_1 (
    .IR(R___L), .IL(A[1]), .A(A[0]), .B(B[0]), .DATA_OUT(Output[0]), .CARRY_IN(Input_from_Register[0]),
    .S3(S0[3]), .S2(S0[2]), .SELECT(multiplexer_4_out), .S1(S0[1]), .S0(S0[0]),
    .CARRY_OUT(alu1bit_1_carry_out));
  ALU1Bit alu1bit_2 (
    .IR(A[0]), .IL(A[2]), .A(A[1]), .B(B[1]), .DATA_OUT(Output[1]), .CARRY_IN(alu1bit_1_carry_out),
    .S3(S0[3]), .S2(S0[2]), .SELECT(multiplexer_4_out), .S1(S0[1]), .S0(S0[0]),
    .CARRY_OUT(alu1bit_2_carry_out));
  ALU1Bit alu1bit_3 (
    .IR(A[1]), .IL(A[3]), .A(A[2]), .B(B[2]), .DATA_OUT(Output[2]), .CARRY_IN(alu1bit_2_carry_out),
    .S3(S0[3]), .S2(S0[2]), .SELECT(multiplexer_4_out), .S1(S0[1]), .S0(S0[0]),
    .CARRY_OUT(alu1bit_3_carry_out));
  ALU1Bit alu1bit_4 (
    .IR(A[2]), .IL(A[4]), .A(A[3]), .B(B[3]), .DATA_OUT(Output[3]), .CARRY_IN(alu1bit_3_carry_out),
    .S3(S0[3]), .S2(S0[2]), .SELECT(multiplexer_4_out), .S1(S0[1]), .S0(S0[0]),
    .CARRY_OUT(alu1bit_4_carry_out));
  ALU1Bit alu1bit_5 (
    .IR(A[3]), .IL(A[5]), .A(A[4]), .B(B[4]), .DATA_OUT(Output[4]), .CARRY_IN(alu1bit_4_carry_out),
    .S3(S0[3]), .S2(S0[2]), .SELECT(multiplexer_4_out), .S1(S0[1]), .S0(S0[0]),
    .CARRY_OUT(alu1bit_5_carry_out));
  ALU1Bit alu1bit_6 (
    .IR(A[4]), .IL(A[6]), .A(A[5]), .B(B[5]), .DATA_OUT(Output[5]), .CARRY_IN(alu1bit_5_carry_out),
    .S3(S0[3]), .S2(S0[2]), .SELECT(multiplexer_4_out), .S1(S0[1]), .S0(S0[0]),
    .CARRY_OUT(alu1bit_6_carry_out));
  ALU1Bit alu1bit_7 (
    .IR(A[5]), .IL(A[7]), .A(A[6]), .B(B[6]), .DATA_OUT(Output[6]), .CARRY_IN(alu1bit_6_carry_out),
    .S3(S0[3]), .S2(S0[2]), .SELECT(multiplexer_4_out), .S1(S0[1]), .S0(S0[0]),
    .CARRY_OUT(alu1bit_7_carry_out));
  ALU1Bit alu1bit_8 (
    .IR(A[6]), .IL(A[8]), .A(A[7]), .B(B[7]), .DATA_OUT(Output[7]), .CARRY_IN(alu1bit_7_carry_out),
    .S3(S0[3]), .S2(S0[2]), .SELECT(multiplexer_4_out), .S1(S0[1]), .S0(S0[0]),
    .CARRY_OUT(alu1bit_8_carry_out));
  ALU1Bit alu1bit_9 (
    .IR(A[7]), .IL(A[9]), .A(A[8]), .B(B[8]), .DATA_OUT(Output[8]), .CARRY_IN(alu1bit_8_carry_out),
    .S3(S0[3]), .S2(S0[2]), .SELECT(multiplexer_4_out), .S1(S0[1]), .S0(S0[0]),
    .CARRY_OUT(alu1bit_9_carry_out));
  ALU1Bit alu1bit_10 (
    .IR(A[8]), .IL(A[10]), .A(A[9]), .B(B[9]), .DATA_OUT(Output[9]), .CARRY_IN(alu1bit_9_carry_out),
    .S3(S0[3]), .S2(S0[2]), .SELECT(multiplexer_4_out), .S1(S0[1]), .S0(S0[0]),
    .CARRY_OUT(alu1bit_10_carry_out));
  ALU1Bit alu1bit_11 (
    .IR(A[9]), .IL(A[11]), .A(A[10]), .B(B[10]), .DATA_OUT(Output[10]), .CARRY_IN(alu1bit_10_carry_out),
    .S3(S0[3]), .S2(S0[2]), .SELECT(multiplexer_4_out), .S1(S0[1]), .S0(S0[0]),
    .CARRY_OUT(alu1bit_11_carry_out));
  ALU1Bit alu1bit_12 (
    .IR(A[10]), .IL(A[12]), .A(A[11]), .B(B[11]), .DATA_OUT(Output[11]), .CARRY_IN(alu1bit_11_carry_out),
    .S3(S0[3]), .S2(S0[2]), .SELECT(multiplexer_4_out), .S1(S0[1]), .S0(S0[0]),
    .CARRY_OUT(alu1bit_12_carry_out));
  ALU1Bit alu1bit_13 (
    .IR(A[11]), .IL(A[13]), .A(A[12]), .B(B[12]), .DATA_OUT(Output[12]), .CARRY_IN(alu1bit_12_carry_out),
    .S3(S0[3]), .S2(S0[2]), .SELECT(multiplexer_4_out), .S1(S0[1]), .S0(S0[0]),
    .CARRY_OUT(alu1bit_13_carry_out));
  ALU1Bit alu1bit_14 (
    .IR(A[12]), .IL(A[14]), .A(A[13]), .B(B[13]), .DATA_OUT(Output[13]), .CARRY_IN(alu1bit_13_carry_out),
    .S3(S0[3]), .S2(S0[2]), .SELECT(multiplexer_4_out), .S1(S0[1]), .S0(S0[0]),
    .CARRY_OUT(alu1bit_14_carry_out));
  ALU1Bit alu1bit_15 (
    .IR(A[13]), .IL(A[15]), .A(A[14]), .B(B[14]), .DATA_OUT(Output[14]), .CARRY_IN(alu1bit_14_carry_out),
    .S3(S0[3]), .S2(S0[2]), .SELECT(multiplexer_4_out), .S1(S0[1]), .S0(S0[0]),
    .CARRY_OUT(alu1bit_15_carry_out));
  ALU1Bit alu1bit_16 (
    .IR(A[14]), .IL(R___L), .A(A[15]), .B(B[15]), .DATA_OUT(Output[15]), .CARRY_IN(alu1bit_15_carry_out),
    .S3(S0[3]), .S2(S0[2]), .SELECT(multiplexer_4_out), .S1(S0[1]), .S0(S0[0]),
    .CARRY_OUT(Output_to_Register[0]));
  not not_2 (not_2_out, A[15]);
  and and_3 (and_3_out, not_2_out, Output[15]);
  xnor xnor_1 (xnor_1_out, A[15], B[15]);
  and and_4 (and_4_out, xnor_1_out, xor_2_out);
  Multiplexer #(.enable("false")) multiplexer_5 (
    .in0(Input_from_Register[1]), .in1(multiplexer_6_out), .out(Oo1), .sel(S0[3]));
  or or_1 (or_1_out, Output[6], Output[5], Output[4], Output[3], Output[2], Output[1], Output[0]);
  or or_2 (or_2_out, Output[15], Output[14], Output[13], Output[12], Output[11], Output[10], Output[9], Output[7], Output[8]);
  xor xor_2 (xor_2_out, Output[15], A[15]);
  nor nor_1 (Output_to_Register[3], or_1_out, or_2_out);
  xor xor_3 (xor_3_out, A[15], B[15]);
  Multiplexer #(.select(2), .enable("false")) multiplexer_6 (
    .in0(and_3_out), .in1(and_4_out), .in2(and_5_out), .in3(and_6_out), .out(multiplexer_6_out), .sel(S0[1:0]));
  xor xor_4 (xor_4_out, Output[15], A[15]);
  and and_5 (and_5_out, xor_3_out, xor_4_out);
  not not_3 (not_3_out, Output[15]);
  and and_6 (and_6_out, A[15], not_3_out);

  assign Input_from_Register[6:5] = {2{Input_from_Register[7]}};
  assign {Output_to_Register[6:5], Output_to_Register[2]} = {{2{Output_to_Register[7]}}, Output[15]};

  // Other names for the same wires on the sheet: Ci = Input_from_Register[0]; S0_t = S0[0]; S1 = S0[1];
  //   Oi = Input_from_Register[1]; Ni = Input_from_Register[2]; Zi = Input_from_Register[3];
  //   Ii = Input_from_Register[4]; Ri = Input_from_Register[7]; F15 = Output[15]; No = Output[15];
  //   Co = Output_to_Register[0]; Oo = Output_to_Register[1]; Zo = Output_to_Register[3]; Io = Output_to_Register[4];
  //   Ro = Output_to_Register[7]; S3 = S0[3]

  // Notes on the sheet:
  //   Overflow case in ASHL
  //   Overflow case in ASHL
  //   Overflow
  //   Overflow case in Arithmetic Operations
  //   S1
  //   S2
  //   S3
  //   Cout
  //   Pos + 1 = Neg
  //   A + 1 Overflow Control
  //   Overflow case in Arithmetic Operations
  //   Addition Overflow Control
  //   Subtraction Overflow Control
  //   Neg - 1 = Pos
  //   A - 1 Overflow Control
endmodule

module ALU1Bit (
  input  IR,
  input  IL,
  input  SELECT,
  input  CARRY_IN,
  input  A,
  input  B,
  input  S3,
  input  S2,
  input  S1,
  input  S0,
  output DATA_OUT,
  output CARRY_OUT
);

  wire arithmeticunit1bit_1_carry_out, arithmeticunit1bit_1_data_out, logicunit1bit_1_carry_out,
       logicunit1bit_1_output, multiplexer_1_out;

  Multiplexer #(.enable("false")) multiplexer_1 (.in0(IR), .in1(IL), .out(multiplexer_1_out), .sel(SELECT));
  LogicUnit1Bit logicunit1bit_1 (
    .A(A), .B(B), .OUTPUT(logicunit1bit_1_output), .CARRY_OUT(logicunit1bit_1_carry_out), .S1(S1), .S0(S0),
    .CARRY_IN(CARRY_IN));
  ArithmeticUnit1Bit arithmeticunit1bit_1 (
    .CARRY_IN(CARRY_IN), .A(A), .B(B), .DATA_OUT(arithmeticunit1bit_1_data_out), .S1(S1), .S0(S0),
    .CARRY_OUT(arithmeticunit1bit_1_carry_out));
  Multiplexer #(.enable("false")) multiplexer_2 (
    .in0(logicunit1bit_1_carry_out), .in1(arithmeticunit1bit_1_carry_out), .out(CARRY_OUT), .sel(S3));
  Multiplexer #(.select(2), .enable("false")) multiplexer_3 (
    .in0(multiplexer_1_out), .in1(logicunit1bit_1_output), .in2(arithmeticunit1bit_1_data_out),
    .in3(arithmeticunit1bit_1_data_out), .out(DATA_OUT), .sel({S3, S2}));

  // Notes on the sheet:
  //   D
  //   E
endmodule
