// Logisim project Week 5  Basic Computer with Hardwired Control Unit.circ as structural Verilog: 14 circuits, main circuit main
module main (
  input  in_1,
  input  in_2,
  input  in_3,
  input  in_4,
  input  in_5,
  input  [9:0] in_6,
  input  in_7,
  input  in_8,
  input  [7:0] in_9,
  input  in_10,
  input  in_11,
  input  in_12,
  input  in_13,
  input  in_14,
  input  [4:0] in_15,
  input  in_16,
  input  in_17,
  input  in_18,
  input  in_19,
  input  in_20,
  input  in_21,
  input  in_22,
  input  in_23,
  input  in_24,
  input  in_25,
  input  in_26,
  input  [3:0] in_27,
  output [7:0] out_28
);

  wire A0, A1, and_1_out, and_2_out, and_3_out, and_4_out, and_5_out, and_6_out, and_7_out, and_8_out,
       and_9_out, and_10_out, and_11_out, and_12_out, and_13_out, and_14_out, and_15_out, and_16_out,
       and_17_out, and_18_out, and_20_out, and_21_out, and_22_out, and_23_out, and_24_out, and_25_out,
       and_26_out, and_27_out, and_28_out, and_30_out, and_32_out, and_33_out, and_34_out, and_35_out,
       and_36_out, and_37_out, and_38_out, and_39_out, and_40_out, and_41_out, and_42_out, and_43_out,
       and_44_out, and_45_out, and_46_out, and_47_out, and_48_out, and_49_out, and_56_out, and_57_out,
       and_58_out, and_59_out, and_60_out, and_61_out, and_63_out, and_64_out, and_65_out, CarryFlag, CL_AC,
       CL_SC, CL_X, clock_1_out, D0, D1, D2, EA0, EA1, EA2, EA3, EA4, EA5, EA6, EA7, EA8, EA9, INC_GPRB,
       INC_PC, INC_X, K0, K1, K2, K3, K4, K5, K6, K7, K8, K9, K10, K11, K12, K13, K14, K15, LD_AC, LD_AR,
       LD_CCR, LD_GPRA, LD_GPRB, LD_PC, LD_SP, M, MLOAD, MSTR, not_1_out, not_2_out, not_3_out, not_4_out,
       not_5_out, not_6_out, or_1_out, or_2_out, or_4_out, or_5_out, or_6_out, or_7_out, or_8_out, or_9_out,
       or_11_out, or_12_out, or_15_out, or_16_out, or_17_out, or_18_out, or_20_out, or_24_out, or_25_out,
       or_26_out, or_27_out, or_29_out, or_30_out, or_32_out, or_33_out, or_35_out, or_37_out, S, S0, S3, T1,
       T2, T3, T4, T5, T6, T7, T8, T9, T10, T11, T12, T13, T14, T15;
  wire [3:0] abus_1_output, abus_1_output_2, AC_output_2, AC_output_3, alubus_1_out_4_2, alubus_1_out_4_3,
       counter_1_q;
  wire [7:0] AC_output, alubus_1_out_4, CCR_output, dbus_1__8bitout, INPR_output;
  wire [7:1] CCR;
  wire [9:0] adder_1_out, AR_out_7, dbus_1__10bitout, multiplexer_1_out, PC_out_7, SP_out_7, X_output;
  wire [9:8] abus_1_output_3;
  wire [15:0] alu16bit_1_output, dbus_1__16bitout, dbus_1__16bitout_2, GPRA_output, GPRB_output, ram_1_data;
  wire [15:10] IR;

  Clock clock_1 (.out(clock_1_out));
  _5_Bit_Register X (
    .INPUT(in_15), .L(in_12), .I(INC_X), .C(CL_X), .CLK(clock_1_out), .OUTPUT({X_output[9], X_output[3:0]}));  // open: Carry
  Adder #(.width(10)) adder_1 (
    .a({{6{X_output[9]}}, X_output[3:0]}), .b(dbus_1__10bitout), .out(adder_1_out));  // open: cin, cout
  DBus dbus_1 (
    .D1(D1), .D2(D2), .D0(D0), ._10BitOut(dbus_1__10bitout), ._16BitOut_2(dbus_1__16bitout_2),
    ._8BitOut(dbus_1__8bitout), .Memory(ram_1_data), .GPRB(GPRB_output), .GPRA(GPRA_output),
    .AC({AC_output_3, AC_output_2, AC_output}), .ABUS({abus_1_output_3, abus_1_output_2, abus_1_output}),
    .INPR(INPR_output), .IR({IR, EA9, EA8, EA7, EA6, EA5, EA4, EA3, EA2, EA1, EA0}),
    ._16BitOut(dbus_1__16bitout), .X({X_output[9], X_output[3:0]}));
  Decoder #(.select(4), .enable("false")) decoder_1 (
    .out0(INC_PC), .out1(T1), .out2(T2), .out3(T3), .out4(T4), .out5(T5), .out6(T6), .out7(T7), .out8(T8),
    .out9(T9), .out10(T10), .out11(T11), .out12(T12), .out13(T13), .out14(T14), .out15(T15), .sel(counter_1_q));
  Counter_part #(.width(4), .max('hf)) counter_1 (
    .D(in_27), .count(1'b1), .Q(counter_1_q), .clk(clock_1_out), .clr(CL_SC));  // open: load, carry
  and and_1 (and_1_out, K8, CCR[3]);
  and and_2 (and_2_out, K9, CCR[2]);
  not not_1 (not_1_out, IR[15]);
  and and_3 (and_3_out, K8, CCR[3]);
  and and_4 (and_4_out, K9, CCR[2]);
  and and_5 (and_5_out, K8, CCR[3]);
  Multiplexer #(.width(10), .enable("false")) multiplexer_1 (
    .in0({EA9, EA8, EA7, EA6, EA5, EA4, EA3, EA2, EA1, EA0}), .in1(adder_1_out), .out(multiplexer_1_out),
    .sel(S));
  Hex_Digit_Display hex_digit_display_1 (.value(alubus_1_out_4_2));  // open: dp
  Hex_Digit_Display hex_digit_display_2 (.value(alubus_1_out_4_3));  // open: dp
  Hex_Digit_Display hex_digit_display_3 (.value(AC_output_2));  // open: dp
  Hex_Digit_Display hex_digit_display_4 (.value(AC_output_3));  // open: dp
  or or_1 (or_1_out, K10, K5);
  and and_6 (and_6_out, K8, CCR[3]);
  and and_7 (and_7_out, K9, CCR[2]);
  and and_8 (and_8_out, K9, CCR[2]);
  and and_9 (and_9_out, K9, CCR[2]);
  _10_Bit_Register AR (
    .L(LD_AR), .in_1(multiplexer_1_out), .I(in_4), .C(in_1), .in_5(clock_1_out), .out_7(AR_out_7));  // open: Carry
  _16_Bit_Register u_IR (
    .Input(dbus_1__16bitout), .CLK(clock_1_out),
    .Output({IR, EA9, EA8, EA7, EA6, EA5, EA4, EA3, EA2, EA1, EA0}), .L(INC_PC), .I(in_10), .C(in_8));  // open: Carry
  _16_Bit_Register GPRA (
    .Input(dbus_1__16bitout_2), .CLK(clock_1_out), .Output(GPRA_output), .L(LD_GPRA), .I(in_21), .C(in_19));  // open: Carry
  Hex_Digit_Display hex_digit_display_5 (.value(alubus_1_out_4[7:4]));  // open: dp
  Hex_Digit_Display hex_digit_display_6 (.value(alubus_1_out_4[3:0]));  // open: dp
  Hex_Digit_Display hex_digit_display_7 (.value(AC_output[7:4]));  // open: dp
  Hex_Digit_Display hex_digit_display_8 (.value(AC_output[3:0]));  // open: dp
  and and_10 (and_10_out, or_1_out, T2);
  and and_11 (and_11_out, K10, T3);
  and and_12 (and_12_out, K8, CCR[3]);
  and and_13 (and_13_out, K9, CCR[2]);
  or or_2 (or_2_out, T3, T4);
  and and_14 (and_14_out, K8, CCR[3]);
  or or_3 (LD_CCR, and_10_out, and_11_out);
  or or_4 (or_4_out, K1, K2, K3, K4, K7, and_1_out, and_2_out, K15);
  and and_15 (and_15_out, not_1_out, IR[14], T2);
  or or_5 (or_5_out, K15, K8, K1, K2, K3, K4, K7);
  or or_6 (or_6_out, K1, K2, K3, K4, K7, and_3_out, and_4_out, K15);
  and and_16 (and_16_out, K10, or_2_out);
  not not_2 (not_2_out, IR[14]);
  RAM #(.addrWidth(10), .dataWidth(16), .bus("separate")) ram_1 (
    .addr({abus_1_output_3, abus_1_output_2, abus_1_output}), .din(dbus_1__16bitout_2), .data(ram_1_data),
    .str(MSTR), .clk(clock_1_out), .ld(MLOAD));  // open: sel, clr
  _10_Bit_Register PC (
    .L(LD_PC), .in_1(dbus_1__10bitout), .I(INC_PC), .C(in_2), .in_5(clock_1_out), .out_7(PC_out_7));  // open: Carry
  ALUBus alubus_1 (
    .S(M), .A(GPRA_output), .B(GPRB_output), .out_4({alubus_1_out_4_3, alubus_1_out_4_2, alubus_1_out_4}));
  Decoder #(.select(4), .enable("false")) decoder_2 (
    .out0(K0), .out1(K1), .out2(K2), .out3(K3), .out4(K4), .out5(K5), .out6(K6), .out7(K7), .out8(K8),
    .out9(K9), .out10(K10), .out11(K11), .out12(K12), .out13(K13), .out14(K14), .out15(K15), .sel(IR[13:10]));
  or or_7 (or_7_out, IR[14], IR[15]);
  and and_17 (and_17_out, or_4_out, and_15_out);
  and and_18 (and_18_out, or_5_out, T3);
  _16_Bit_Register GPRB (
    .Input(dbus_1__16bitout_2), .CLK(clock_1_out), .Output(GPRB_output), .L(LD_GPRB), .I(INC_GPRB), .C(in_20));  // open: Carry
  ALU16Bit alu16bit_1 (
    .Input_from_Register(CCR_output), .Output_to_Register({CCR, CarryFlag}),
    .A({alubus_1_out_4_3, alubus_1_out_4_2, alubus_1_out_4}), .Output(alu16bit_1_output),
    .B({AC_output_3, AC_output_2, AC_output}), .S0({S3, in_24, in_25, S0}));
  or or_8 (or_8_out, K1, K2, K3, K4, K7, and_6_out, and_7_out, K15);
  and and_19 (A1, or_6_out, IR[14], T2, IR[15]);
  or or_9 (or_9_out, K1, K2, K3, K4, K7, and_14_out, and_9_out, K15);
  _10_Bit_Register SP (
    .L(LD_SP), .in_1(dbus_1__10bitout), .I(in_5), .C(in_3), .in_5(clock_1_out), .out_7(SP_out_7));  // open: Carry
  and and_20 (and_20_out, or_8_out, or_7_out);
  or or_10 (A0, and_17_out, and_18_out);
  or or_11 (or_11_out, K1, K2, K3, K4, K7, and_12_out, and_13_out, K15);
  and and_21 (and_21_out, IR[15], IR[14], T2);
  or or_12 (or_12_out, K7, and_5_out, and_8_out);
  and and_22 (and_22_out, or_12_out, T3);
  ABus abus_1 (
    .A0(A0), .A1(A1), .Adress_Register(AR_out_7), .Stack_Pointer(SP_out_7), .Program_Counter(PC_out_7),
    .Output({abus_1_output_3, abus_1_output_2, abus_1_output}));
  _8_Bit_Register INPR (
    .INPUT(in_9), .I(in_13), .C(in_11), .OUTPUT(INPR_output), .CLK(clock_1_out), .L(in_14));  // open: Carry
  _8_Bit_Register OUTR (
    .INPUT(dbus_1__8bitout), .I(in_17), .C(in_16), .OUTPUT(out_28), .CLK(clock_1_out), .L(in_18));  // open: Carry
  Hex_Digit_Display hex_digit_display_9 (.value(dbus_1__16bitout_2[11:8]));  // open: dp
  Hex_Digit_Display hex_digit_display_10 (.value(dbus_1__16bitout_2[15:12]));  // open: dp
  _16_Bit_Register AC (
    .Input(alu16bit_1_output), .CLK(clock_1_out), .Output({AC_output_3, AC_output_2, AC_output}), .L(LD_AC),
    .I(in_26), .C(CL_AC));  // open: Carry
  and and_23 (and_23_out, and_20_out, T2);
  and and_24 (and_24_out, or_11_out, and_21_out);
  and and_25 (and_25_out, or_9_out, not_2_out, T2, IR[15]);
  and and_26 (and_26_out, K9, CCR[2]);
  Hex_Digit_Display hex_digit_display_11 (.value(dbus_1__16bitout_2[7:4]));  // open: dp
  Hex_Digit_Display hex_digit_display_12 (.value(dbus_1__16bitout_2[3:0]));  // open: dp
  _8_Bit_Register u_CCR (
    .INPUT({CCR, CarryFlag}), .I(in_23), .C(in_22), .OUTPUT(CCR_output), .CLK(clock_1_out), .L(LD_CCR));  // open: Carry
  and and_27 (and_27_out, K8, CCR[3]);
  Hex_Digit_Display hex_digit_display_13 (.value({2'b00, abus_1_output_3}));  // open: dp
  Hex_Digit_Display hex_digit_display_14 (.value(abus_1_output_2));  // open: dp
  or or_13 (LD_AR, and_23_out, T1);
  or or_14 (D0, and_24_out, and_22_out, and_16_out, and_25_out);
  not not_3 (not_3_out, IR[14]);
  Hex_Digit_Display hex_digit_display_15 (.value(abus_1_output));  // open: dp
  and and_28 (and_28_out, K9, CCR[2]);
  or or_15 (or_15_out, K1, K2, K3, K4, K7, and_27_out, and_26_out, K15);
  and and_29 (CL_AC, K11, T2);
  and and_30 (and_30_out, K8, CCR[3]);
  and and_31 (INC_X, T2, K13);
  and and_32 (and_32_out, K8, CCR[3]);
  and and_33 (and_33_out, K9, CCR[2]);
  and and_34 (and_34_out, K3, T3);
  not not_4 (not_4_out, IR[14]);
  or or_16 (or_16_out, T3, T4);
  and and_35 (and_35_out, or_15_out, not_3_out, T2, IR[15]);
  and and_36 (and_36_out, K8, CCR[3]);
  and and_37 (and_37_out, K9, CCR[2]);
  and and_38 (and_38_out, or_16_out, K10);
  and and_39 (and_39_out, K4, T3);
  or or_17 (or_17_out, K5, K6);
  and and_40 (and_40_out, or_17_out, T2);
  or or_18 (or_18_out, T2, T3);
  and and_41 (and_41_out, K8, CCR[3]);
  and and_42 (and_42_out, K9, CCR[2]);
  or or_19 (D2, and_34_out, and_46_out);
  or or_20 (or_20_out, K1, K2, K3, K4, K7, and_30_out, and_28_out, K15);
  and and_43 (and_43_out, K12, T2);
  and and_44 (and_44_out, T1, IR[14]);
  or or_21 (LD_AC, and_40_out, and_45_out);
  and and_45 (and_45_out, or_18_out, K10);
  not not_5 (not_5_out, IR[14]);
  or or_22 (D1, and_38_out, and_39_out, and_35_out);
  or or_23 (CL_X, and_43_out, and_44_out);
  or or_24 (or_24_out, K1, K2, K3, K4, K7, and_32_out, and_33_out, K15);
  or or_25 (or_25_out, K11, K12, K13, K14, K5, K6);
  or or_26 (or_26_out, K7, and_41_out, and_42_out);
  and and_46 (and_46_out, or_20_out, not_4_out, T2, IR[15]);
  and and_47 (and_47_out, or_24_out, T4);
  and and_48 (and_48_out, or_25_out, T3);
  and and_49 (and_49_out, K10, T5);
  or or_27 (or_27_out, K1, K2, K3, K4, K7, and_36_out, and_37_out, K15);
  and and_50 (LD_PC, T3, or_26_out);
  or or_28 (CL_SC, and_47_out, and_48_out, and_49_out);
  and and_51 (S, or_27_out, not_5_out, T2, IR[15]);
  and and_52 (LD_SP, K15, T3);
  or or_29 (or_29_out, K3, K4);
  and and_53 (MSTR, or_29_out, T3);
  or or_30 (or_30_out, K2, K10);
  and and_54 (LD_GPRB, or_30_out, T3);
  and and_55 (INC_GPRB, K14, T2);
  and and_56 (and_56_out, K1, T3);
  and and_57 (and_57_out, K10, T4);
  and and_58 (and_58_out, K8, CCR[3]);
  and and_59 (and_59_out, K9, CCR[2]);
  or or_31 (LD_GPRA, and_56_out, and_57_out);
  not not_6 (not_6_out, IR[15]);
  or or_32 (or_32_out, K5, K6);
  or or_33 (or_33_out, T2, T3);
  and and_60 (and_60_out, K10, T3);
  and and_61 (and_61_out, K6, T2);
  and and_62 (S0, or_32_out, T2);
  and and_63 (and_63_out, or_33_out, K10);
  or or_34 (M, and_60_out, and_61_out);
  or or_35 (or_35_out, K1, K2, K3, K4, K7, and_58_out, and_59_out, K15);
  or or_36 (S3, S0, and_63_out);
  and and_64 (and_64_out, or_35_out, IR[14], T2, not_6_out);
  or or_37 (or_37_out, K1, K2, K15);
  and and_65 (and_65_out, or_37_out, T3);
  or or_38 (MLOAD, and_64_out, and_65_out, INC_PC);

  // Other names for the same wires on the sheet: IR[9:0] = {EA9, EA8, EA7, EA6, EA5, EA4, EA3, EA2, EA1, EA0};
  //   OpCode0 = IR[10]; OpCode1 = IR[11]; OpCode2 = IR[12]; OpCode3 = IR[13]; CCR[0] = CarryFlag;
  //   OverflowFlag = CCR[1]; NegativeFlag = CCR[2]; ZeroFlag = CCR[3]; R0 = IR[14]; R1 = IR[15]; LD_IR = INC_PC;
  //   T0 = INC_PC

  // Notes on the sheet:
  //   Extension to 10bit
  //   CCR
  //   ALU-Bus DISPLAY
  //   AC DISPLAY
  //   Address Register
  //   A-BUS Selectors
  //   Control Unit INPUTs
  //   D-BUS Selectors
  //   D-Bus DISPLAY
  //   A-Bus DISPLAY
  //   X Register
  //   Accumulator
  //   Sequence Counter
  //   Program Counter
  //   Instruction Register
  //   MUX Select Bit
  //   SP Register
  //   GPRB Register
  //   RAM
  //   GPRA Register
  //   ALU Select Bit
  //   ALU-BUS Selector
endmodule

module _8_Bit_Register (
  input  [7:0] INPUT,
  input  L,
  input  I,
  input  C,
  input  CLK,
  output Carry,
  output [7:0] OUTPUT
);

  wire and_2_out, and_3_out, and_4_out, and_5_out, and_6_out, and_7_out, and_8_out, and_9_out, and_10_out,
       and_11_out, and_12_out, and_13_out, and_14_out, and_15_out, and_16_out, and_17_out, and_18_out,
       and_19_out, and_20_out, and_21_out, and_22_out, and_23_out, and_24_out, and_25_out, and_26_out,
       not_1_out, not_2_out, not_3_out, not_4_out, not_5_out, not_6_out, not_7_out, not_8_out, not_9_out,
       not_10_out, or_1_out, or_2_out, or_3_out, or_4_out, or_5_out, or_6_out, or_7_out, or_8_out, or_9_out,
       or_10_out, or_11_out, or_12_out, or_13_out, or_14_out, or_15_out, or_16_out;

  not not_1 (not_1_out, L);
  not not_2 (not_2_out, INPUT[7]);
  not not_3 (not_3_out, INPUT[6]);
  not not_4 (not_4_out, INPUT[5]);
  not not_5 (not_5_out, INPUT[4]);
  not not_6 (not_6_out, INPUT[3]);
  not not_7 (not_7_out, INPUT[2]);
  not not_8 (not_8_out, INPUT[1]);
  not not_9 (not_9_out, INPUT[0]);
  not not_10 (not_10_out, I);
  and and_1 (Carry, and_4_out, OUTPUT[7]);
  and and_2 (and_2_out, L, not_2_out);
  and and_3 (and_3_out, INPUT[7], L);
  and and_4 (and_4_out, and_7_out, OUTPUT[6]);
  and and_5 (and_5_out, L, not_3_out);
  and and_6 (and_6_out, INPUT[6], L);
  and and_7 (and_7_out, and_10_out, OUTPUT[5]);
  and and_8 (and_8_out, L, not_4_out);
  and and_9 (and_9_out, INPUT[5], L);
  and and_10 (and_10_out, and_13_out, OUTPUT[4]);
  and and_11 (and_11_out, L, not_5_out);
  and and_12 (and_12_out, INPUT[4], L);
  and and_13 (and_13_out, and_16_out, OUTPUT[3]);
  and and_14 (and_14_out, L, not_6_out);
  and and_15 (and_15_out, INPUT[3], L);
  and and_16 (and_16_out, and_19_out, OUTPUT[2]);
  and and_17 (and_17_out, L, not_7_out);
  and and_18 (and_18_out, INPUT[2], L);
  and and_19 (and_19_out, and_22_out, OUTPUT[1]);
  and and_20 (and_20_out, L, not_8_out);
  and and_21 (and_21_out, INPUT[1], L);
  and and_22 (and_22_out, and_26_out, OUTPUT[0]);
  and and_23 (and_23_out, L, not_9_out);
  and and_24 (and_24_out, INPUT[0], L);
  and and_25 (and_25_out, not_1_out, not_10_out, C);
  and and_26 (and_26_out, not_1_out, I);
  or or_1 (or_1_out, and_4_out, and_25_out, and_2_out);
  or or_2 (or_2_out, and_4_out, and_3_out);
  or or_3 (or_3_out, and_7_out, and_25_out, and_5_out);
  or or_4 (or_4_out, and_7_out, and_6_out);
  or or_5 (or_5_out, and_10_out, and_25_out, and_8_out);
  or or_6 (or_6_out, and_10_out, and_9_out);
  or or_7 (or_7_out, and_13_out, and_25_out, and_11_out);
  or or_8 (or_8_out, and_13_out, and_12_out);
  or or_9 (or_9_out, and_16_out, and_25_out, and_14_out);
  or or_10 (or_10_out, and_16_out, and_15_out);
  or or_11 (or_11_out, and_19_out, and_25_out, and_17_out);
  or or_12 (or_12_out, and_19_out, and_18_out);
  or or_13 (or_13_out, and_22_out, and_25_out, and_20_out);
  or or_14 (or_14_out, and_22_out, and_21_out);
  or or_15 (or_15_out, and_26_out, and_25_out, and_23_out);
  or or_16 (or_16_out, and_26_out, and_24_out);
  J_K_Flip_Flop j_k_ff_1 (.J(or_2_out), .clk(CLK), .K(or_1_out), .Q(OUTPUT[7]));  // open: Qn, preset, en, reset
  J_K_Flip_Flop j_k_ff_2 (.J(or_4_out), .clk(CLK), .K(or_3_out), .Q(OUTPUT[6]));  // open: Qn, preset, en, reset
  J_K_Flip_Flop j_k_ff_3 (.J(or_6_out), .clk(CLK), .K(or_5_out), .Q(OUTPUT[5]));  // open: Qn, preset, en, reset
  J_K_Flip_Flop j_k_ff_4 (.J(or_8_out), .clk(CLK), .K(or_7_out), .Q(OUTPUT[4]));  // open: Qn, preset, en, reset
  J_K_Flip_Flop j_k_ff_5 (.J(or_10_out), .clk(CLK), .K(or_9_out), .Q(OUTPUT[3]));  // open: Qn, preset, en, reset
  J_K_Flip_Flop j_k_ff_6 (.J(or_12_out), .clk(CLK), .K(or_11_out), .Q(OUTPUT[2]));  // open: Qn, preset, en, reset
  J_K_Flip_Flop j_k_ff_7 (.J(or_14_out), .clk(CLK), .K(or_13_out), .Q(OUTPUT[1]));  // open: Qn, preset, en, reset
  J_K_Flip_Flop j_k_ff_8 (.J(or_16_out), .clk(CLK), .K(or_15_out), .Q(OUTPUT[0]));  // open: Qn, preset, en, reset
endmodule

module ABus (
  input  A0,
  input  A1,
  input  [9:0] Adress_Register,
  input  [9:0] Stack_Pointer,
  input  [9:0] Program_Counter,
  output [9:0] Output
);

  wire decoder_1_out0, decoder_1_out1, decoder_1_out2, decoder_1_out3, decoder_2_out0, decoder_2_out1,
       decoder_2_out2, decoder_2_out3, decoder_3_out0, decoder_3_out1, decoder_3_out2, decoder_3_out3,
       decoder_4_out0, decoder_4_out1, decoder_4_out2, decoder_4_out3, decoder_5_out0, decoder_5_out1,
       decoder_5_out2, decoder_5_out3, decoder_6_out0, decoder_6_out1, decoder_6_out2, decoder_6_out3,
       decoder_7_out0, decoder_7_out1, decoder_7_out2, decoder_7_out3, decoder_8_out0, decoder_8_out1,
       decoder_8_out2, decoder_8_out3, decoder_9_out0, decoder_9_out1, decoder_9_out2, decoder_9_out3,
       decoder_10_out0, decoder_10_out1, decoder_10_out2, decoder_10_out3;

  assign Output[0] = decoder_1_out0 ? Program_Counter[0] : 1'bz;  // Controlled_Buffer controlled_buffer_1
  Decoder #(.select(2), .enable("false")) decoder_1 (
    .out0(decoder_1_out0), .out1(decoder_1_out1), .out2(decoder_1_out2), .out3(decoder_1_out3), .sel({A1, A0}));
  assign Output[0] = decoder_1_out1 ? Adress_Register[0] : 1'bz;  // Controlled_Buffer controlled_buffer_2
  assign Output[0] = decoder_1_out2 ? Stack_Pointer[0] : 1'bz;  // Controlled_Buffer controlled_buffer_3
  assign Output[0] = decoder_1_out3 ? Stack_Pointer[0] : 1'bz;  // Controlled_Buffer controlled_buffer_4
  assign Output[1] = decoder_2_out0 ? Program_Counter[1] : 1'bz;  // Controlled_Buffer controlled_buffer_5
  Decoder #(.select(2), .enable("false")) decoder_2 (
    .out0(decoder_2_out0), .out1(decoder_2_out1), .out2(decoder_2_out2), .out3(decoder_2_out3), .sel({A1, A0}));
  assign Output[1] = decoder_2_out1 ? Adress_Register[1] : 1'bz;  // Controlled_Buffer controlled_buffer_6
  assign Output[1] = decoder_2_out2 ? Stack_Pointer[1] : 1'bz;  // Controlled_Buffer controlled_buffer_7
  assign Output[1] = decoder_2_out3 ? Stack_Pointer[1] : 1'bz;  // Controlled_Buffer controlled_buffer_8
  assign Output[2] = decoder_3_out0 ? Program_Counter[2] : 1'bz;  // Controlled_Buffer controlled_buffer_9
  Decoder #(.select(2), .enable("false")) decoder_3 (
    .out0(decoder_3_out0), .out1(decoder_3_out1), .out2(decoder_3_out2), .out3(decoder_3_out3), .sel({A1, A0}));
  assign Output[2] = decoder_3_out1 ? Adress_Register[2] : 1'bz;  // Controlled_Buffer controlled_buffer_10
  assign Output[2] = decoder_3_out2 ? Stack_Pointer[2] : 1'bz;  // Controlled_Buffer controlled_buffer_11
  assign Output[2] = decoder_3_out3 ? Stack_Pointer[2] : 1'bz;  // Controlled_Buffer controlled_buffer_12
  assign Output[3] = decoder_4_out0 ? Program_Counter[3] : 1'bz;  // Controlled_Buffer controlled_buffer_13
  Decoder #(.select(2), .enable("false")) decoder_4 (
    .out0(decoder_4_out0), .out1(decoder_4_out1), .out2(decoder_4_out2), .out3(decoder_4_out3), .sel({A1, A0}));
  assign Output[3] = decoder_4_out1 ? Adress_Register[3] : 1'bz;  // Controlled_Buffer controlled_buffer_14
  assign Output[3] = decoder_4_out2 ? Stack_Pointer[3] : 1'bz;  // Controlled_Buffer controlled_buffer_15
  assign Output[3] = decoder_4_out3 ? Stack_Pointer[3] : 1'bz;  // Controlled_Buffer controlled_buffer_16
  assign Output[4] = decoder_5_out0 ? Program_Counter[4] : 1'bz;  // Controlled_Buffer controlled_buffer_17
  Decoder #(.select(2), .enable("false")) decoder_5 (
    .out0(decoder_5_out0), .out1(decoder_5_out1), .out2(decoder_5_out2), .out3(decoder_5_out3), .sel({A1, A0}));
  assign Output[4] = decoder_5_out1 ? Adress_Register[4] : 1'bz;  // Controlled_Buffer controlled_buffer_18
  assign Output[4] = decoder_5_out2 ? Stack_Pointer[4] : 1'bz;  // Controlled_Buffer controlled_buffer_19
  assign Output[4] = decoder_5_out3 ? Stack_Pointer[4] : 1'bz;  // Controlled_Buffer controlled_buffer_20
  assign Output[5] = decoder_6_out0 ? Program_Counter[5] : 1'bz;  // Controlled_Buffer controlled_buffer_21
  Decoder #(.select(2), .enable("false")) decoder_6 (
    .out0(decoder_6_out0), .out1(decoder_6_out1), .out2(decoder_6_out2), .out3(decoder_6_out3), .sel({A1, A0}));
  assign Output[5] = decoder_6_out1 ? Adress_Register[5] : 1'bz;  // Controlled_Buffer controlled_buffer_22
  assign Output[5] = decoder_6_out2 ? Stack_Pointer[5] : 1'bz;  // Controlled_Buffer controlled_buffer_23
  assign Output[5] = decoder_6_out3 ? Stack_Pointer[5] : 1'bz;  // Controlled_Buffer controlled_buffer_24
  assign Output[6] = decoder_7_out0 ? Program_Counter[6] : 1'bz;  // Controlled_Buffer controlled_buffer_25
  Decoder #(.select(2), .enable("false")) decoder_7 (
    .out0(decoder_7_out0), .out1(decoder_7_out1), .out2(decoder_7_out2), .out3(decoder_7_out3), .sel({A1, A0}));
  assign Output[6] = decoder_7_out1 ? Adress_Register[6] : 1'bz;  // Controlled_Buffer controlled_buffer_26
  assign Output[6] = decoder_7_out2 ? Stack_Pointer[6] : 1'bz;  // Controlled_Buffer controlled_buffer_27
  assign Output[6] = decoder_7_out3 ? Stack_Pointer[6] : 1'bz;  // Controlled_Buffer controlled_buffer_28
  assign Output[7] = decoder_8_out0 ? Program_Counter[7] : 1'bz;  // Controlled_Buffer controlled_buffer_29
  Decoder #(.select(2), .enable("false")) decoder_8 (
    .out0(decoder_8_out0), .out1(decoder_8_out1), .out2(decoder_8_out2), .out3(decoder_8_out3), .sel({A1, A0}));
  assign Output[7] = decoder_8_out1 ? Adress_Register[7] : 1'bz;  // Controlled_Buffer controlled_buffer_30
  assign Output[7] = decoder_8_out2 ? Stack_Pointer[7] : 1'bz;  // Controlled_Buffer controlled_buffer_31
  assign Output[7] = decoder_8_out3 ? Stack_Pointer[7] : 1'bz;  // Controlled_Buffer controlled_buffer_32
  assign Output[8] = decoder_9_out0 ? Program_Counter[8] : 1'bz;  // Controlled_Buffer controlled_buffer_33
  Decoder #(.select(2), .enable("false")) decoder_9 (
    .out0(decoder_9_out0), .out1(decoder_9_out1), .out2(decoder_9_out2), .out3(decoder_9_out3), .sel({A1, A0}));
  assign Output[8] = decoder_9_out1 ? Adress_Register[8] : 1'bz;  // Controlled_Buffer controlled_buffer_34
  assign Output[8] = decoder_9_out2 ? Stack_Pointer[8] : 1'bz;  // Controlled_Buffer controlled_buffer_35
  assign Output[8] = decoder_9_out3 ? Stack_Pointer[8] : 1'bz;  // Controlled_Buffer controlled_buffer_36
  assign Output[9] = decoder_10_out0 ? Program_Counter[9] : 1'bz;  // Controlled_Buffer controlled_buffer_37
  Decoder #(.select(2), .enable("false")) decoder_10 (
    .out0(decoder_10_out0), .out1(decoder_10_out1), .out2(decoder_10_out2), .out3(decoder_10_out3),
    .sel({A1, A0}));
  assign Output[9] = decoder_10_out1 ? Adress_Register[9] : 1'bz;  // Controlled_Buffer controlled_buffer_38
  assign Output[9] = decoder_10_out2 ? Stack_Pointer[9] : 1'bz;  // Controlled_Buffer controlled_buffer_39
  assign Output[9] = decoder_10_out3 ? Stack_Pointer[9] : 1'bz;  // Controlled_Buffer controlled_buffer_40

  // Other names for the same wires on the sheet: AR0 = Adress_Register[0]; AR1 = Adress_Register[1];
  //   AR2 = Adress_Register[2]; AR3 = Adress_Register[3]; AR4 = Adress_Register[4]; AR5 = Adress_Register[5];
  //   AR6 = Adress_Register[6]; AR7 = Adress_Register[7]; AR8 = Adress_Register[8]; AR9 = Adress_Register[9];
  //   A0_t = Output[0]; A1_t = Output[1]; A2 = Output[2]; A3 = Output[3]; A4 = Output[4]; A5 = Output[5];
  //   A6 = Output[6]; A7 = Output[7]; A8 = Output[8]; A9 = Output[9]; PC0 = Program_Counter[0];
  //   PC1 = Program_Counter[1]; PC2 = Program_Counter[2]; PC3 = Program_Counter[3]; PC4 = Program_Counter[4];
  //   PC5 = Program_Counter[5]; PC6 = Program_Counter[6]; PC7 = Program_Counter[7]; PC8 = Program_Counter[8];
  //   PC9 = Program_Counter[9]; SP0 = Stack_Pointer[0]; SP1 = Stack_Pointer[1]; SP2 = Stack_Pointer[2];
  //   SP3 = Stack_Pointer[3]; SP4 = Stack_Pointer[4]; SP5 = Stack_Pointer[5]; SP6 = Stack_Pointer[6];
  //   SP7 = Stack_Pointer[7]; SP8 = Stack_Pointer[8]; SP9 = Stack_Pointer[9]
endmodule

module DBus (
  input  D1,
  input  D2,
  input  D0,
  input  [15:0] Memory,
  input  [15:0] GPRB,
  input  [15:0] GPRA,
  input  [15:0] AC,
  input  [9:0] ABUS,
  input  [7:0] INPR,
  input  [15:0] IR,
  input  [4:0] X,
  output [15:0] _16BitOut,
  output [9:0] _10BitOut,
  output [15:0] _16BitOut_2,
  output [7:0] _8BitOut
);

  wire decoder_1_out0, decoder_1_out1, decoder_1_out2, decoder_1_out3, decoder_1_out4, decoder_1_out5,
       decoder_1_out6, decoder_1_out7, decoder_2_out0, decoder_2_out1, decoder_2_out2, decoder_2_out3,
       decoder_2_out4, decoder_2_out5, decoder_2_out6, decoder_2_out7, decoder_3_out0, decoder_3_out1,
       decoder_3_out2, decoder_3_out3, decoder_3_out4, decoder_3_out5, decoder_3_out6, decoder_3_out7,
       decoder_4_out0, decoder_4_out1, decoder_4_out2, decoder_4_out3, decoder_4_out4, decoder_4_out5,
       decoder_4_out6, decoder_4_out7, decoder_5_out0, decoder_5_out1, decoder_5_out2, decoder_5_out3,
       decoder_5_out4, decoder_5_out5, decoder_5_out6, decoder_5_out7, decoder_6_out0, decoder_6_out1,
       decoder_6_out2, decoder_6_out3, decoder_6_out4, decoder_6_out5, decoder_6_out6, decoder_6_out7,
       decoder_7_out0, decoder_7_out1, decoder_7_out2, decoder_7_out3, decoder_7_out4, decoder_7_out5,
       decoder_7_out6, decoder_7_out7, decoder_8_out0, decoder_8_out1, decoder_8_out2, decoder_8_out3,
       decoder_8_out4, decoder_8_out5, decoder_8_out6, decoder_8_out7, decoder_9_out0, decoder_9_out1,
       decoder_9_out2, decoder_9_out3, decoder_9_out4, decoder_9_out5, decoder_9_out6, decoder_9_out7,
       decoder_10_out0, decoder_10_out1, decoder_10_out2, decoder_10_out3, decoder_10_out4, decoder_10_out5,
       decoder_10_out6, decoder_10_out7, decoder_11_out0, decoder_11_out1, decoder_11_out2, decoder_11_out3,
       decoder_11_out4, decoder_11_out5, decoder_11_out6, decoder_11_out7, decoder_12_out0, decoder_12_out1,
       decoder_12_out2, decoder_12_out3, decoder_12_out4, decoder_12_out5, decoder_12_out6, decoder_12_out7,
       decoder_13_out0, decoder_13_out1, decoder_13_out2, decoder_13_out3, decoder_13_out4, decoder_13_out5,
       decoder_13_out6, decoder_13_out7, decoder_14_out0, decoder_14_out1, decoder_14_out2, decoder_14_out3,
       decoder_14_out4, decoder_14_out5, decoder_14_out6, decoder_14_out7, decoder_15_out0, decoder_15_out1,
       decoder_15_out2, decoder_15_out3, decoder_15_out4, decoder_15_out5, decoder_15_out6, decoder_15_out7,
       decoder_16_out0, decoder_16_out1, decoder_16_out2, decoder_16_out3, decoder_16_out4, decoder_16_out5,
       decoder_16_out6, decoder_16_out7;

  Decoder #(.select(3), .enable("false")) decoder_1 (
    .out0(decoder_1_out0), .out1(decoder_1_out1), .out2(decoder_1_out2), .out3(decoder_1_out3),
    .out4(decoder_1_out4), .out5(decoder_1_out5), .out6(decoder_1_out6), .out7(decoder_1_out7),
    .sel({D2, D1, D0}));
  Decoder #(.select(3), .enable("false")) decoder_2 (
    .out0(decoder_2_out0), .out1(decoder_2_out1), .out2(decoder_2_out2), .out3(decoder_2_out3),
    .out4(decoder_2_out4), .out5(decoder_2_out5), .out6(decoder_2_out6), .out7(decoder_2_out7),
    .sel({D2, D1, D0}));
  Decoder #(.select(3), .enable("false")) decoder_3 (
    .out0(decoder_3_out0), .out1(decoder_3_out1), .out2(decoder_3_out2), .out3(decoder_3_out3),
    .out4(decoder_3_out4), .out5(decoder_3_out5), .out6(decoder_3_out6), .out7(decoder_3_out7),
    .sel({D2, D1, D0}));
  Decoder #(.select(3), .enable("false")) decoder_4 (
    .out0(decoder_4_out0), .out1(decoder_4_out1), .out2(decoder_4_out2), .out3(decoder_4_out3),
    .out4(decoder_4_out4), .out5(decoder_4_out5), .out6(decoder_4_out6), .out7(decoder_4_out7),
    .sel({D2, D1, D0}));
  Decoder #(.select(3), .enable("false")) decoder_5 (
    .out0(decoder_5_out0), .out1(decoder_5_out1), .out2(decoder_5_out2), .out3(decoder_5_out3),
    .out4(decoder_5_out4), .out5(decoder_5_out5), .out6(decoder_5_out6), .out7(decoder_5_out7),
    .sel({D2, D1, D0}));
  Decoder #(.select(3), .enable("false")) decoder_6 (
    .out0(decoder_6_out0), .out1(decoder_6_out1), .out2(decoder_6_out2), .out3(decoder_6_out3),
    .out4(decoder_6_out4), .out5(decoder_6_out5), .out6(decoder_6_out6), .out7(decoder_6_out7),
    .sel({D2, D1, D0}));
  Decoder #(.select(3), .enable("false")) decoder_7 (
    .out0(decoder_7_out0), .out1(decoder_7_out1), .out2(decoder_7_out2), .out3(decoder_7_out3),
    .out4(decoder_7_out4), .out5(decoder_7_out5), .out6(decoder_7_out6), .out7(decoder_7_out7),
    .sel({D2, D1, D0}));
  Decoder #(.select(3), .enable("false")) decoder_8 (
    .out0(decoder_8_out0), .out1(decoder_8_out1), .out2(decoder_8_out2), .out3(decoder_8_out3),
    .out4(decoder_8_out4), .out5(decoder_8_out5), .out6(decoder_8_out6), .out7(decoder_8_out7),
    .sel({D2, D1, D0}));
  Decoder #(.select(3), .enable("false")) decoder_9 (
    .out0(decoder_9_out0), .out1(decoder_9_out1), .out2(decoder_9_out2), .out3(decoder_9_out3),
    .out4(decoder_9_out4), .out5(decoder_9_out5), .out6(decoder_9_out6), .out7(decoder_9_out7),
    .sel({D2, D1, D0}));
  Decoder #(.select(3), .enable("false")) decoder_10 (
    .out0(decoder_10_out0), .out1(decoder_10_out1), .out2(decoder_10_out2), .out3(decoder_10_out3),
    .out4(decoder_10_out4), .out5(decoder_10_out5), .out6(decoder_10_out6), .out7(decoder_10_out7),
    .sel({D2, D1, D0}));
  Decoder #(.select(3), .enable("false")) decoder_11 (
    .out0(decoder_11_out0), .out1(decoder_11_out1), .out2(decoder_11_out2), .out3(decoder_11_out3),
    .out4(decoder_11_out4), .out5(decoder_11_out5), .out6(decoder_11_out6), .out7(decoder_11_out7),
    .sel({D2, D1, D0}));
  Decoder #(.select(3), .enable("false")) decoder_12 (
    .out0(decoder_12_out0), .out1(decoder_12_out1), .out2(decoder_12_out2), .out3(decoder_12_out3),
    .out4(decoder_12_out4), .out5(decoder_12_out5), .out6(decoder_12_out6), .out7(decoder_12_out7),
    .sel({D2, D1, D0}));
  Decoder #(.select(3), .enable("false")) decoder_13 (
    .out0(decoder_13_out0), .out1(decoder_13_out1), .out2(decoder_13_out2), .out3(decoder_13_out3),
    .out4(decoder_13_out4), .out5(decoder_13_out5), .out6(decoder_13_out6), .out7(decoder_13_out7),
    .sel({D2, D1, D0}));
  Decoder #(.select(3), .enable("false")) decoder_14 (
    .out0(decoder_14_out0), .out1(decoder_14_out1), .out2(decoder_14_out2), .out3(decoder_14_out3),
    .out4(decoder_14_out4), .out5(decoder_14_out5), .out6(decoder_14_out6), .out7(decoder_14_out7),
    .sel({D2, D1, D0}));
  Decoder #(.select(3), .enable("false")) decoder_15 (
    .out0(decoder_15_out0), .out1(decoder_15_out1), .out2(decoder_15_out2), .out3(decoder_15_out3),
    .out4(decoder_15_out4), .out5(decoder_15_out5), .out6(decoder_15_out6), .out7(decoder_15_out7),
    .sel({D2, D1, D0}));
  Decoder #(.select(3), .enable("false")) decoder_16 (
    .out0(decoder_16_out0), .out1(decoder_16_out1), .out2(decoder_16_out2), .out3(decoder_16_out3),
    .out4(decoder_16_out4), .out5(decoder_16_out5), .out6(decoder_16_out6), .out7(decoder_16_out7),
    .sel({D2, D1, D0}));
  assign _8BitOut[0] = decoder_8_out0 ? Memory[0] : 1'bz;  // Controlled_Buffer controlled_buffer_1
  assign _8BitOut[1] = decoder_9_out0 ? Memory[1] : 1'bz;  // Controlled_Buffer controlled_buffer_2
  assign _8BitOut[1] = decoder_9_out1 ? ABUS[1] : 1'bz;  // Controlled_Buffer controlled_buffer_3
  assign _8BitOut[2] = decoder_10_out0 ? Memory[2] : 1'bz;  // Controlled_Buffer controlled_buffer_4
  assign _8BitOut[2] = decoder_10_out1 ? ABUS[2] : 1'bz;  // Controlled_Buffer controlled_buffer_5
  assign _8BitOut[3] = decoder_11_out0 ? Memory[3] : 1'bz;  // Controlled_Buffer controlled_buffer_6
  assign _8BitOut[3] = decoder_11_out1 ? ABUS[3] : 1'bz;  // Controlled_Buffer controlled_buffer_7
  assign _8BitOut[4] = decoder_12_out0 ? Memory[4] : 1'bz;  // Controlled_Buffer controlled_buffer_8
  assign _8BitOut[4] = decoder_12_out1 ? ABUS[4] : 1'bz;  // Controlled_Buffer controlled_buffer_9
  assign _8BitOut[5] = decoder_1_out0 ? Memory[5] : 1'bz;  // Controlled_Buffer controlled_buffer_10
  assign _8BitOut[5] = decoder_1_out1 ? ABUS[5] : 1'bz;  // Controlled_Buffer controlled_buffer_11
  assign _8BitOut[6] = decoder_2_out0 ? Memory[6] : 1'bz;  // Controlled_Buffer controlled_buffer_12
  assign _8BitOut[6] = decoder_2_out1 ? ABUS[6] : 1'bz;  // Controlled_Buffer controlled_buffer_13
  assign _8BitOut[7] = decoder_3_out0 ? Memory[7] : 1'bz;  // Controlled_Buffer controlled_buffer_14
  assign _8BitOut[7] = decoder_3_out1 ? ABUS[7] : 1'bz;  // Controlled_Buffer controlled_buffer_15
  assign _10BitOut[8] = decoder_4_out0 ? Memory[8] : 1'bz;  // Controlled_Buffer controlled_buffer_16
  assign _10BitOut[8] = decoder_4_out1 ? ABUS[8] : 1'bz;  // Controlled_Buffer controlled_buffer_17
  assign _10BitOut[9] = decoder_5_out0 ? Memory[9] : 1'bz;  // Controlled_Buffer controlled_buffer_18
  assign _10BitOut[9] = decoder_5_out1 ? ABUS[9] : 1'bz;  // Controlled_Buffer controlled_buffer_19
  assign _16BitOut[10] = decoder_6_out0 ? Memory[10] : 1'bz;  // Controlled_Buffer controlled_buffer_20
  assign _16BitOut[10] = decoder_6_out1 ? 1'b0 : 1'bz;  // Controlled_Buffer controlled_buffer_21
  assign _16BitOut[11] = decoder_7_out0 ? Memory[11] : 1'bz;  // Controlled_Buffer controlled_buffer_22
  assign _16BitOut[11] = decoder_7_out1 ? 1'b0 : 1'bz;  // Controlled_Buffer controlled_buffer_23
  assign _16BitOut[12] = decoder_13_out0 ? Memory[12] : 1'bz;  // Controlled_Buffer controlled_buffer_24
  assign _16BitOut[12] = decoder_13_out1 ? 1'b0 : 1'bz;  // Controlled_Buffer controlled_buffer_25
  assign _16BitOut[13] = decoder_14_out0 ? Memory[13] : 1'bz;  // Controlled_Buffer controlled_buffer_26
  assign _16BitOut[14] = decoder_15_out0 ? Memory[14] : 1'bz;  // Controlled_Buffer controlled_buffer_27
  assign _16BitOut[14] = decoder_15_out1 ? 1'b0 : 1'bz;  // Controlled_Buffer controlled_buffer_28
  assign _16BitOut[15] = decoder_16_out0 ? Memory[15] : 1'bz;  // Controlled_Buffer controlled_buffer_29
  assign _16BitOut[15] = decoder_16_out1 ? 1'b0 : 1'bz;  // Controlled_Buffer controlled_buffer_30
  assign _8BitOut[0] = decoder_8_out1 ? ABUS[0] : 1'bz;  // Controlled_Buffer controlled_buffer_31
  assign _8BitOut[0] = decoder_8_out2 ? GPRB[0] : 1'bz;  // Controlled_Buffer controlled_buffer_32
  assign _8BitOut[1] = decoder_9_out2 ? GPRB[1] : 1'bz;  // Controlled_Buffer controlled_buffer_33
  assign _8BitOut[1] = decoder_9_out3 ? AC[1] : 1'bz;  // Controlled_Buffer controlled_buffer_34
  assign _8BitOut[2] = decoder_10_out2 ? GPRB[2] : 1'bz;  // Controlled_Buffer controlled_buffer_35
  assign _8BitOut[2] = decoder_10_out3 ? AC[2] : 1'bz;  // Controlled_Buffer controlled_buffer_36
  assign _8BitOut[3] = decoder_11_out2 ? GPRB[3] : 1'bz;  // Controlled_Buffer controlled_buffer_37
  assign _8BitOut[3] = decoder_11_out3 ? AC[3] : 1'bz;  // Controlled_Buffer controlled_buffer_38
  assign _8BitOut[4] = decoder_12_out2 ? GPRB[4] : 1'bz;  // Controlled_Buffer controlled_buffer_39
  assign _8BitOut[4] = decoder_12_out3 ? AC[4] : 1'bz;  // Controlled_Buffer controlled_buffer_40
  assign _8BitOut[5] = decoder_1_out2 ? GPRB[5] : 1'bz;  // Controlled_Buffer controlled_buffer_41
  assign _8BitOut[5] = decoder_1_out3 ? AC[5] : 1'bz;  // Controlled_Buffer controlled_buffer_42
  assign _8BitOut[6] = decoder_2_out2 ? GPRB[6] : 1'bz;  // Controlled_Buffer controlled_buffer_43
  assign _8BitOut[6] = decoder_2_out3 ? AC[6] : 1'bz;  // Controlled_Buffer controlled_buffer_44
  assign _8BitOut[7] = decoder_3_out2 ? GPRB[7] : 1'bz;  // Controlled_Buffer controlled_buffer_45
  assign _8BitOut[7] = decoder_3_out3 ? AC[7] : 1'bz;  // Controlled_Buffer controlled_buffer_46
  assign _10BitOut[8] = decoder_4_out2 ? GPRB[8] : 1'bz;  // Controlled_Buffer controlled_buffer_47
  assign _10BitOut[8] = decoder_4_out3 ? AC[8] : 1'bz;  // Controlled_Buffer controlled_buffer_48
  assign _10BitOut[9] = decoder_5_out2 ? GPRB[9] : 1'bz;  // Controlled_Buffer controlled_buffer_49
  assign _10BitOut[9] = decoder_5_out3 ? AC[9] : 1'bz;  // Controlled_Buffer controlled_buffer_50
  assign _16BitOut[10] = decoder_6_out2 ? GPRB[10] : 1'bz;  // Controlled_Buffer controlled_buffer_51
  assign _16BitOut[10] = decoder_6_out3 ? AC[10] : 1'bz;  // Controlled_Buffer controlled_buffer_52
  assign _16BitOut[11] = decoder_7_out2 ? GPRB[11] : 1'bz;  // Controlled_Buffer controlled_buffer_53
  assign _16BitOut[11] = decoder_7_out3 ? AC[11] : 1'bz;  // Controlled_Buffer controlled_buffer_54
  assign _16BitOut[12] = decoder_13_out2 ? GPRB[12] : 1'bz;  // Controlled_Buffer controlled_buffer_55
  assign _16BitOut[12] = decoder_13_out3 ? AC[12] : 1'bz;  // Controlled_Buffer controlled_buffer_56
  assign _16BitOut[13] = decoder_14_out1 ? 1'b0 : 1'bz;  // Controlled_Buffer controlled_buffer_57
  assign _16BitOut[13] = decoder_14_out2 ? GPRB[13] : 1'bz;  // Controlled_Buffer controlled_buffer_58
  assign _16BitOut[14] = decoder_15_out2 ? GPRB[14] : 1'bz;  // Controlled_Buffer controlled_buffer_59
  assign _16BitOut[14] = decoder_15_out3 ? AC[14] : 1'bz;  // Controlled_Buffer controlled_buffer_60
  assign _16BitOut[15] = decoder_16_out2 ? GPRB[15] : 1'bz;  // Controlled_Buffer controlled_buffer_61
  assign _16BitOut[15] = decoder_16_out3 ? AC[15] : 1'bz;  // Controlled_Buffer controlled_buffer_62
  assign _8BitOut[0] = decoder_8_out3 ? AC[0] : 1'bz;  // Controlled_Buffer controlled_buffer_63
  assign _8BitOut[0] = decoder_8_out4 ? GPRA[0] : 1'bz;  // Controlled_Buffer controlled_buffer_64
  assign _8BitOut[0] = decoder_8_out5 ? X[0] : 1'bz;  // Controlled_Buffer controlled_buffer_65
  assign _8BitOut[1] = decoder_9_out4 ? GPRA[1] : 1'bz;  // Controlled_Buffer controlled_buffer_66
  assign _8BitOut[1] = decoder_9_out5 ? X[1] : 1'bz;  // Controlled_Buffer controlled_buffer_67
  assign _8BitOut[2] = decoder_10_out4 ? GPRA[2] : 1'bz;  // Controlled_Buffer controlled_buffer_68
  assign _8BitOut[2] = decoder_10_out5 ? X[2] : 1'bz;  // Controlled_Buffer controlled_buffer_69
  assign _8BitOut[3] = decoder_11_out4 ? GPRA[3] : 1'bz;  // Controlled_Buffer controlled_buffer_70
  assign _8BitOut[3] = decoder_11_out5 ? X[3] : 1'bz;  // Controlled_Buffer controlled_buffer_71
  assign _8BitOut[4] = decoder_12_out4 ? GPRA[4] : 1'bz;  // Controlled_Buffer controlled_buffer_72
  assign _8BitOut[4] = decoder_12_out5 ? X[4] : 1'bz;  // Controlled_Buffer controlled_buffer_73
  assign _8BitOut[5] = decoder_1_out4 ? GPRA[5] : 1'bz;  // Controlled_Buffer controlled_buffer_74
  assign _8BitOut[5] = decoder_1_out5 ? X[4] : 1'bz;  // Controlled_Buffer controlled_buffer_75
  assign _8BitOut[5] = decoder_1_out6 ? INPR[5] : 1'bz;  // Controlled_Buffer controlled_buffer_76
  assign _8BitOut[6] = decoder_2_out4 ? GPRA[6] : 1'bz;  // Controlled_Buffer controlled_buffer_77
  assign _8BitOut[6] = decoder_2_out5 ? X[4] : 1'bz;  // Controlled_Buffer controlled_buffer_78
  assign _8BitOut[6] = decoder_2_out6 ? INPR[6] : 1'bz;  // Controlled_Buffer controlled_buffer_79
  assign _8BitOut[7] = decoder_3_out4 ? GPRA[7] : 1'bz;  // Controlled_Buffer controlled_buffer_80
  assign _8BitOut[7] = decoder_3_out5 ? X[4] : 1'bz;  // Controlled_Buffer controlled_buffer_81
  assign _8BitOut[7] = decoder_3_out6 ? INPR[7] : 1'bz;  // Controlled_Buffer controlled_buffer_82
  assign _10BitOut[8] = decoder_4_out4 ? GPRA[8] : 1'bz;  // Controlled_Buffer controlled_buffer_83
  assign _10BitOut[8] = decoder_4_out5 ? X[4] : 1'bz;  // Controlled_Buffer controlled_buffer_84
  assign _10BitOut[8] = decoder_4_out6 ? 1'b0 : 1'bz;  // Controlled_Buffer controlled_buffer_85
  assign _10BitOut[9] = decoder_5_out4 ? GPRA[9] : 1'bz;  // Controlled_Buffer controlled_buffer_86
  assign _10BitOut[9] = decoder_5_out5 ? X[4] : 1'bz;  // Controlled_Buffer controlled_buffer_87
  assign _10BitOut[9] = decoder_5_out6 ? 1'b0 : 1'bz;  // Controlled_Buffer controlled_buffer_88
  assign _16BitOut[10] = decoder_6_out4 ? GPRA[10] : 1'bz;  // Controlled_Buffer controlled_buffer_89
  assign _16BitOut[10] = decoder_6_out5 ? X[4] : 1'bz;  // Controlled_Buffer controlled_buffer_90
  assign _16BitOut[10] = decoder_6_out6 ? 1'b0 : 1'bz;  // Controlled_Buffer controlled_buffer_91
  assign _16BitOut[11] = decoder_7_out4 ? GPRA[11] : 1'bz;  // Controlled_Buffer controlled_buffer_92
  assign _16BitOut[11] = decoder_7_out5 ? X[4] : 1'bz;  // Controlled_Buffer controlled_buffer_93
  assign _16BitOut[11] = decoder_7_out6 ? 1'b0 : 1'bz;  // Controlled_Buffer controlled_buffer_94
  assign _16BitOut[12] = decoder_13_out4 ? GPRA[12] : 1'bz;  // Controlled_Buffer controlled_buffer_95
  assign _16BitOut[12] = decoder_13_out5 ? X[4] : 1'bz;  // Controlled_Buffer controlled_buffer_96
  assign _16BitOut[13] = decoder_14_out3 ? AC[13] : 1'bz;  // Controlled_Buffer controlled_buffer_97
  assign _16BitOut[13] = decoder_14_out4 ? GPRA[13] : 1'bz;  // Controlled_Buffer controlled_buffer_98
  assign _16BitOut[13] = decoder_14_out5 ? X[4] : 1'bz;  // Controlled_Buffer controlled_buffer_99
  assign _16BitOut[14] = decoder_15_out4 ? GPRA[14] : 1'bz;  // Controlled_Buffer controlled_buffer_100
  assign _16BitOut[14] = decoder_15_out5 ? X[4] : 1'bz;  // Controlled_Buffer controlled_buffer_101
  assign _16BitOut[15] = decoder_16_out4 ? GPRA[15] : 1'bz;  // Controlled_Buffer controlled_buffer_102
  assign _16BitOut[15] = decoder_16_out5 ? X[4] : 1'bz;  // Controlled_Buffer controlled_buffer_103
  assign _8BitOut[0] = decoder_8_out6 ? INPR[0] : 1'bz;  // Controlled_Buffer controlled_buffer_104
  assign _8BitOut[0] = decoder_8_out7 ? IR[0] : 1'bz;  // Controlled_Buffer controlled_buffer_105
  assign _8BitOut[1] = decoder_9_out6 ? INPR[1] : 1'bz;  // Controlled_Buffer controlled_buffer_106
  assign _8BitOut[1] = decoder_9_out7 ? IR[1] : 1'bz;  // Controlled_Buffer controlled_buffer_107
  assign _8BitOut[2] = decoder_10_out6 ? INPR[2] : 1'bz;  // Controlled_Buffer controlled_buffer_108
  assign _8BitOut[2] = decoder_10_out7 ? IR[2] : 1'bz;  // Controlled_Buffer controlled_buffer_109
  assign _8BitOut[3] = decoder_11_out6 ? INPR[3] : 1'bz;  // Controlled_Buffer controlled_buffer_110
  assign _8BitOut[3] = decoder_11_out7 ? IR[3] : 1'bz;  // Controlled_Buffer controlled_buffer_111
  assign _8BitOut[4] = decoder_12_out6 ? INPR[4] : 1'bz;  // Controlled_Buffer controlled_buffer_112
  assign _8BitOut[4] = decoder_12_out7 ? IR[4] : 1'bz;  // Controlled_Buffer controlled_buffer_113
  assign _8BitOut[5] = decoder_1_out7 ? IR[5] : 1'bz;  // Controlled_Buffer controlled_buffer_114
  assign _8BitOut[6] = decoder_2_out7 ? IR[6] : 1'bz;  // Controlled_Buffer controlled_buffer_115
  assign _8BitOut[7] = decoder_3_out7 ? IR[7] : 1'bz;  // Controlled_Buffer controlled_buffer_116
  assign _10BitOut[8] = decoder_4_out7 ? IR[8] : 1'bz;  // Controlled_Buffer controlled_buffer_117
  assign _10BitOut[9] = decoder_5_out7 ? IR[9] : 1'bz;  // Controlled_Buffer controlled_buffer_118
  assign _16BitOut[10] = decoder_6_out7 ? IR[10] : 1'bz;  // Controlled_Buffer controlled_buffer_119
  assign _16BitOut[11] = decoder_7_out7 ? IR[11] : 1'bz;  // Controlled_Buffer controlled_buffer_120
  assign _16BitOut[12] = decoder_13_out6 ? 1'b0 : 1'bz;  // Controlled_Buffer controlled_buffer_121
  assign _16BitOut[12] = decoder_13_out7 ? IR[12] : 1'bz;  // Controlled_Buffer controlled_buffer_122
  assign _16BitOut[13] = decoder_14_out6 ? 1'b0 : 1'bz;  // Controlled_Buffer controlled_buffer_123
  assign _16BitOut[13] = decoder_14_out7 ? IR[13] : 1'bz;  // Controlled_Buffer controlled_buffer_124
  assign _16BitOut[14] = decoder_15_out6 ? 1'b0 : 1'bz;  // Controlled_Buffer controlled_buffer_125
  assign _16BitOut[14] = decoder_15_out7 ? IR[14] : 1'bz;  // Controlled_Buffer controlled_buffer_126
  assign _16BitOut[15] = decoder_16_out6 ? 1'b0 : 1'bz;  // Controlled_Buffer controlled_buffer_127
  assign _16BitOut[15] = decoder_16_out7 ? IR[15] : 1'bz;  // Controlled_Buffer controlled_buffer_128

  assign _10BitOut[7:0] = _8BitOut;
  assign _16BitOut[9:0] = {_10BitOut[9:8], _8BitOut};
  assign _16BitOut_2 = {_16BitOut[15:10], _10BitOut[9:8], _8BitOut};

  // Other names for the same wires on the sheet: D0_t = _8BitOut[0]; D1_t = _8BitOut[1]; D2_t = _8BitOut[2];
  //   D3 = _8BitOut[3]; D4 = _8BitOut[4]; D5 = _8BitOut[5]; D6 = _8BitOut[6]; D7 = _8BitOut[7]; D8 = _10BitOut[8];
  //   D9 = _10BitOut[9]; D10 = _16BitOut[10]; D11 = _16BitOut[11]; D12 = _16BitOut[12]; D13 = _16BitOut[13];
  //   D14 = _16BitOut[14]; D15 = _16BitOut[15]; A0 = ABUS[0]; A1 = ABUS[1]; A2 = ABUS[2]; A3 = ABUS[3]; A4 = ABUS[4];
  //   A5 = ABUS[5]; A6 = ABUS[6]; A7 = ABUS[7]; A8 = ABUS[8]; A9 = ABUS[9]; IN0 = INPR[0]; IN1 = INPR[1];
  //   IN2 = INPR[2]; IN3 = INPR[3]; IN4 = INPR[4]; IN5 = INPR[5]; IN6 = INPR[6]; IN7 = INPR[7]; M0 = Memory[0];
  //   M1 = Memory[1]; M2 = Memory[2]; M3 = Memory[3]; M4 = Memory[4]; M5 = Memory[5]; M6 = Memory[6]; M7 = Memory[7];
  //   M8 = Memory[8]; M9 = Memory[9]; M10 = Memory[10]; M11 = Memory[11]; M12 = Memory[12]; M13 = Memory[13];
  //   M14 = Memory[14]; M15 = Memory[15]
endmodule

module _5_Bit_Register (
  input  CLK,
  input  L,
  input  I,
  input  C,
  input  [4:0] INPUT,
  output Carry,
  output [4:0] OUTPUT
);

  wire and_2_out, and_3_out, and_4_out, and_5_out, and_6_out, and_7_out, and_8_out, and_9_out, and_10_out,
       and_11_out, and_12_out, and_13_out, and_14_out, and_15_out, and_16_out, and_17_out, not_1_out,
       not_2_out, not_3_out, not_4_out, not_5_out, not_6_out, not_7_out, or_1_out, or_2_out, or_3_out,
       or_4_out, or_5_out, or_6_out, or_7_out, or_8_out, or_9_out, or_10_out;

  not not_1 (not_1_out, L);
  not not_2 (not_2_out, INPUT[4]);
  not not_3 (not_3_out, INPUT[3]);
  not not_4 (not_4_out, INPUT[2]);
  not not_5 (not_5_out, INPUT[1]);
  not not_6 (not_6_out, INPUT[0]);
  not not_7 (not_7_out, I);
  and and_1 (Carry, and_4_out, OUTPUT[4]);
  and and_2 (and_2_out, L, not_2_out);
  and and_3 (and_3_out, INPUT[4], L);
  and and_4 (and_4_out, and_7_out, OUTPUT[3]);
  and and_5 (and_5_out, L, not_3_out);
  and and_6 (and_6_out, INPUT[3], L);
  and and_7 (and_7_out, and_10_out, OUTPUT[2]);
  and and_8 (and_8_out, L, not_4_out);
  and and_9 (and_9_out, INPUT[2], L);
  and and_10 (and_10_out, and_13_out, OUTPUT[1]);
  and and_11 (and_11_out, L, not_5_out);
  and and_12 (and_12_out, INPUT[1], L);
  and and_13 (and_13_out, and_17_out, OUTPUT[0]);
  and and_14 (and_14_out, L, not_6_out);
  and and_15 (and_15_out, INPUT[0], L);
  and and_16 (and_16_out, not_1_out, not_7_out, C);
  and and_17 (and_17_out, not_1_out, I);
  or or_1 (or_1_out, and_4_out, and_16_out, and_2_out);
  or or_2 (or_2_out, and_4_out, and_3_out);
  or or_3 (or_3_out, and_7_out, and_16_out, and_5_out);
  or or_4 (or_4_out, and_7_out, and_6_out);
  or or_5 (or_5_out, and_10_out, and_16_out, and_8_out);
  or or_6 (or_6_out, and_10_out, and_9_out);
  or or_7 (or_7_out, and_13_out, and_16_out, and_11_out);
  or or_8 (or_8_out, and_13_out, and_12_out);
  or or_9 (or_9_out, and_17_out, and_16_out, and_14_out);
  or or_10 (or_10_out, and_17_out, and_15_out);
  J_K_Flip_Flop j_k_ff_1 (.J(or_2_out), .clk(CLK), .K(or_1_out), .Q(OUTPUT[4]));  // open: Qn, preset, en, reset
  J_K_Flip_Flop j_k_ff_2 (.J(or_4_out), .clk(CLK), .K(or_3_out), .Q(OUTPUT[3]));  // open: Qn, preset, en, reset
  J_K_Flip_Flop j_k_ff_3 (.J(or_6_out), .clk(CLK), .K(or_5_out), .Q(OUTPUT[2]));  // open: Qn, preset, en, reset
  J_K_Flip_Flop j_k_ff_4 (.J(or_8_out), .clk(CLK), .K(or_7_out), .Q(OUTPUT[1]));  // open: Qn, preset, en, reset
  J_K_Flip_Flop j_k_ff_5 (.J(or_10_out), .clk(CLK), .K(or_9_out), .Q(OUTPUT[0]));  // open: Qn, preset, en, reset
endmodule

module _10_Bit_Register (
  input  [9:0] in_1,
  input  L,
  input  I,
  input  C,
  input  in_5,
  output Carry,
  output [9:0] out_7
);

  wire and_2_out, and_3_out, and_4_out, and_5_out, and_6_out, and_7_out, and_8_out, and_9_out, and_10_out,
       and_11_out, and_12_out, and_13_out, and_14_out, and_15_out, and_16_out, and_17_out, and_18_out,
       and_19_out, and_20_out, and_21_out, and_22_out, and_23_out, and_24_out, and_25_out, and_26_out,
       and_27_out, and_28_out, and_29_out, and_30_out, and_31_out, and_32_out, not_1_out, not_2_out,
       not_3_out, not_4_out, not_5_out, not_6_out, not_7_out, not_8_out, not_9_out, not_10_out, not_11_out,
       not_12_out, or_1_out, or_2_out, or_3_out, or_4_out, or_5_out, or_6_out, or_7_out, or_8_out, or_9_out,
       or_10_out, or_11_out, or_12_out, or_13_out, or_14_out, or_15_out, or_16_out, or_17_out, or_18_out,
       or_19_out, or_20_out;

  not not_1 (not_1_out, in_1[9]);
  not not_2 (not_2_out, in_1[8]);
  not not_3 (not_3_out, in_1[7]);
  not not_4 (not_4_out, in_1[6]);
  not not_5 (not_5_out, in_1[5]);
  not not_6 (not_6_out, in_1[4]);
  not not_7 (not_7_out, in_1[3]);
  not not_8 (not_8_out, in_1[2]);
  not not_9 (not_9_out, in_1[1]);
  not not_10 (not_10_out, in_1[0]);
  not not_11 (not_11_out, L);
  and and_1 (Carry, and_4_out, out_7[9]);
  and and_2 (and_2_out, L, not_1_out);
  and and_3 (and_3_out, in_1[9], L);
  and and_4 (and_4_out, and_7_out, out_7[8]);
  and and_5 (and_5_out, L, not_2_out);
  and and_6 (and_6_out, in_1[8], L);
  and and_7 (and_7_out, and_10_out, out_7[7]);
  and and_8 (and_8_out, L, not_3_out);
  and and_9 (and_9_out, in_1[7], L);
  and and_10 (and_10_out, and_13_out, out_7[6]);
  and and_11 (and_11_out, L, not_4_out);
  and and_12 (and_12_out, in_1[6], L);
  and and_13 (and_13_out, and_16_out, out_7[5]);
  and and_14 (and_14_out, L, not_5_out);
  and and_15 (and_15_out, in_1[5], L);
  and and_16 (and_16_out, and_19_out, out_7[4]);
  and and_17 (and_17_out, L, not_6_out);
  and and_18 (and_18_out, in_1[4], L);
  and and_19 (and_19_out, and_22_out, out_7[3]);
  and and_20 (and_20_out, L, not_7_out);
  and and_21 (and_21_out, in_1[3], L);
  and and_22 (and_22_out, and_25_out, out_7[2]);
  and and_23 (and_23_out, L, not_8_out);
  and and_24 (and_24_out, in_1[2], L);
  and and_25 (and_25_out, and_28_out, out_7[1]);
  and and_26 (and_26_out, L, not_9_out);
  and and_27 (and_27_out, in_1[1], L);
  and and_28 (and_28_out, and_31_out, out_7[0]);
  and and_29 (and_29_out, L, not_10_out);
  and and_30 (and_30_out, in_1[0], L);
  and and_31 (and_31_out, not_11_out, I);
  not not_12 (not_12_out, I);
  or or_1 (or_1_out, and_4_out, and_32_out, and_2_out);
  or or_2 (or_2_out, and_4_out, and_3_out);
  or or_3 (or_3_out, and_7_out, and_32_out, and_5_out);
  or or_4 (or_4_out, and_7_out, and_6_out);
  or or_5 (or_5_out, and_10_out, and_32_out, and_8_out);
  or or_6 (or_6_out, and_10_out, and_9_out);
  or or_7 (or_7_out, and_13_out, and_32_out, and_11_out);
  or or_8 (or_8_out, and_13_out, and_12_out);
  or or_9 (or_9_out, and_16_out, and_32_out, and_14_out);
  or or_10 (or_10_out, and_16_out, and_15_out);
  or or_11 (or_11_out, and_19_out, and_32_out, and_17_out);
  or or_12 (or_12_out, and_19_out, and_18_out);
  or or_13 (or_13_out, and_22_out, and_32_out, and_20_out);
  or or_14 (or_14_out, and_22_out, and_21_out);
  or or_15 (or_15_out, and_25_out, and_32_out, and_23_out);
  or or_16 (or_16_out, and_25_out, and_24_out);
  or or_17 (or_17_out, and_28_out, and_32_out, and_26_out);
  or or_18 (or_18_out, and_28_out, and_27_out);
  or or_19 (or_19_out, and_31_out, and_32_out, and_29_out);
  or or_20 (or_20_out, and_31_out, and_30_out);
  and and_32 (and_32_out, not_11_out, not_12_out, C);
  J_K_Flip_Flop j_k_ff_1 (.J(or_2_out), .clk(in_5), .K(or_1_out), .Q(out_7[9]));  // open: Qn, preset, en, reset
  J_K_Flip_Flop j_k_ff_2 (.J(or_4_out), .clk(in_5), .K(or_3_out), .Q(out_7[8]));  // open: Qn, preset, en, reset
  J_K_Flip_Flop j_k_ff_3 (.J(or_6_out), .clk(in_5), .K(or_5_out), .Q(out_7[7]));  // open: Qn, preset, en, reset
  J_K_Flip_Flop j_k_ff_4 (.J(or_8_out), .clk(in_5), .K(or_7_out), .Q(out_7[6]));  // open: Qn, preset, en, reset
  J_K_Flip_Flop j_k_ff_5 (.J(or_10_out), .clk(in_5), .K(or_9_out), .Q(out_7[5]));  // open: Qn, preset, en, reset
  J_K_Flip_Flop j_k_ff_6 (.J(or_12_out), .clk(in_5), .K(or_11_out), .Q(out_7[4]));  // open: Qn, preset, en, reset
  J_K_Flip_Flop j_k_ff_7 (.J(or_14_out), .clk(in_5), .K(or_13_out), .Q(out_7[3]));  // open: Qn, preset, en, reset
  J_K_Flip_Flop j_k_ff_8 (.J(or_16_out), .clk(in_5), .K(or_15_out), .Q(out_7[2]));  // open: Qn, preset, en, reset
  J_K_Flip_Flop j_k_ff_9 (.J(or_18_out), .clk(in_5), .K(or_17_out), .Q(out_7[1]));  // open: Qn, preset, en, reset
  J_K_Flip_Flop j_k_ff_10 (.J(or_20_out), .clk(in_5), .K(or_19_out), .Q(out_7[0]));  // open: Qn, preset, en, reset

  // Notes on the sheet:
  //   INPUT
  //   CLK
  //   OUTPUT
endmodule

module _16_Bit_Register (
  input  [15:0] Input,
  input  CLK,
  input  L,
  input  I,
  input  C,
  output Carry,
  output [15:0] Output
);

  wire and_2_out, and_3_out, and_4_out, and_5_out, and_6_out, and_7_out, and_8_out, and_9_out, and_10_out,
       and_11_out, and_12_out, and_13_out, and_14_out, and_15_out, and_16_out, and_17_out, and_18_out,
       and_19_out, and_20_out, and_21_out, and_22_out, and_23_out, and_24_out, and_25_out, and_26_out,
       and_27_out, and_28_out, and_29_out, and_30_out, and_31_out, and_32_out, and_33_out, and_34_out,
       and_35_out, and_36_out, and_37_out, and_38_out, and_39_out, and_40_out, and_41_out, and_42_out,
       and_43_out, and_44_out, and_45_out, and_46_out, and_47_out, and_48_out, and_49_out, and_50_out,
       not_1_out, not_2_out, not_3_out, not_4_out, not_5_out, not_6_out, not_7_out, not_8_out, not_9_out,
       not_10_out, not_11_out, not_12_out, not_13_out, not_14_out, not_15_out, not_16_out, not_17_out,
       not_18_out, or_1_out, or_2_out, or_3_out, or_4_out, or_5_out, or_6_out, or_7_out, or_8_out, or_9_out,
       or_10_out, or_11_out, or_12_out, or_13_out, or_14_out, or_15_out, or_16_out, or_17_out, or_18_out,
       or_19_out, or_20_out, or_21_out, or_22_out, or_23_out, or_24_out, or_25_out, or_26_out, or_27_out,
       or_28_out, or_29_out, or_30_out, or_31_out, or_32_out;

  not not_1 (not_1_out, Input[15]);
  not not_2 (not_2_out, Input[14]);
  not not_3 (not_3_out, Input[13]);
  not not_4 (not_4_out, Input[12]);
  not not_5 (not_5_out, Input[11]);
  not not_6 (not_6_out, Input[10]);
  not not_7 (not_7_out, Input[9]);
  not not_8 (not_8_out, Input[8]);
  not not_9 (not_9_out, Input[7]);
  not not_10 (not_10_out, Input[6]);
  not not_11 (not_11_out, Input[5]);
  not not_12 (not_12_out, Input[4]);
  not not_13 (not_13_out, Input[3]);
  not not_14 (not_14_out, Input[2]);
  not not_15 (not_15_out, Input[1]);
  not not_16 (not_16_out, Input[0]);
  not not_17 (not_17_out, L);
  and and_1 (Carry, and_4_out, Output[15]);
  and and_2 (and_2_out, L, not_1_out);
  and and_3 (and_3_out, Input[15], L);
  and and_4 (and_4_out, and_7_out, Output[14]);
  and and_5 (and_5_out, L, not_2_out);
  and and_6 (and_6_out, Input[14], L);
  and and_7 (and_7_out, and_10_out, Output[13]);
  and and_8 (and_8_out, L, not_3_out);
  and and_9 (and_9_out, Input[13], L);
  and and_10 (and_10_out, and_13_out, Output[12]);
  and and_11 (and_11_out, L, not_4_out);
  and and_12 (and_12_out, Input[12], L);
  and and_13 (and_13_out, and_16_out, Output[11]);
  and and_14 (and_14_out, L, not_5_out);
  and and_15 (and_15_out, Input[11], L);
  and and_16 (and_16_out, and_19_out, Output[10]);
  and and_17 (and_17_out, L, not_6_out);
  and and_18 (and_18_out, Input[10], L);
  and and_19 (and_19_out, and_22_out, Output[9]);
  and and_20 (and_20_out, L, not_7_out);
  and and_21 (and_21_out, Input[9], L);
  and and_22 (and_22_out, and_25_out, Output[8]);
  and and_23 (and_23_out, L, not_8_out);
  and and_24 (and_24_out, Input[8], L);
  and and_25 (and_25_out, and_28_out, Output[7]);
  and and_26 (and_26_out, L, not_9_out);
  and and_27 (and_27_out, Input[7], L);
  and and_28 (and_28_out, and_31_out, Output[6]);
  and and_29 (and_29_out, L, not_10_out);
  and and_30 (and_30_out, Input[6], L);
  and and_31 (and_31_out, and_34_out, Output[5]);
  and and_32 (and_32_out, L, not_11_out);
  and and_33 (and_33_out, Input[5], L);
  and and_34 (and_34_out, and_37_out, Output[4]);
  and and_35 (and_35_out, L, not_12_out);
  and and_36 (and_36_out, Input[4], L);
  and and_37 (and_37_out, and_40_out, Output[3]);
  and and_38 (and_38_out, L, not_13_out);
  and and_39 (and_39_out, Input[3], L);
  and and_40 (and_40_out, and_43_out, Output[2]);
  and and_41 (and_41_out, L, not_14_out);
  and and_42 (and_42_out, Input[2], L);
  and and_43 (and_43_out, and_46_out, Output[1]);
  and and_44 (and_44_out, L, not_15_out);
  and and_45 (and_45_out, Input[1], L);
  and and_46 (and_46_out, and_50_out, Output[0]);
  and and_47 (and_47_out, L, not_16_out);
  and and_48 (and_48_out, Input[0], L);
  not not_18 (not_18_out, I);
  or or_1 (or_1_out, and_4_out, and_49_out, and_2_out);
  or or_2 (or_2_out, and_4_out, and_3_out);
  or or_3 (or_3_out, and_7_out, and_49_out, and_5_out);
  or or_4 (or_4_out, and_7_out, and_6_out);
  or or_5 (or_5_out, and_10_out, and_49_out, and_8_out);
  or or_6 (or_6_out, and_10_out, and_9_out);
  or or_7 (or_7_out, and_13_out, and_49_out, and_11_out);
  or or_8 (or_8_out, and_13_out, and_12_out);
  or or_9 (or_9_out, and_16_out, and_49_out, and_14_out);
  or or_10 (or_10_out, and_16_out, and_15_out);
  or or_11 (or_11_out, and_19_out, and_49_out, and_17_out);
  or or_12 (or_12_out, and_19_out, and_18_out);
  or or_13 (or_13_out, and_22_out, and_49_out, and_20_out);
  or or_14 (or_14_out, and_22_out, and_21_out);
  or or_15 (or_15_out, and_25_out, and_49_out, and_23_out);
  or or_16 (or_16_out, and_25_out, and_24_out);
  or or_17 (or_17_out, and_28_out, and_49_out, and_26_out);
  or or_18 (or_18_out, and_28_out, and_27_out);
  or or_19 (or_19_out, and_31_out, and_49_out, and_29_out);
  or or_20 (or_20_out, and_31_out, and_30_out);
  or or_21 (or_21_out, and_34_out, and_49_out, and_32_out);
  or or_22 (or_22_out, and_34_out, and_33_out);
  or or_23 (or_23_out, and_37_out, and_49_out, and_35_out);
  or or_24 (or_24_out, and_37_out, and_36_out);
  or or_25 (or_25_out, and_40_out, and_49_out, and_38_out);
  or or_26 (or_26_out, and_40_out, and_39_out);
  or or_27 (or_27_out, and_43_out, and_49_out, and_41_out);
  or or_28 (or_28_out, and_43_out, and_42_out);
  or or_29 (or_29_out, and_46_out, and_49_out, and_44_out);
  or or_30 (or_30_out, and_46_out, and_45_out);
  or or_31 (or_31_out, and_50_out, and_49_out, and_47_out);
  or or_32 (or_32_out, and_50_out, and_48_out);
  and and_49 (and_49_out, not_17_out, not_18_out, C);
  and and_50 (and_50_out, not_17_out, I);
  J_K_Flip_Flop j_k_ff_1 (.J(or_2_out), .clk(CLK), .K(or_1_out), .Q(Output[15]));  // open: Qn, preset, en, reset
  J_K_Flip_Flop j_k_ff_2 (.J(or_4_out), .clk(CLK), .K(or_3_out), .Q(Output[14]));  // open: Qn, preset, en, reset
  J_K_Flip_Flop j_k_ff_3 (.J(or_6_out), .clk(CLK), .K(or_5_out), .Q(Output[13]));  // open: Qn, preset, en, reset
  J_K_Flip_Flop j_k_ff_4 (.J(or_8_out), .clk(CLK), .K(or_7_out), .Q(Output[12]));  // open: Qn, preset, en, reset
  J_K_Flip_Flop j_k_ff_5 (.J(or_10_out), .clk(CLK), .K(or_9_out), .Q(Output[11]));  // open: Qn, preset, en, reset
  J_K_Flip_Flop j_k_ff_6 (.J(or_12_out), .clk(CLK), .K(or_11_out), .Q(Output[10]));  // open: Qn, preset, en, reset
  J_K_Flip_Flop j_k_ff_7 (.J(or_14_out), .clk(CLK), .K(or_13_out), .Q(Output[9]));  // open: Qn, preset, en, reset
  J_K_Flip_Flop j_k_ff_8 (.J(or_16_out), .clk(CLK), .K(or_15_out), .Q(Output[8]));  // open: Qn, preset, en, reset
  J_K_Flip_Flop j_k_ff_9 (.J(or_18_out), .clk(CLK), .K(or_17_out), .Q(Output[7]));  // open: Qn, preset, en, reset
  J_K_Flip_Flop j_k_ff_10 (.J(or_20_out), .clk(CLK), .K(or_19_out), .Q(Output[6]));  // open: Qn, preset, en, reset
  J_K_Flip_Flop j_k_ff_11 (.J(or_22_out), .clk(CLK), .K(or_21_out), .Q(Output[5]));  // open: Qn, preset, en, reset
  J_K_Flip_Flop j_k_ff_12 (.J(or_24_out), .clk(CLK), .K(or_23_out), .Q(Output[4]));  // open: Qn, preset, en, reset
  J_K_Flip_Flop j_k_ff_13 (.J(or_26_out), .clk(CLK), .K(or_25_out), .Q(Output[3]));  // open: Qn, preset, en, reset
  J_K_Flip_Flop j_k_ff_14 (.J(or_28_out), .clk(CLK), .K(or_27_out), .Q(Output[2]));  // open: Qn, preset, en, reset
  J_K_Flip_Flop j_k_ff_15 (.J(or_30_out), .clk(CLK), .K(or_29_out), .Q(Output[1]));  // open: Qn, preset, en, reset
  J_K_Flip_Flop j_k_ff_16 (.J(or_32_out), .clk(CLK), .K(or_31_out), .Q(Output[0]));  // open: Qn, preset, en, reset
endmodule

module ALUBus (
  input  S,
  input  [15:0] A,
  input  [15:0] B,
  output [15:0] out_4
);

  wire decoder_1_out0, decoder_1_out1, decoder_2_out0, decoder_2_out1, decoder_3_out0, decoder_3_out1,
       decoder_4_out0, decoder_4_out1, decoder_5_out0, decoder_5_out1, decoder_6_out0, decoder_6_out1,
       decoder_7_out0, decoder_7_out1, decoder_8_out0, decoder_8_out1, decoder_9_out0, decoder_9_out1,
       decoder_10_out0, decoder_10_out1, decoder_11_out0, decoder_11_out1, decoder_12_out0, decoder_12_out1,
       decoder_13_out0, decoder_13_out1, decoder_14_out0, decoder_14_out1, decoder_15_out0, decoder_15_out1,
       decoder_16_out0, decoder_16_out1;

  assign out_4[15] = decoder_1_out1 ? B[15] : 1'bz;  // Controlled_Buffer controlled_buffer_1
  assign out_4[15] = decoder_1_out0 ? A[15] : 1'bz;  // Controlled_Buffer controlled_buffer_2
  Decoder #(.enable("false")) decoder_1 (.out0(decoder_1_out0), .out1(decoder_1_out1), .sel(S));
  assign out_4[14] = decoder_2_out0 ? A[14] : 1'bz;  // Controlled_Buffer controlled_buffer_3
  Decoder #(.enable("false")) decoder_2 (.out0(decoder_2_out0), .out1(decoder_2_out1), .sel(S));
  assign out_4[14] = decoder_2_out1 ? B[14] : 1'bz;  // Controlled_Buffer controlled_buffer_4
  assign out_4[13] = decoder_3_out1 ? B[13] : 1'bz;  // Controlled_Buffer controlled_buffer_5
  assign out_4[13] = decoder_3_out0 ? A[13] : 1'bz;  // Controlled_Buffer controlled_buffer_6
  Decoder #(.enable("false")) decoder_3 (.out0(decoder_3_out0), .out1(decoder_3_out1), .sel(S));
  Decoder #(.enable("false")) decoder_4 (.out0(decoder_4_out0), .out1(decoder_4_out1), .sel(S));
  assign out_4[12] = decoder_4_out1 ? B[12] : 1'bz;  // Controlled_Buffer controlled_buffer_7
  assign out_4[12] = decoder_4_out0 ? A[12] : 1'bz;  // Controlled_Buffer controlled_buffer_8
  assign out_4[11] = decoder_5_out0 ? A[11] : 1'bz;  // Controlled_Buffer controlled_buffer_9
  Decoder #(.enable("false")) decoder_5 (.out0(decoder_5_out0), .out1(decoder_5_out1), .sel(S));
  assign out_4[11] = decoder_5_out1 ? B[11] : 1'bz;  // Controlled_Buffer controlled_buffer_10
  assign out_4[10] = decoder_6_out1 ? B[10] : 1'bz;  // Controlled_Buffer controlled_buffer_11
  assign out_4[10] = decoder_6_out0 ? A[10] : 1'bz;  // Controlled_Buffer controlled_buffer_12
  Decoder #(.enable("false")) decoder_6 (.out0(decoder_6_out0), .out1(decoder_6_out1), .sel(S));
  Decoder #(.enable("false")) decoder_7 (.out0(decoder_7_out0), .out1(decoder_7_out1), .sel(S));
  assign out_4[9] = decoder_7_out1 ? B[9] : 1'bz;  // Controlled_Buffer controlled_buffer_13
  assign out_4[9] = decoder_7_out0 ? A[9] : 1'bz;  // Controlled_Buffer controlled_buffer_14
  assign out_4[8] = decoder_8_out0 ? A[8] : 1'bz;  // Controlled_Buffer controlled_buffer_15
  Decoder #(.enable("false")) decoder_8 (.out0(decoder_8_out0), .out1(decoder_8_out1), .sel(S));
  assign out_4[8] = decoder_8_out1 ? B[8] : 1'bz;  // Controlled_Buffer controlled_buffer_16
  assign out_4[7] = decoder_9_out1 ? B[7] : 1'bz;  // Controlled_Buffer controlled_buffer_17
  assign out_4[7] = decoder_9_out0 ? A[7] : 1'bz;  // Controlled_Buffer controlled_buffer_18
  Decoder #(.enable("false")) decoder_9 (.out0(decoder_9_out0), .out1(decoder_9_out1), .sel(S));
  assign out_4[6] = decoder_10_out0 ? A[6] : 1'bz;  // Controlled_Buffer controlled_buffer_19
  Decoder #(.enable("false")) decoder_10 (.out0(decoder_10_out0), .out1(decoder_10_out1), .sel(S));
  assign out_4[6] = decoder_10_out1 ? B[6] : 1'bz;  // Controlled_Buffer controlled_buffer_20
  assign out_4[5] = decoder_11_out0 ? A[5] : 1'bz;  // Controlled_Buffer controlled_buffer_21
  Decoder #(.enable("false")) decoder_11 (.out0(decoder_11_out0), .out1(decoder_11_out1), .sel(S));
  assign out_4[5] = decoder_11_out1 ? B[5] : 1'bz;  // Controlled_Buffer controlled_buffer_22
  assign out_4[4] = decoder_12_out1 ? B[4] : 1'bz;  // Controlled_Buffer controlled_buffer_23
  assign out_4[4] = decoder_12_out0 ? A[4] : 1'bz;  // Controlled_Buffer controlled_buffer_24
  Decoder #(.enable("false")) decoder_12 (.out0(decoder_12_out0), .out1(decoder_12_out1), .sel(S));
  assign out_4[3] = decoder_13_out0 ? A[3] : 1'bz;  // Controlled_Buffer controlled_buffer_25
  Decoder #(.enable("false")) decoder_13 (.out0(decoder_13_out0), .out1(decoder_13_out1), .sel(S));
  assign out_4[3] = decoder_13_out1 ? B[3] : 1'bz;  // Controlled_Buffer controlled_buffer_26
  assign out_4[2] = decoder_14_out0 ? A[2] : 1'bz;  // Controlled_Buffer controlled_buffer_27
  Decoder #(.enable("false")) decoder_14 (.out0(decoder_14_out0), .out1(decoder_14_out1), .sel(S));
  assign out_4[2] = decoder_14_out1 ? B[2] : 1'bz;  // Controlled_Buffer controlled_buffer_28
  assign out_4[1] = decoder_15_out1 ? B[1] : 1'bz;  // Controlled_Buffer controlled_buffer_29
  assign out_4[1] = decoder_15_out0 ? A[1] : 1'bz;  // Controlled_Buffer controlled_buffer_30
  Decoder #(.enable("false")) decoder_15 (.out0(decoder_15_out0), .out1(decoder_15_out1), .sel(S));
  assign out_4[0] = decoder_16_out0 ? A[0] : 1'bz;  // Controlled_Buffer controlled_buffer_31
  Decoder #(.enable("false")) decoder_16 (.out0(decoder_16_out0), .out1(decoder_16_out1), .sel(S));
  assign out_4[0] = decoder_16_out1 ? B[0] : 1'bz;  // Controlled_Buffer controlled_buffer_32

  // Other names for the same wires on the sheet: O0 = out_4[0]; O1 = out_4[1]; O2 = out_4[2]; O3 = out_4[3];
  //   O4 = out_4[4]; O5 = out_4[5]; O6 = out_4[6]; O7 = out_4[7]; O8 = out_4[8]; O9 = out_4[9]; O10 = out_4[10];
  //   O11 = out_4[11]; O12 = out_4[12]; O13 = out_4[13]; O14 = out_4[14]; O15 = out_4[15]
endmodule

module LogicUnit1Bit (
  input  A,
  input  B,
  input  s1,
  input  s0,
  input  cin,
  output Output,
  output Cout
);

  wire and_1_out, not_1_out, not_2_out, not_3_out, not_4_out, or_1_out, xor_1_out;

  not not_1 (not_1_out, A);
  and and_1 (and_1_out, B, A);
  not not_2 (not_2_out, and_1_out);
  not not_3 (not_3_out, or_1_out);
  or or_1 (or_1_out, A, B);
  not not_4 (not_4_out, xor_1_out);
  xor xor_1 (xor_1_out, A, B);
  Multiplexer #(.select(3), .enable("false")) multiplexer_1 (
    .in0(and_1_out), .in1(not_2_out), .in2(not_3_out), .in3(not_4_out), .in4(or_1_out), .in5(xor_1_out),
    .in6(not_1_out), .in7(not_1_out), .out(Output), .sel({s1, s0, cin}));

  assign Cout = cin;
endmodule

module ArithmeticUnit1Bit (
  input  Cin,
  input  A,
  input  B,
  input  S1,
  input  S0,
  output O,
  output COUT
);

  wire multiplexer_1_out, not_1_out;

  not not_1 (not_1_out, B);
  Multiplexer #(.select(2), .enable("false")) multiplexer_1 (
    .in0(1'b0), .in1(B), .in2(not_1_out), .in3(1'b1), .out(multiplexer_1_out), .sel({S1, S0}));
  Adder #(.width(1)) adder_1 (.a(A), .b(multiplexer_1_out), .out(O), .cin(Cin), .cout(COUT));
endmodule

module ALU16Bit (
  input  [3:0] S0,
  input  [7:0] Input_from_Register,
  input  [15:0] A,
  input  [15:0] B,
  output [7:0] Output_to_Register,
  output [15:0] Output
);

  wire alu1bit_1_carry, alu1bit_2_carry, alu1bit_3_carry, alu1bit_4_carry, alu1bit_5_carry, alu1bit_6_carry,
       alu1bit_7_carry, alu1bit_8_carry, alu1bit_9_carry, alu1bit_10_carry, alu1bit_11_carry,
       alu1bit_12_carry, alu1bit_13_carry, alu1bit_14_carry, alu1bit_15_carry, and_1_out, and_2_out,
       and_3_out, and_4_out, and_5_out, and_6_out, multiplexer_4_out, multiplexer_6_out, nand_1_out,
       not_1_out, not_2_out, not_3_out, Oo1, Oo2, or_1_out, or_2_out, R___L, xnor_1_out, xor_1_out,
       xor_2_out, xor_3_out, xor_4_out;

  Multiplexer #(.select(3), .enable("false")) multiplexer_1 (
    .in0(1'b0), .in1(A[15]), .in2(A[0]), .in3(1'b0), .in4(1'b0), .in5(A[15]), .in6(1'b0), .out(R___L),
    .sel({S0[1:0], Input_from_Register[0]}));  // open: in7
  and and_1 (and_1_out, and_2_out, nand_1_out);
  xor xor_1 (xor_1_out, A[14], A[15]);
  Multiplexer #(.enable("false")) multiplexer_2 (
    .in0(Input_from_Register[1]), .in1(xor_1_out), .out(Oo2), .sel(and_1_out));
  Multiplexer #(.enable("false")) multiplexer_3 (.in0(Oo2), .in1(Oo1), .out(Output_to_Register[1]), .sel(S0[3]));
  and and_2 (and_2_out, not_1_out, S0[1]);
  nand nand_1 (nand_1_out, S0[3], S0[2]);
  not not_1 (not_1_out, Input_from_Register[0]);
  Multiplexer #(.select(3), .enable("false")) multiplexer_4 (
    .in0(1'b1), .in1(1'b1), .in2(1'b1), .in3(1'b0), .in4(1'b0), .in5(1'b0), .in6(1'b0),
    .out(multiplexer_4_out), .sel({S0[1:0], Input_from_Register[0]}));  // open: in7
  ALU1Bit alu1bit_1 (
    .IR(R___L), .IL(A[1]), .A(A[0]), .B(B[0]), .F(Output[0]), .Cin(Input_from_Register[0]), .S3(S0[3]),
    .S2(S0[2]), .Select(multiplexer_4_out), .S1(S0[1]), .S0(S0[0]), .Carry(alu1bit_1_carry));
  ALU1Bit alu1bit_2 (
    .IR(A[0]), .IL(A[2]), .A(A[1]), .B(B[1]), .F(Output[1]), .Cin(alu1bit_1_carry), .S3(S0[3]), .S2(S0[2]),
    .Select(multiplexer_4_out), .S1(S0[1]), .S0(S0[0]), .Carry(alu1bit_2_carry));
  ALU1Bit alu1bit_3 (
    .IR(A[1]), .IL(A[3]), .A(A[2]), .B(B[2]), .F(Output[2]), .Cin(alu1bit_2_carry), .S3(S0[3]), .S2(S0[2]),
    .Select(multiplexer_4_out), .S1(S0[1]), .S0(S0[0]), .Carry(alu1bit_3_carry));
  ALU1Bit alu1bit_4 (
    .IR(A[2]), .IL(A[4]), .A(A[3]), .B(B[3]), .F(Output[3]), .Cin(alu1bit_3_carry), .S3(S0[3]), .S2(S0[2]),
    .Select(multiplexer_4_out), .S1(S0[1]), .S0(S0[0]), .Carry(alu1bit_4_carry));
  ALU1Bit alu1bit_5 (
    .IR(A[3]), .IL(A[5]), .A(A[4]), .B(B[4]), .F(Output[4]), .Cin(alu1bit_4_carry), .S3(S0[3]), .S2(S0[2]),
    .Select(multiplexer_4_out), .S1(S0[1]), .S0(S0[0]), .Carry(alu1bit_5_carry));
  ALU1Bit alu1bit_6 (
    .IR(A[4]), .IL(A[6]), .A(A[5]), .B(B[5]), .F(Output[5]), .Cin(alu1bit_5_carry), .S3(S0[3]), .S2(S0[2]),
    .Select(multiplexer_4_out), .S1(S0[1]), .S0(S0[0]), .Carry(alu1bit_6_carry));
  ALU1Bit alu1bit_7 (
    .IR(A[5]), .IL(A[7]), .A(A[6]), .B(B[6]), .F(Output[6]), .Cin(alu1bit_6_carry), .S3(S0[3]), .S2(S0[2]),
    .Select(multiplexer_4_out), .S1(S0[1]), .S0(S0[0]), .Carry(alu1bit_7_carry));
  ALU1Bit alu1bit_8 (
    .IR(A[6]), .IL(A[8]), .A(A[7]), .B(B[7]), .F(Output[7]), .Cin(alu1bit_7_carry), .S3(S0[3]), .S2(S0[2]),
    .Select(multiplexer_4_out), .S1(S0[1]), .S0(S0[0]), .Carry(alu1bit_8_carry));
  ALU1Bit alu1bit_9 (
    .IR(A[7]), .IL(A[9]), .A(A[8]), .B(B[8]), .F(Output[8]), .Cin(alu1bit_8_carry), .S3(S0[3]), .S2(S0[2]),
    .Select(multiplexer_4_out), .S1(S0[1]), .S0(S0[0]), .Carry(alu1bit_9_carry));
  ALU1Bit alu1bit_10 (
    .IR(A[8]), .IL(A[10]), .A(A[9]), .B(B[9]), .F(Output[9]), .Cin(alu1bit_9_carry), .S3(S0[3]), .S2(S0[2]),
    .Select(multiplexer_4_out), .S1(S0[1]), .S0(S0[0]), .Carry(alu1bit_10_carry));
  ALU1Bit alu1bit_11 (
    .IR(A[9]), .IL(A[11]), .A(A[10]), .B(B[10]), .F(Output[10]), .Cin(alu1bit_10_carry), .S3(S0[3]),
    .S2(S0[2]), .Select(multiplexer_4_out), .S1(S0[1]), .S0(S0[0]), .Carry(alu1bit_11_carry));
  ALU1Bit alu1bit_12 (
    .IR(A[10]), .IL(A[12]), .A(A[11]), .B(B[11]), .F(Output[11]), .Cin(alu1bit_11_carry), .S3(S0[3]),
    .S2(S0[2]), .Select(multiplexer_4_out), .S1(S0[1]), .S0(S0[0]), .Carry(alu1bit_12_carry));
  ALU1Bit alu1bit_13 (
    .IR(A[11]), .IL(A[13]), .A(A[12]), .B(B[12]), .F(Output[12]), .Cin(alu1bit_12_carry), .S3(S0[3]),
    .S2(S0[2]), .Select(multiplexer_4_out), .S1(S0[1]), .S0(S0[0]), .Carry(alu1bit_13_carry));
  ALU1Bit alu1bit_14 (
    .IR(A[12]), .IL(A[14]), .A(A[13]), .B(B[13]), .F(Output[13]), .Cin(alu1bit_13_carry), .S3(S0[3]),
    .S2(S0[2]), .Select(multiplexer_4_out), .S1(S0[1]), .S0(S0[0]), .Carry(alu1bit_14_carry));
  ALU1Bit alu1bit_15 (
    .IR(A[13]), .IL(A[15]), .A(A[14]), .B(B[14]), .F(Output[14]), .Cin(alu1bit_14_carry), .S3(S0[3]),
    .S2(S0[2]), .Select(multiplexer_4_out), .S1(S0[1]), .S0(S0[0]), .Carry(alu1bit_15_carry));
  ALU1Bit alu1bit_16 (
    .IR(A[14]), .IL(R___L), .A(A[15]), .B(B[15]), .F(Output[15]), .Cin(alu1bit_15_carry), .S3(S0[3]),
    .S2(S0[2]), .Select(multiplexer_4_out), .S1(S0[1]), .S0(S0[0]), .Carry(Output_to_Register[0]));
  not not_2 (not_2_out, A[15]);
  and and_3 (and_3_out, not_2_out, Output[15]);
  xnor xnor_1 (xnor_1_out, A[15], B[15]);
  and and_4 (and_4_out, xnor_1_out, xor_2_out);
  Multiplexer #(.enable("false")) multiplexer_5 (
    .in0(Input_from_Register[1]), .in1(multiplexer_6_out), .out(Oo1), .sel(S0[3]));
  or or_1 (or_1_out, Output[6], Output[5], Output[4], Output[3], Output[2], Output[1], Output[0]);
  or or_2 (or_2_out, Output[15], Output[14], Output[13], Output[12], Output[11], Output[10], Output[9], Output[7], Output[8]);
  xor xor_2 (xor_2_out, Output[15], A[15]);
  nor nor_1 (Output_to_Register[3], or_1_out, or_2_out);
  xor xor_3 (xor_3_out, A[15], B[15]);
  Multiplexer #(.select(2), .enable("false")) multiplexer_6 (
    .in0(and_3_out), .in1(and_4_out), .in2(and_5_out), .in3(and_6_out), .out(multiplexer_6_out), .sel(S0[1:0]));
  xor xor_4 (xor_4_out, Output[15], A[15]);
  and and_5 (and_5_out, xor_3_out, xor_4_out);
  not not_3 (not_3_out, Output[15]);
  and and_6 (and_6_out, A[15], not_3_out);

  assign Input_from_Register[6:5] = {2{Input_from_Register[7]}};
  assign {Output_to_Register[6:5], Output_to_Register[2]} = {{2{Output_to_Register[7]}}, Output[15]};

  // Other names for the same wires on the sheet: Ci = Input_from_Register[0]; S0_t = S0[0]; S1 = S0[1];
  //   Oi = Input_from_Register[1]; Ni = Input_from_Register[2]; Zi = Input_from_Register[3];
  //   Ii = Input_from_Register[4]; Ri = Input_from_Register[7]; F15 = Output[15]; No = Output[15];
  //   Co = Output_to_Register[0]; Oo = Output_to_Register[1]; Zo = Output_to_Register[3]; Io = Output_to_Register[4];
  //   Ro = Output_to_Register[7]; S3 = S0[3]

  // Notes on the sheet:
  //   Overflow case in ASHL
  //   Overflow case in ASHL
  //   Overflow
  //   Overflow case in Arithmetic Operations
  //   S1
  //   S2
  //   S3
  //   Cout
  //   Pos + 1 = Neg
  //   A + 1 Overflow Control
  //   Overflow case in Arithmetic Operations
  //   Addition Overflow Control
  //   Subtraction Overflow Control
  //   Neg - 1 = Pos
  //   A - 1 Overflow Control
endmodule

module ALU1Bit (
  input  IR,
  input  IL,
  input  Select,
  input  Cin,
  input  A,
  input  B,
  input  S3,
  input  S2,
  input  S1,
  input  S0,
  output F,
  output Carry
);

  wire arithmeticunit1bit_1_cout, arithmeticunit1bit_1_o, logicunit1bit_1_cout, logicunit1bit_1_output,
       multiplexer_1_out;

  Multiplexer #(.enable("false")) multiplexer_1 (.in0(IR), .in1(IL), .out(multiplexer_1_out), .sel(Select));
  LogicUnit1Bit logicunit1bit_1 (
    .A(A), .B(B), .Output(logicunit1bit_1_output), .Cout(logicunit1bit_1_cout), .s1(S1), .s0(S0), .cin(Cin));
  ArithmeticUnit1Bit arithmeticunit1bit_1 (
    .Cin(Cin), .A(A), .B(B), .O(arithmeticunit1bit_1_o), .S1(S1), .S0(S0), .COUT(arithmeticunit1bit_1_cout));
  Multiplexer #(.enable("false")) multiplexer_2 (
    .in0(logicunit1bit_1_cout), .in1(arithmeticunit1bit_1_cout), .out(Carry), .sel(S3));
  Multiplexer #(.select(2), .enable("false")) multiplexer_3 (
    .in0(multiplexer_1_out), .in1(logicunit1bit_1_output), .in2(arithmeticunit1bit_1_o),
    .in3(arithmeticunit1bit_1_o), .out(F), .sel({S3, S2}));

  // Notes on the sheet:
  //   D
  //   E
endmodule

// LD(AR)
module ControlUnit (
  input  [7:0] CCR,
  input  CLK,
  input  [15:0] IR,
  output LD_CCR,
  output CL_X,
  output LD_AR,
  output LD_IR,
  output CL_AC,
  output INC_X,
  output MSTR,
  output LD_AC,
  output S,
  output A1,
  output S0,
  output M,
  output S3,
  output D1,
  output D2,
  output MLOAD,
  output LD_PC,
  output INC_PC,
  output LD_SP,
  output LD_GPRA,
  output LD_GPRB,
  output INC_GPRB,
  output A0,
  output D0
);

  wire and_1_out, and_2_out, and_3_out, and_4_out, and_5_out, and_6_out, and_7_out, and_8_out, and_9_out,
       and_10_out, and_11_out, and_12_out, and_13_out, and_14_out, and_16_out, and_17_out, and_19_out,
       and_21_out, and_22_out, and_26_out, and_27_out, and_28_out, and_29_out, and_30_out, and_31_out,
       and_32_out, and_35_out, and_36_out, and_37_out, and_38_out, and_39_out, and_40_out, and_41_out,
       and_43_out, and_44_out, and_46_out, and_47_out, and_48_out, and_49_out, and_50_out, and_51_out,
       and_52_out, and_53_out, CL_SC, K0, K1, K2, K3, K4, K5, K6, K7, K8, K9, K10, K11, K12, K13, K14, K15,
       not_1_out, not_2_out, not_3_out, not_4_out, or_1_out, or_2_out, or_4_out, or_5_out, or_8_out,
       or_9_out, or_10_out, or_11_out, or_12_out, or_13_out, or_14_out, or_15_out, or_16_out, or_17_out,
       or_18_out, or_24_out, or_25_out, or_26_out, or_27_out, or_28_out, or_29_out, T1, T2, T3, T4, T5, T6,
       T7, T8, T9, T10, T11, T12, T13, T14, T15;
  wire [3:0] counter_1_t;

  and and_1 (and_1_out, K8, CCR[3]);
  and and_2 (and_2_out, K9, CCR[2]);
  or or_1 (or_1_out, T3, T4);
  Decoder #(.select(4), .enable("false")) decoder_1 (
    .out0(INC_PC), .out1(T1), .out2(T2), .out3(T3), .out4(T4), .out5(T5), .out6(T6), .out7(T7), .out8(T8),
    .out9(T9), .out10(T10), .out11(T11), .out12(T12), .out13(T13), .out14(T14), .out15(T15), .sel(counter_1_t));
  Counter counter_1 (.Enable(1'b1), .Clock(CLK), .Clear(CL_SC), .T(counter_1_t));
  and and_3 (and_3_out, K5, T2);
  or or_2 (or_2_out, T2, T3);
  and and_4 (and_4_out, K8, CCR[3]);
  and and_5 (and_5_out, K9, CCR[2]);
  and and_6 (and_6_out, K8, CCR[3]);
  and and_7 (and_7_out, K9, CCR[2]);
  not not_1 (not_1_out, IR[15]);
  not not_2 (not_2_out, IR[15]);
  and and_8 (and_8_out, K8, CCR[3]);
  and and_9 (and_9_out, K9, CCR[2]);
  or or_3 (LD_AC, and_3_out, and_10_out);
  and and_10 (and_10_out, or_2_out, K10);
  and and_11 (and_11_out, K8, CCR[3]);
  and and_12 (and_12_out, K9, CCR[2]);
  and and_13 (and_13_out, K8, CCR[3]);
  and and_14 (and_14_out, K9, CCR[2]);
  and and_15 (LD_SP, K15, T3);
  and and_16 (and_16_out, K1, T3);
  and and_17 (and_17_out, K10, T4);
  or or_4 (or_4_out, K2, K10);
  and and_18 (INC_GPRB, K14, T2);
  and and_19 (and_19_out, K10, or_1_out);
  and and_20 (INC_X, T2, K13);
  and and_21 (and_21_out, K10, T3);
  and and_22 (and_22_out, K6, T2);
  and and_23 (D2, K3, T3);
  not not_3 (not_3_out, IR[15]);
  or or_5 (or_5_out, K7, and_13_out, and_14_out);
  or or_6 (LD_GPRA, and_16_out, and_17_out);
  and and_24 (LD_GPRB, or_4_out, T3);
  or or_7 (M, and_21_out, and_22_out);
  and and_25 (LD_PC, T3, or_5_out);
  or or_8 (or_8_out, K1, K2, K3, K4, K7, and_6_out, and_7_out, K15);
  and and_26 (and_26_out, not_1_out, IR[14], T2);
  or or_9 (or_9_out, K1, K2, K3, K4);
  or or_10 (or_10_out, K1, K2, K3, K4, K7, and_1_out, and_2_out, K15);
  and and_27 (and_27_out, not_2_out, IR[14], T2);
  or or_11 (or_11_out, K7, K8, CCR[3], K9, CCR[2]);
  Decoder #(.select(4), .enable("false")) decoder_2 (
    .out0(K0), .out1(K1), .out2(K2), .out3(K3), .out4(K4), .out5(K5), .out6(K6), .out7(K7), .out8(K8),
    .out9(K9), .out10(K10), .out11(K11), .out12(K12), .out13(K13), .out14(K14), .out15(K15), .sel(IR[13:10]));
  or or_12 (or_12_out, IR[14], IR[15]);
  or or_13 (or_13_out, K1, K2, K3, K4, K7, and_4_out, and_5_out, K15);
  and and_28 (and_28_out, or_8_out, and_26_out);
  and and_29 (and_29_out, or_9_out, T3);
  and and_30 (and_30_out, or_10_out, and_27_out);
  and and_31 (and_31_out, or_11_out, T3);
  or or_14 (or_14_out, K1, K2, K3, K4, K7, and_8_out, and_9_out, K15);
  or or_15 (or_15_out, K3, K4);
  or or_16 (or_16_out, K1, K2, K3, K4, K7, and_11_out, and_12_out, K15);
  and and_32 (and_32_out, or_14_out, or_12_out);
  and and_33 (MSTR, or_15_out, T3);
  and and_34 (A1, or_13_out, IR[14], T2, IR[15]);
  or or_17 (or_17_out, T3, T4);
  or or_18 (or_18_out, K1, K2, K15);
  or or_19 (A0, and_28_out, and_29_out);
  or or_20 (D0, and_30_out, and_31_out, and_19_out);
  and and_35 (and_35_out, or_17_out, K10);
  and and_36 (and_36_out, K4, T3);
  and and_37 (and_37_out, or_16_out, IR[14], T2, not_3_out);
  and and_38 (and_38_out, or_18_out, T3);
  and and_39 (and_39_out, K8, CCR[3]);
  and and_40 (and_40_out, K9, CCR[2]);
  and and_41 (and_41_out, and_32_out, T2);
  and and_42 (CL_AC, K11, T2);
  or or_21 (D1, and_35_out, and_36_out);
  or or_22 (MLOAD, and_37_out, and_38_out, INC_PC);
  or or_23 (LD_AR, and_41_out, T1);
  and and_43 (and_43_out, K8, CCR[3]);
  and and_44 (and_44_out, K9, CCR[2]);
  not not_4 (not_4_out, IR[14]);
  or or_24 (or_24_out, K5, K6);
  or or_25 (or_25_out, T2, T3);
  or or_26 (or_26_out, K1, K2, K3, K4, K7, and_39_out, and_40_out, K15);
  or or_27 (or_27_out, K11, K12, K13, K14, K5, K6);
  or or_28 (or_28_out, K10, K5);
  or or_29 (or_29_out, K1, K2, K3, K4, K7, and_43_out, and_44_out, K15);
  and and_45 (S0, or_24_out, T2);
  and and_46 (and_46_out, or_25_out, K10);
  and and_47 (and_47_out, or_26_out, T3);
  and and_48 (and_48_out, or_27_out, T2);
  and and_49 (and_49_out, K10, T4);
  and and_50 (and_50_out, or_28_out, T2);
  and and_51 (and_51_out, K10, T3);
  or or_30 (S3, S0, and_46_out);
  or or_31 (LD_CCR, and_50_out, and_51_out);
  and and_52 (and_52_out, K12, T2);
  and and_53 (and_53_out, T1, IR[14]);
  and and_54 (S, or_29_out, not_4_out, T2, IR[15]);
  or or_32 (CL_SC, and_47_out, and_48_out, and_49_out);
  or or_33 (CL_X, and_52_out, and_53_out);
  // AND_Gate and_55 is placed but not wired

  assign LD_IR = INC_PC;

  // Other names for the same wires on the sheet: OpCode0 = IR[10]; OpCode1 = IR[11]; OpCode2 = IR[12];
  //   OpCode3 = IR[13]; CarryFlag = CCR[0]; OverflowFlag = CCR[1]; NegativeFlag = CCR[2]; ZeroFlag = CCR[3];
  //   EA0 = IR[0]; EA1 = IR[1]; EA2 = IR[2]; EA3 = IR[3]; EA4 = IR[4]; EA5 = IR[5]; EA6 = IR[6]; EA7 = IR[7];
  //   EA8 = IR[8]; EA9 = IR[9]; R0 = IR[14]; R1 = IR[15]; T0 = INC_PC
endmodule

module Counter (
  input  Enable,
  input  Clock,
  input  Clear,
  output [3:0] T
);

  wire and_1_out, and_2_out, and_3_out, d_ff_4_qn, xor_1_out, xor_2_out, xor_3_out;

  and and_1 (and_1_out, Clock, Clear);
  D_Flip_Flop d_ff_1 (.clk(Clock), .D(xor_1_out), .Q(T[3]), .en(Enable), .reset(and_1_out));  // open: Qn, preset
  xor xor_1 (xor_1_out, T[3], and_2_out);
  D_Flip_Flop d_ff_2 (.clk(Clock), .D(xor_2_out), .Q(T[2]), .en(Enable), .reset(and_1_out));  // open: Qn, preset
  xor xor_2 (xor_2_out, T[2], and_3_out);
  and and_2 (and_2_out, and_3_out, T[2]);
  xor xor_3 (xor_3_out, T[1], T[0]);
  and and_3 (and_3_out, T[1], T[0]);
  D_Flip_Flop d_ff_3 (.clk(Clock), .D(xor_3_out), .Q(T[1]), .en(Enable), .reset(and_1_out));  // open: Qn, preset
  D_Flip_Flop d_ff_4 (
    .clk(Clock), .D(d_ff_4_qn), .Q(T[0]), .Qn(d_ff_4_qn), .en(Enable), .reset(and_1_out));  // open: preset

  // Notes on the sheet:
  //   4-Bit Counter
endmodule
